// Logisim project Gfgg_PC_8.1.circ as structural Verilog: 4 circuits, main circuit Gfgg_PC_8
module Gfgg_PC_8 (
  output out_1,
  output out_2,
  output out_3,
  output out_4,
  output out_5,
  output out_6,
  output out_7,
  output out_8,
  output out_9,
  output out_10,
  output out_11,
  output out_12,
  output [2:0] out_13
);

  wire and_1_out, clock_1_out, gfgg_control_unit_1_1_add, gfgg_control_unit_1_1_hlt, not_1_out;
  wire [3:0] adder_1_out, and_2_out, and_3_out, RegA_q, RegB_q;
  wire [3:3] gfgg_control_unit_1_1_lda, gfgg_control_unit_1_1_ldb;
  wire [7:0] rom_1_data;

  Clock clock_1 (.out(clock_1_out));
  not not_1 (not_1_out, gfgg_control_unit_1_1_hlt);
  and and_1 (and_1_out, clock_1_out, not_1_out);
  Gfgg_3Bit_PC_2 gfgg_3bit_pc_2_1 (.CLK(and_1_out), .out_2(out_13));
  ROM #(.addrWidth(3)) rom_1 (.addr(out_13), .data(rom_1_data));
  assign and_2_out = rom_1_data[7:4] & {4{gfgg_control_unit_1_1_lda[3]}};  // AND_Gate and_2, 4 bits wide
  assign and_3_out = rom_1_data[7:4] & {4{gfgg_control_unit_1_1_ldb[3]}};  // AND_Gate and_3, 4 bits wide
  Register #(.width(4)) RegA (
    .D(and_2_out), .en(gfgg_control_unit_1_1_lda[3]), .clk(and_1_out), .Q(RegA_q));  // open: clr
  Register #(.width(4)) RegB (
    .D(and_3_out), .en(gfgg_control_unit_1_1_ldb[3]), .clk(and_1_out), .Q(RegB_q));  // open: clr
  Gfgg_Control_Unit_1 gfgg_control_unit_1_1 (
    .in_1(rom_1_data[3]), .in_2(rom_1_data[2]), .in_3(rom_1_data[1]), .in_4(rom_1_data[0]), .NOP(out_9),
    .LDA(gfgg_control_unit_1_1_lda[3]), .LDB(gfgg_control_unit_1_1_ldb[3]), .STA(out_10), .STB(out_11),
    .ADD(gfgg_control_unit_1_1_add), .HLT(gfgg_control_unit_1_1_hlt), .GTO(out_12));
  Adder #(.width(4)) adder_1 (.a(RegA_q), .b(RegB_q), .out(adder_1_out));  // open: cin, cout
  Register #(.width(4)) RegC (
    .D(adder_1_out), .en(gfgg_control_unit_1_1_add), .clk(and_1_out), .Q({out_5, out_6, out_7, out_8}));  // open: clr

  // Notes on the sheet:
  //   contents of rom_1 (hex, n*v repeats v):
  //   b 5 5 6
endmodule

module Gfgg_4_AND (
  input  in_1,
  input  in_2,
  input  in_3,
  input  in_4,
  output out_5
);

  wire and_1_out, and_2_out;

  and and_1 (and_1_out, in_1, in_2);
  and and_2 (and_2_out, in_3, in_4);
  and and_3 (out_5, and_1_out, and_2_out);
endmodule

module Gfgg_3Bit_PC_2 (
  input  CLK,
  output [2:0] out_2
);

  wire [2:0] adder_1_out;

  Adder #(.width(3)) adder_1 (.a(3'b001), .b(out_2), .out(adder_1_out));  // open: cin, cout
  Register #(.width(3)) register_1 (.D(adder_1_out), .en(1'b1), .clk(CLK), .Q(out_2));  // open: clr
endmodule

module Gfgg_Control_Unit_1 (
  input  in_1,
  input  in_2,
  input  in_3,
  input  in_4,
  output NOP,
  output LDA,
  output LDB,
  output STA,
  output STB,
  output ADD,
  output HLT,
  output GTO
);

  wire not_1_out, not_2_out, not_3_out, not_4_out, not_5_out, not_6_out, not_7_out, not_8_out, not_9_out,
       not_10_out, not_11_out, not_12_out, not_13_out, not_14_out, not_15_out, not_16_out, not_17_out;

  not not_1 (not_1_out, in_4);
  not not_2 (not_2_out, in_3);
  not not_3 (not_3_out, in_2);
  not not_4 (not_4_out, in_1);
  not not_5 (not_5_out, in_3);
  not not_6 (not_6_out, in_4);
  not not_7 (not_7_out, in_2);
  not not_8 (not_8_out, in_4);
  not not_9 (not_9_out, in_3);
  not not_10 (not_10_out, in_4);
  not not_11 (not_11_out, in_2);
  not not_12 (not_12_out, in_1);
  not not_13 (not_13_out, in_4);
  not not_14 (not_14_out, in_2);
  not not_15 (not_15_out, in_4);
  not not_16 (not_16_out, in_1);
  not not_17 (not_17_out, in_4);
  Gfgg_4_AND gfgg_4_and_1 (.in_1(not_1_out), .in_2(not_2_out), .in_3(not_3_out), .in_4(not_4_out), .out_5(NOP));
  Gfgg_4_AND gfgg_4_and_2 (.in_1(in_4), .in_2(not_5_out), .in_3(in_2), .in_4(in_1), .out_5(LDA));
  Gfgg_4_AND gfgg_4_and_3 (.in_1(not_6_out), .in_2(in_3), .in_3(not_7_out), .in_4(in_1), .out_5(LDB));
  Gfgg_4_AND gfgg_4_and_4 (.in_1(not_8_out), .in_2(not_9_out), .in_3(in_2), .in_4(in_1), .out_5(STA));
  Gfgg_4_AND gfgg_4_and_5 (.in_1(not_10_out), .in_2(in_3), .in_3(not_11_out), .in_4(not_12_out), .out_5(STB));
  Gfgg_4_AND gfgg_4_and_6 (.in_1(not_13_out), .in_2(in_3), .in_3(not_14_out), .in_4(in_1), .out_5(ADD));
  Gfgg_4_AND gfgg_4_and_7 (.in_1(not_15_out), .in_2(in_3), .in_3(in_2), .in_4(not_16_out), .out_5(HLT));
  Gfgg_4_AND gfgg_4_and_8 (.in_1(not_17_out), .in_2(in_3), .in_3(in_2), .in_4(in_1), .out_5(GTO));
endmodule
