// Logisim project Gfgg_PC_8.2.circ as structural Verilog: 5 circuits, main circuit Gfgg_PC_8
module Gfgg_PC_8 (
  input  in_1,
  output out_2,
  output out_3,
  output out_4,
  output out_5,
  output out_6,
  output out_7,
  output out_8,
  output out_9,
  output [2:0] out_10
);

  wire and_1_out, clock_1_out, gfgg_control_unit_2_1_addc, gfgg_control_unit_2_1_halt,
       gfgg_control_unit_2_1_ldia, gfgg_control_unit_2_1_ldib, gfgg_control_unit_2_1_subc, not_1_out,
       or_1_out;
  wire [3:0] gfgg_alu_1_out_4, RegA_q, RegB_q, RegC_q;
  wire [3:3] gfgg_control_unit_2_1_outc;
  wire [7:0] rom_1_data;

  Clock clock_1 (.out(clock_1_out));
  not not_1 (not_1_out, gfgg_control_unit_2_1_halt);
  and and_1 (and_1_out, clock_1_out, not_1_out);
  Gfgg_3Bit_PC_3 gfgg_3bit_pc_3_1 (.MIN(in_1), .CLK(and_1_out), .out_3(out_10));
  ROM #(.addrWidth(3)) rom_1 (.addr(out_10), .data(rom_1_data));
  Register #(.width(4)) RegA (
    .D(rom_1_data[7:4]), .en(gfgg_control_unit_2_1_ldia), .clk(and_1_out), .Q(RegA_q));  // open: clr
  Register #(.width(4)) RegB (
    .D(rom_1_data[7:4]), .en(gfgg_control_unit_2_1_ldib), .clk(and_1_out), .Q(RegB_q));  // open: clr
  Gfgg_Control_Unit_2 gfgg_control_unit_2_1 (
    .in_1(rom_1_data[3]), .in_2(rom_1_data[2]), .in_3(rom_1_data[1]), .in_4(rom_1_data[0]), .NOPO(out_6),
    .LDIA(gfgg_control_unit_2_1_ldia), .LDIB(gfgg_control_unit_2_1_ldib), .STRA(out_7), .STRB(out_8),
    .ADDC(gfgg_control_unit_2_1_addc), .HALT(gfgg_control_unit_2_1_halt), .GOTO(out_9),
    .SUBC(gfgg_control_unit_2_1_subc), .OUTC(gfgg_control_unit_2_1_outc[3]));
  Gfgg_ALU gfgg_alu_1 (.in_1(RegA_q), .in_2(RegB_q), .in_3(gfgg_control_unit_2_1_subc), .out_4(gfgg_alu_1_out_4));
  or or_1 (or_1_out, gfgg_control_unit_2_1_addc, gfgg_control_unit_2_1_subc);
  Register #(.width(4)) RegC (.D(gfgg_alu_1_out_4), .en(or_1_out), .clk(and_1_out), .Q(RegC_q));  // open: clr
  assign {out_2, out_3, out_4, out_5} = RegC_q & {4{gfgg_control_unit_2_1_outc[3]}};  // AND_Gate and_2, 4 bits wide

  // Notes on the sheet:
  //   Zoom out to see the PC!
  //   contents of rom_1 (hex, n*v repeats v):
  //   b 5 5 6
endmodule

module Gfgg_4_AND (
  input  in_1,
  input  in_2,
  input  in_3,
  input  in_4,
  output out_5
);

  wire and_1_out, and_2_out;

  and and_1 (and_1_out, in_1, in_2);
  and and_2 (and_2_out, in_3, in_4);
  and and_3 (out_5, and_1_out, and_2_out);
endmodule

module Gfgg_3Bit_PC_3 (
  input  MIN,
  input  CLK,
  output [2:0] out_3
);

  wire or_1_out;
  wire [2:0] adder_1_out;

  or or_1 (or_1_out, MIN, CLK);
  Adder #(.width(3)) adder_1 (.a(3'b001), .b(out_3), .out(adder_1_out));  // open: cin, cout
  Register #(.width(3)) register_1 (.D(adder_1_out), .en(1'b1), .clk(or_1_out), .Q(out_3));  // open: clr
endmodule

module Gfgg_Control_Unit_2 (
  input  in_1,
  input  in_2,
  input  in_3,
  input  in_4,
  output NOPO,
  output LDIA,
  output LDIB,
  output STRA,
  output STRB,
  output ADDC,
  output HALT,
  output GOTO,
  output SUBC,
  output OUTC
);

  wire not_1_out, not_2_out, not_3_out, not_4_out, not_5_out, not_6_out, not_7_out, not_8_out, not_9_out,
       not_10_out, not_11_out, not_12_out, not_13_out, not_14_out, not_15_out, not_16_out, not_17_out,
       not_18_out, not_19_out, not_20_out, not_21_out, not_22_out;

  not not_1 (not_1_out, in_4);
  not not_2 (not_2_out, in_3);
  not not_3 (not_3_out, in_2);
  not not_4 (not_4_out, in_1);
  not not_5 (not_5_out, in_3);
  not not_6 (not_6_out, in_4);
  not not_7 (not_7_out, in_2);
  not not_8 (not_8_out, in_4);
  not not_9 (not_9_out, in_3);
  not not_10 (not_10_out, in_4);
  not not_11 (not_11_out, in_2);
  not not_12 (not_12_out, in_1);
  not not_13 (not_13_out, in_4);
  not not_14 (not_14_out, in_2);
  not not_15 (not_15_out, in_4);
  not not_16 (not_16_out, in_1);
  not not_17 (not_17_out, in_4);
  not not_18 (not_18_out, in_3);
  not not_19 (not_19_out, in_2);
  not not_20 (not_20_out, in_1);
  not not_21 (not_21_out, in_3);
  not not_22 (not_22_out, in_2);
  Gfgg_4_AND gfgg_4_and_1 (.in_1(not_1_out), .in_2(not_2_out), .in_3(not_3_out), .in_4(not_4_out), .out_5(NOPO));
  Gfgg_4_AND gfgg_4_and_2 (.in_1(in_4), .in_2(not_5_out), .in_3(in_2), .in_4(in_1), .out_5(LDIA));
  Gfgg_4_AND gfgg_4_and_3 (.in_1(not_6_out), .in_2(in_3), .in_3(not_7_out), .in_4(in_1), .out_5(LDIB));
  Gfgg_4_AND gfgg_4_and_4 (.in_1(not_8_out), .in_2(not_9_out), .in_3(in_2), .in_4(in_1), .out_5(STRA));
  Gfgg_4_AND gfgg_4_and_5 (.in_1(not_10_out), .in_2(in_3), .in_3(not_11_out), .in_4(not_12_out), .out_5(STRB));
  Gfgg_4_AND gfgg_4_and_6 (.in_1(not_13_out), .in_2(in_3), .in_3(not_14_out), .in_4(in_1), .out_5(ADDC));
  Gfgg_4_AND gfgg_4_and_7 (.in_1(not_15_out), .in_2(in_3), .in_3(in_2), .in_4(not_16_out), .out_5(HALT));
  Gfgg_4_AND gfgg_4_and_8 (.in_1(not_17_out), .in_2(in_3), .in_3(in_2), .in_4(in_1), .out_5(GOTO));
  Gfgg_4_AND gfgg_4_and_9 (.in_1(in_4), .in_2(not_18_out), .in_3(not_19_out), .in_4(not_20_out), .out_5(SUBC));
  Gfgg_4_AND gfgg_4_and_10 (.in_1(in_4), .in_2(not_21_out), .in_3(not_22_out), .in_4(in_1), .out_5(OUTC));
endmodule

module Gfgg_ALU (
  input  [3:0] in_1,
  input  [3:0] in_2,
  input  in_3,
  output [3:0] out_4
);

  wire [3:0] adder_1_out, and_1_out, and_2_out, subtractor_1_out;
  wire [3:3] not_1_out;

  Adder #(.width(4)) adder_1 (.a(in_1), .b(in_2), .out(adder_1_out));  // open: cin, cout
  not not_1 (not_1_out[3], in_3);
  Subtractor #(.width(4)) subtractor_1 (.a(in_1), .b(in_2), .out(subtractor_1_out));  // open: bin, bout
  assign and_1_out = adder_1_out & {4{not_1_out[3]}};  // AND_Gate and_1, 4 bits wide
  assign and_2_out = subtractor_1_out & {4{in_3}};  // AND_Gate and_2, 4 bits wide
  assign out_4 = and_1_out | and_2_out;  // OR_Gate or_1, 4 bits wide
endmodule
