// Logisim project Gfgg_PC_8.5.circ as structural Verilog: 8 circuits, main circuit Gfgg_PC_8
module Gfgg_PC_8 (
  input  [3:0] in_1,
  input  in_2,
  output out_3,
  output out_4,
  output [3:0] out_5,
  output out_6,
  output out_7,
  output out_8,
  output out_9,
  output out_10,
  output out_11,
  output out_12,
  output out_13,
  output out_14,
  output out_15,
  output [4:0] out_16
);

  wire CLK, clock_1_out, gfgg_control_unit_2_1_addc, gfgg_control_unit_2_1_ldia, gfgg_control_unit_2_1_ldib,
       gfgg_control_unit_2_1_subc, HALT, not_1_out, or_1_out, STRC;
  wire [3:0] and_1_out, and_3_out, gfgg_alu_1_out_5, RegA_q, RegB_q, RegC_q;
  wire [3:3] gfgg_control_unit_2_1_outc;
  wire [7:0] rom_1_data;

  RAM #(.addrWidth(4), .dataWidth(4)) ram_1 (
    .addr(and_1_out), .we(STRC), .oe(1'b1), .clk(CLK), .din({out_6, out_7, out_8, out_9}), .dout(out_5));
  assign and_1_out = {4{STRC}} & rom_1_data[7:4];  // AND_Gate and_1, 4 bits wide
  Gfgg_5Bit_PC_1 gfgg_5bit_pc_1_1 (.MIN(in_2), .CLK(CLK), .out_3(out_16));
  Clock clock_1 (.out(clock_1_out));
  ROM #(.addrWidth(5)) rom_1 (.addr(out_16), .data(rom_1_data));
  not not_1 (not_1_out, HALT);
  and and_2 (CLK, clock_1_out, not_1_out);
  Register #(.width(4)) RegA (
    .D(rom_1_data[7:4]), .en(gfgg_control_unit_2_1_ldia), .clk(CLK), .Q(RegA_q));  // open: clr
  Register #(.width(4)) RegB (
    .D(rom_1_data[7:4]), .en(gfgg_control_unit_2_1_ldib), .clk(CLK), .Q(RegB_q));  // open: clr
  Gfgg_Control_Unit_2 gfgg_control_unit_2_1 (
    .in_1(rom_1_data[3]), .in_2(rom_1_data[2]), .in_3(rom_1_data[1]), .in_4(rom_1_data[0]), .NOPO(out_10),
    .LDIA(gfgg_control_unit_2_1_ldia), .LDIB(gfgg_control_unit_2_1_ldib), .STRA(out_11), .STRB(out_12),
    .ADDC(gfgg_control_unit_2_1_addc), .HALT(HALT), .GOTO(out_13), .SUBC(gfgg_control_unit_2_1_subc),
    .OUTC(gfgg_control_unit_2_1_outc[3]), .STRC(STRC), .BTND(out_14), .BTOR(out_15));
  Gfgg_SR_Latch gfgg_sr_latch_1 (.in_1(and_3_out), .in_2(in_1), .out_3({out_6, out_7, out_8, out_9}));
  Gfgg_ALU gfgg_alu_1 (
    .in_1(RegA_q), .in_2(RegB_q), .Select0(gfgg_control_unit_2_1_subc), .out_5(gfgg_alu_1_out_5),
    .Zero(out_3), .CB_OUT(out_4));  // open: Select1_WIP
  or or_1 (or_1_out, gfgg_control_unit_2_1_addc, gfgg_control_unit_2_1_subc);
  Register #(.width(4)) RegC (.D(gfgg_alu_1_out_5), .en(or_1_out), .clk(CLK), .Q(RegC_q));  // open: clr
  assign and_3_out = RegC_q & {4{gfgg_control_unit_2_1_outc[3]}};  // AND_Gate and_3, 4 bits wide

  // Notes on the sheet:
  //   Zoom out to see the PC!
endmodule

module Gfgg_4_AND (
  input  in_1,
  input  in_2,
  input  in_3,
  input  in_4,
  output out_5
);

  wire and_1_out, and_2_out;

  and and_1 (and_1_out, in_1, in_2);
  and and_2 (and_2_out, in_3, in_4);
  and and_3 (out_5, and_1_out, and_2_out);
endmodule

module Gfgg_5Bit_PC_1 (
  input  MIN,
  input  CLK,
  output [4:0] out_3
);

  wire or_1_out;
  wire [4:0] adder_1_out;

  Adder #(.width(5)) adder_1 (.a(5'b00001), .b(out_3), .out(adder_1_out));  // open: cin, cout
  or or_1 (or_1_out, MIN, CLK);
  Register #(.width(5)) register_1 (.D(adder_1_out), .en(1'b1), .clk(or_1_out), .Q(out_3));  // open: clr
endmodule

module Gfgg_Control_Unit_2 (
  input  in_1,
  input  in_2,
  input  in_3,
  input  in_4,
  output NOPO,
  output LDIA,
  output LDIB,
  output STRA,
  output STRB,
  output ADDC,
  output HALT,
  output GOTO,
  output SUBC,
  output OUTC,
  output STRC,
  output BTND,
  output BTOR
);

  wire not_1_out, not_2_out, not_3_out, not_4_out, not_5_out, not_6_out, not_7_out, not_8_out, not_9_out,
       not_10_out, not_11_out, not_12_out, not_13_out, not_14_out, not_15_out, not_16_out, not_17_out,
       not_18_out, not_19_out, not_20_out, not_21_out, not_22_out, not_23_out, not_24_out, not_25_out,
       not_26_out, not_27_out, not_28_out, not_29_out, not_30_out;

  not not_1 (not_1_out, in_4);
  not not_2 (not_2_out, in_3);
  not not_3 (not_3_out, in_2);
  not not_4 (not_4_out, in_1);
  not not_5 (not_5_out, in_3);
  not not_6 (not_6_out, in_4);
  not not_7 (not_7_out, in_2);
  not not_8 (not_8_out, in_4);
  not not_9 (not_9_out, in_3);
  not not_10 (not_10_out, in_4);
  not not_11 (not_11_out, in_2);
  not not_12 (not_12_out, in_1);
  not not_13 (not_13_out, in_4);
  not not_14 (not_14_out, in_3);
  not not_15 (not_15_out, in_1);
  not not_16 (not_16_out, in_4);
  not not_17 (not_17_out, in_1);
  not not_18 (not_18_out, in_4);
  not not_19 (not_19_out, in_3);
  not not_20 (not_20_out, in_2);
  not not_21 (not_21_out, in_1);
  not not_22 (not_22_out, in_3);
  not not_23 (not_23_out, in_2);
  not not_24 (not_24_out, in_2);
  not not_25 (not_25_out, in_4);
  not not_26 (not_26_out, in_3);
  not not_27 (not_27_out, in_2);
  not not_28 (not_28_out, in_4);
  not not_29 (not_29_out, in_3);
  not not_30 (not_30_out, in_2);
  Gfgg_4_AND gfgg_4_and_1 (.in_1(not_1_out), .in_2(not_2_out), .in_3(not_3_out), .in_4(not_4_out), .out_5(NOPO));
  Gfgg_4_AND gfgg_4_and_2 (.in_1(in_4), .in_2(not_5_out), .in_3(in_2), .in_4(in_1), .out_5(LDIA));
  Gfgg_4_AND gfgg_4_and_3 (.in_1(not_6_out), .in_2(in_3), .in_3(not_7_out), .in_4(in_1), .out_5(LDIB));
  Gfgg_4_AND gfgg_4_and_4 (.in_1(not_8_out), .in_2(not_9_out), .in_3(in_2), .in_4(in_1), .out_5(STRA));
  Gfgg_4_AND gfgg_4_and_5 (.in_1(not_10_out), .in_2(in_3), .in_3(not_11_out), .in_4(not_12_out), .out_5(STRB));
  Gfgg_4_AND gfgg_4_and_6 (.in_1(not_13_out), .in_2(not_14_out), .in_3(in_2), .in_4(not_15_out), .out_5(ADDC));
  Gfgg_4_AND gfgg_4_and_7 (.in_1(not_16_out), .in_2(in_3), .in_3(in_2), .in_4(not_17_out), .out_5(HALT));
  Gfgg_4_AND gfgg_4_and_8 (.in_1(not_18_out), .in_2(in_3), .in_3(in_2), .in_4(in_1), .out_5(GOTO));
  Gfgg_4_AND gfgg_4_and_9 (.in_1(in_4), .in_2(not_19_out), .in_3(not_20_out), .in_4(not_21_out), .out_5(SUBC));
  Gfgg_4_AND gfgg_4_and_10 (.in_1(in_4), .in_2(not_22_out), .in_3(not_23_out), .in_4(in_1), .out_5(OUTC));
  Gfgg_4_AND gfgg_4_and_11 (.in_1(in_4), .in_2(in_3), .in_3(not_24_out), .in_4(in_1), .out_5(STRC));
  Gfgg_4_AND gfgg_4_and_12 (.in_1(not_25_out), .in_2(not_26_out), .in_3(not_27_out), .in_4(in_1), .out_5(BTND));
  Gfgg_4_AND gfgg_4_and_13 (.in_1(not_28_out), .in_2(not_29_out), .in_3(not_30_out), .in_4(in_1), .out_5(BTOR));
endmodule

module Gfgg_ALU (
  input  [3:0] in_1,
  input  [3:0] in_2,
  input  Select0,
  input  Select1_WIP,
  output [3:0] out_5,
  output Zero,
  output CB_OUT
);

  wire adder_1_cout, not_3_out, not_4_out, not_5_out, not_6_out, subtractor_1_bout;
  wire [3:0] adder_1_out, and_1_out, and_2_out, and_3_out, and_4_out, gfgg_bitwise_and_1_out_3,
       gfgg_bitwise_or_1_out_3, SEL0N, SEL1N, subtractor_1_out;

  assign SEL0N = ~{4{Select0}};  // NOT_Gate not_1, 4 bits wide
  assign SEL1N = ~{4{Select1_WIP}};  // NOT_Gate not_2, 4 bits wide
  Adder #(.width(4)) adder_1 (.a(in_1), .b(in_2), .out(adder_1_out), .cout(adder_1_cout));  // open: cin
  Subtractor #(.width(4)) subtractor_1 (
    .a(in_1), .b(in_2), .out(subtractor_1_out), .bout(subtractor_1_bout));  // open: bin
  Gfgg_Bitwise_AND gfgg_bitwise_and_1 (.in_1(in_1), .in_2(in_2), .out_3(gfgg_bitwise_and_1_out_3));
  Gfgg_Bitwise_OR gfgg_bitwise_or_1 (.in_1(in_1), .in_2(in_2), .out_3(gfgg_bitwise_or_1_out_3));
  assign and_1_out = adder_1_out & SEL0N & SEL1N;  // AND_Gate and_1, 4 bits wide
  assign and_2_out = subtractor_1_out & {4{Select0}} & SEL1N;  // AND_Gate and_2, 4 bits wide
  assign and_3_out = gfgg_bitwise_and_1_out_3 & SEL0N & {4{Select1_WIP}};  // AND_Gate and_3, 4 bits wide
  assign and_4_out = gfgg_bitwise_or_1_out_3 & {4{Select0}} & {4{Select1_WIP}};  // AND_Gate and_4, 4 bits wide
  assign out_5 = and_1_out | and_2_out | and_3_out | and_4_out;  // OR_Gate or_1, 4 bits wide
  not not_3 (not_3_out, out_5[0]);
  not not_4 (not_4_out, out_5[1]);
  not not_5 (not_5_out, out_5[2]);
  not not_6 (not_6_out, out_5[3]);
  or or_2 (CB_OUT, adder_1_cout, subtractor_1_bout);
  Gfgg_4_AND gfgg_4_and_1 (.in_1(not_3_out), .in_2(not_4_out), .in_3(not_5_out), .in_4(not_6_out), .out_5(Zero));

  // Other names for the same wires on the sheet: SEL0P[3:0] = {4{Select0}}; SEL1P[3:0] = {4{Select1_WIP}}
endmodule

module Gfgg_Bitwise_AND (
  input  [3:0] in_1,
  input  [3:0] in_2,
  output [3:0] out_3
);

  and and_1 (out_3[0], in_1[0], in_2[0]);
  and and_2 (out_3[1], in_1[1], in_2[1]);
  and and_3 (out_3[2], in_1[2], in_2[2]);
  and and_4 (out_3[3], in_1[3], in_2[3]);
endmodule

module Gfgg_Bitwise_OR (
  input  [3:0] in_1,
  input  [3:0] in_2,
  output [3:0] out_3
);

  or or_1 (out_3[0], in_1[0], in_2[0]);
  or or_2 (out_3[1], in_1[1], in_2[1]);
  or or_3 (out_3[2], in_1[2], in_2[2]);
  or or_4 (out_3[3], in_1[3], in_2[3]);
endmodule

module Gfgg_SR_Latch (
  input  [3:0] in_1,
  input  [3:0] in_2,
  output [3:0] out_3
);

  wire [3:0] not_1_out, or_1_out;

  assign or_1_out = out_3 | in_1;  // OR_Gate or_1, 4 bits wide
  assign not_1_out = ~in_2;  // NOT_Gate not_1, 4 bits wide
  assign out_3 = or_1_out & not_1_out;  // AND_Gate and_1, 4 bits wide
endmodule
