// Logisim project Gfgg_PC_8.circ as structural Verilog
module Gfgg_Full_Adder (
  input  in_1,
  input  in_2,
  input  in_3,
  output out_4,
  output out_5
);

  wire and_1_out, and_2_out, xor_1_out;

  xor xor_1 (xor_1_out, in_1, in_2);
  and and_1 (and_1_out, in_2, in_1);
  and and_2 (and_2_out, xor_1_out, in_3);
  xor xor_2 (out_4, xor_1_out, in_3);
  or or_1 (out_5, and_2_out, and_1_out);
endmodule

module Gfgg_4Bit_Adder (
  input  in_1,
  input  in_2,
  input  in_3,
  input  in_4,
  input  in_5,
  input  in_6,
  input  in_7,
  input  in_8,
  input  in_9,
  input  in_10,
  output out_11,
  output out_12,
  output out_13,
  output out_14,
  output out_15
);

  wire gfgg_full_adder_1_out_4, gfgg_full_adder_1_out_5, gfgg_full_adder_2_out_4, gfgg_full_adder_2_out_5,
       gfgg_full_adder_3_out_4, gfgg_full_adder_3_out_5, gfgg_full_adder_4_out_4, gfgg_full_adder_4_out_5;

  Gfgg_Full_Adder gfgg_full_adder_1 (
    .in_1(in_4), .in_2(in_8), .in_3(in_9), .out_4(gfgg_full_adder_1_out_4), .out_5(gfgg_full_adder_1_out_5));
  Gfgg_Full_Adder gfgg_full_adder_2 (
    .in_1(in_3), .in_2(in_7), .in_3(gfgg_full_adder_1_out_5), .out_4(gfgg_full_adder_2_out_4),
    .out_5(gfgg_full_adder_2_out_5));
  Gfgg_Full_Adder gfgg_full_adder_3 (
    .in_1(in_2), .in_2(in_6), .in_3(gfgg_full_adder_2_out_5), .out_4(gfgg_full_adder_3_out_4),
    .out_5(gfgg_full_adder_3_out_5));
  Gfgg_Full_Adder gfgg_full_adder_4 (
    .in_1(in_1), .in_2(in_5), .in_3(gfgg_full_adder_3_out_5), .out_4(gfgg_full_adder_4_out_4),
    .out_5(gfgg_full_adder_4_out_5));
  and and_1 (out_11, in_10, gfgg_full_adder_4_out_4);
  and and_2 (out_12, gfgg_full_adder_3_out_4, in_10);
  and and_3 (out_13, gfgg_full_adder_2_out_4, in_10);
  and and_4 (out_14, gfgg_full_adder_1_out_4, in_10);
  and and_5 (out_15, gfgg_full_adder_4_out_5, in_10);
endmodule

module Gfgg_4Bit_ALU_1 (
  input  in_1,
  input  in_2,
  input  in_3,
  input  in_4,
  input  in_5,
  input  in_6,
  input  in_7,
  input  in_8,
  input  in_9,
  input  in_10,
  output out_11,
  output out_12,
  output out_13,
  output out_14,
  output out_15,
  output out_16,
  output out_17
);

  wire and_1_out, and_2_out, not_1_out, not_2_out, not_3_out, not_4_out, xor_1_out, xor_2_out, xor_3_out,
       xor_4_out;

  xor xor_1 (xor_1_out, in_5, in_9);
  xor xor_2 (xor_2_out, in_6, in_9);
  xor xor_3 (xor_3_out, in_7, in_9);
  xor xor_4 (xor_4_out, in_8, in_9);
  Gfgg_4Bit_Adder gfgg_4bit_adder_1 (
    .in_1(in_1), .in_2(in_2), .in_3(in_3), .in_4(in_4), .in_5(xor_1_out), .in_6(xor_2_out), .in_7(xor_3_out),
    .in_8(xor_4_out), .in_9(in_9), .in_10(in_10), .out_11(out_11), .out_12(out_12), .out_13(out_13),
    .out_14(out_14), .out_15(out_15));
  not not_1 (not_1_out, out_13);
  not not_2 (not_2_out, out_12);
  not not_3 (not_3_out, out_13);
  not not_4 (not_4_out, out_14);
  and and_1 (and_1_out, not_1_out, not_2_out);
  and and_2 (and_2_out, and_1_out, not_3_out);
  and and_3 (out_17, and_2_out, not_4_out);

  assign out_16 = out_11;
endmodule

module Gfgg_D_Latch (
  input  in_1,
  input  in_2,
  output out_3
);

  wire and_1_out, and_2_out, not_1_out, not_2_out, or_1_out;

  not not_1 (not_1_out, in_1);
  and and_1 (and_1_out, in_2, in_1);
  and and_2 (and_2_out, not_1_out, in_2);
  or or_1 (or_1_out, out_3, and_1_out);
  not not_2 (not_2_out, and_2_out);
  and and_3 (out_3, or_1_out, not_2_out);
endmodule

module Gfgg_4Bit_RAM (
  input  in_1,
  input  in_2,
  input  in_3,
  input  in_4,
  input  in_5,
  output out_6,
  output out_7,
  output out_8,
  output out_9
);

  Gfgg_D_Latch gfgg_d_latch_1 (.in_1(in_1), .in_2(in_5), .out_3(out_6));
  Gfgg_D_Latch gfgg_d_latch_2 (.in_1(in_2), .in_2(in_5), .out_3(out_7));
  Gfgg_D_Latch gfgg_d_latch_3 (.in_1(in_3), .in_2(in_5), .out_3(out_8));
  Gfgg_D_Latch gfgg_d_latch_4 (.in_1(in_4), .in_2(in_5), .out_3(out_9));
endmodule

module Gfgg_PC_1 (
  input  in_1,
  input  in_2,
  input  in_3,
  input  in_4,
  input  in_5,
  input  in_6,
  input  in_7,
  input  in_8,
  input  in_9,
  input  in_10,
  input  in_11,
  input  in_12,
  output out_13,
  output out_14,
  output out_15,
  output out_16,
  output out_17,
  output out_18,
  output out_19
);

  wire gfgg_4bit_ram_1_out_6, gfgg_4bit_ram_1_out_7, gfgg_4bit_ram_1_out_8, gfgg_4bit_ram_1_out_9,
       gfgg_4bit_ram_2_out_6, gfgg_4bit_ram_2_out_7, gfgg_4bit_ram_2_out_8, gfgg_4bit_ram_2_out_9;

  Gfgg_4Bit_RAM gfgg_4bit_ram_1 (
    .in_1(in_1), .in_2(in_2), .in_3(in_3), .in_4(in_4), .in_5(in_5), .out_6(gfgg_4bit_ram_1_out_6),
    .out_7(gfgg_4bit_ram_1_out_7), .out_8(gfgg_4bit_ram_1_out_8), .out_9(gfgg_4bit_ram_1_out_9));
  Gfgg_4Bit_RAM gfgg_4bit_ram_2 (
    .in_1(in_6), .in_2(in_7), .in_3(in_8), .in_4(in_9), .in_5(in_10), .out_6(gfgg_4bit_ram_2_out_6),
    .out_7(gfgg_4bit_ram_2_out_7), .out_8(gfgg_4bit_ram_2_out_8), .out_9(gfgg_4bit_ram_2_out_9));
  Gfgg_4Bit_ALU_1 gfgg_4bit_alu_1_1 (
    .in_1(gfgg_4bit_ram_1_out_6), .in_2(gfgg_4bit_ram_1_out_7), .in_3(gfgg_4bit_ram_1_out_8),
    .in_4(gfgg_4bit_ram_1_out_9), .in_5(gfgg_4bit_ram_2_out_6), .in_6(gfgg_4bit_ram_2_out_7),
    .in_7(gfgg_4bit_ram_2_out_8), .in_8(gfgg_4bit_ram_2_out_9), .in_9(in_11), .in_10(in_12), .out_11(out_13),
    .out_12(out_14), .out_13(out_15), .out_14(out_16), .out_15(out_17), .out_16(out_18), .out_17(out_19));
endmodule

module Gfgg_2Bit_Decoder (
  input  in_1,
  input  in_2,
  output out_3,
  output out_4,
  output out_5,
  output out_6
);

  wire not_1_out, not_2_out, not_3_out, not_4_out;

  not not_1 (not_1_out, in_2);
  not not_2 (not_2_out, in_1);
  not not_3 (not_3_out, in_1);
  not not_4 (not_4_out, in_2);
  and and_1 (out_3, not_1_out, not_2_out);
  and and_2 (out_4, in_2, not_3_out);
  and and_3 (out_5, not_4_out, in_1);
  and and_4 (out_6, in_2, in_1);
endmodule

module Gfgg_8Bit_RAM (
  input  in_1,
  input  in_2,
  input  in_3,
  input  in_4,
  input  in_5,
  input  in_6,
  input  in_7,
  input  in_8,
  input  in_9,
  output out_10,
  output out_11,
  output out_12,
  output out_13,
  output out_14,
  output out_15,
  output out_16,
  output out_17
);

  Gfgg_D_Latch gfgg_d_latch_1 (.in_1(in_1), .in_2(in_9), .out_3(out_10));
  Gfgg_D_Latch gfgg_d_latch_2 (.in_1(in_2), .in_2(in_9), .out_3(out_11));
  Gfgg_D_Latch gfgg_d_latch_3 (.in_1(in_3), .in_2(in_9), .out_3(out_12));
  Gfgg_D_Latch gfgg_d_latch_4 (.in_1(in_4), .in_2(in_9), .out_3(out_13));
  Gfgg_D_Latch gfgg_d_latch_5 (.in_1(in_5), .in_2(in_9), .out_3(out_14));
  Gfgg_D_Latch gfgg_d_latch_6 (.in_1(in_6), .in_2(in_9), .out_3(out_15));
  Gfgg_D_Latch gfgg_d_latch_7 (.in_1(in_7), .in_2(in_9), .out_3(out_16));
  Gfgg_D_Latch gfgg_d_latch_8 (.in_1(in_8), .in_2(in_9), .out_3(out_17));
endmodule

module Gfgg_8Bit_Adder (
  input  in_1,
  input  in_2,
  input  in_3,
  input  in_4,
  input  in_5,
  input  in_6,
  input  in_7,
  input  in_8,
  input  in_9,
  input  in_10,
  input  in_11,
  input  in_12,
  input  in_13,
  input  in_14,
  input  in_15,
  input  in_16,
  input  in_17,
  output out_18,
  output out_19,
  output out_20,
  output out_21,
  output out_22,
  output out_23,
  output out_24,
  output out_25,
  output out_26
);

  wire gfgg_full_adder_1_out_5, gfgg_full_adder_2_out_5, gfgg_full_adder_3_out_5, gfgg_full_adder_4_out_5,
       gfgg_full_adder_5_out_5, gfgg_full_adder_6_out_5, gfgg_full_adder_7_out_5;

  Gfgg_Full_Adder gfgg_full_adder_1 (
    .in_1(in_8), .in_2(in_16), .in_3(in_17), .out_4(out_25), .out_5(gfgg_full_adder_1_out_5));
  Gfgg_Full_Adder gfgg_full_adder_2 (
    .in_1(in_7), .in_2(in_15), .in_3(gfgg_full_adder_1_out_5), .out_4(out_24), .out_5(gfgg_full_adder_2_out_5));
  Gfgg_Full_Adder gfgg_full_adder_3 (
    .in_1(in_6), .in_2(in_14), .in_3(gfgg_full_adder_2_out_5), .out_4(out_23), .out_5(gfgg_full_adder_3_out_5));
  Gfgg_Full_Adder gfgg_full_adder_4 (
    .in_1(in_5), .in_2(in_13), .in_3(gfgg_full_adder_3_out_5), .out_4(out_22), .out_5(gfgg_full_adder_4_out_5));
  Gfgg_Full_Adder gfgg_full_adder_5 (
    .in_1(in_4), .in_2(in_12), .in_3(gfgg_full_adder_4_out_5), .out_4(out_21), .out_5(gfgg_full_adder_5_out_5));
  Gfgg_Full_Adder gfgg_full_adder_6 (
    .in_1(in_3), .in_2(in_11), .in_3(gfgg_full_adder_5_out_5), .out_4(out_20), .out_5(gfgg_full_adder_6_out_5));
  Gfgg_Full_Adder gfgg_full_adder_7 (
    .in_1(in_2), .in_2(in_10), .in_3(gfgg_full_adder_6_out_5), .out_4(out_19), .out_5(gfgg_full_adder_7_out_5));
  Gfgg_Full_Adder gfgg_full_adder_8 (
    .in_1(in_1), .in_2(in_9), .in_3(gfgg_full_adder_7_out_5), .out_4(out_18), .out_5(out_26));
endmodule

module Gfgg_8Bit_RAM_Adder (
  input  in_1,
  input  in_2,
  input  in_3,
  input  in_4,
  input  in_5,
  input  in_6,
  input  in_7,
  input  in_8,
  input  in_9,
  input  in_10,
  input  in_11,
  input  in_12,
  input  in_13,
  input  in_14,
  input  in_15,
  input  in_16,
  input  in_17,
  input  in_18,
  input  in_19,
  output out_20,
  output out_21,
  output out_22,
  output out_23,
  output out_24,
  output out_25,
  output out_26,
  output out_27,
  output out_28
);

  wire gfgg_8bit_ram_1_out_10, gfgg_8bit_ram_1_out_11, gfgg_8bit_ram_1_out_12, gfgg_8bit_ram_1_out_13,
       gfgg_8bit_ram_1_out_14, gfgg_8bit_ram_1_out_15, gfgg_8bit_ram_1_out_16, gfgg_8bit_ram_1_out_17,
       gfgg_8bit_ram_2_out_10, gfgg_8bit_ram_2_out_11, gfgg_8bit_ram_2_out_12, gfgg_8bit_ram_2_out_13,
       gfgg_8bit_ram_2_out_14, gfgg_8bit_ram_2_out_15, gfgg_8bit_ram_2_out_16, gfgg_8bit_ram_2_out_17;

  Gfgg_8Bit_RAM gfgg_8bit_ram_1 (
    .in_1(in_1), .in_2(in_2), .in_3(in_3), .in_4(in_4), .in_5(in_5), .in_6(in_6), .in_7(in_7), .in_8(in_8),
    .in_9(in_9), .out_10(gfgg_8bit_ram_1_out_10), .out_11(gfgg_8bit_ram_1_out_11),
    .out_12(gfgg_8bit_ram_1_out_12), .out_13(gfgg_8bit_ram_1_out_13), .out_14(gfgg_8bit_ram_1_out_14),
    .out_15(gfgg_8bit_ram_1_out_15), .out_16(gfgg_8bit_ram_1_out_16), .out_17(gfgg_8bit_ram_1_out_17));
  Gfgg_8Bit_RAM gfgg_8bit_ram_2 (
    .in_1(in_10), .in_2(in_11), .in_3(in_12), .in_4(in_13), .in_5(in_14), .in_6(in_15), .in_7(in_16),
    .in_8(in_17), .in_9(in_18), .out_10(gfgg_8bit_ram_2_out_10), .out_11(gfgg_8bit_ram_2_out_11),
    .out_12(gfgg_8bit_ram_2_out_12), .out_13(gfgg_8bit_ram_2_out_13), .out_14(gfgg_8bit_ram_2_out_14),
    .out_15(gfgg_8bit_ram_2_out_15), .out_16(gfgg_8bit_ram_2_out_16), .out_17(gfgg_8bit_ram_2_out_17));
  Gfgg_8Bit_Adder gfgg_8bit_adder_1 (
    .in_1(gfgg_8bit_ram_1_out_10), .in_2(gfgg_8bit_ram_1_out_11), .in_3(gfgg_8bit_ram_1_out_12),
    .in_4(gfgg_8bit_ram_1_out_13), .in_5(gfgg_8bit_ram_1_out_14), .in_6(gfgg_8bit_ram_1_out_15),
    .in_7(gfgg_8bit_ram_1_out_16), .in_8(gfgg_8bit_ram_1_out_17), .in_9(gfgg_8bit_ram_2_out_10),
    .in_10(gfgg_8bit_ram_2_out_11), .in_11(gfgg_8bit_ram_2_out_12), .in_12(gfgg_8bit_ram_2_out_13),
    .in_13(gfgg_8bit_ram_2_out_14), .in_14(gfgg_8bit_ram_2_out_15), .in_15(gfgg_8bit_ram_2_out_16),
    .in_16(gfgg_8bit_ram_2_out_17), .in_17(in_19), .out_18(out_20), .out_19(out_21), .out_20(out_22),
    .out_21(out_23), .out_22(out_24), .out_23(out_25), .out_24(out_26), .out_25(out_27), .out_26(out_28));
endmodule

module Gfgg_PC_3 (
  input  in_1,
  input  in_2,
  input  in_3,
  input  in_4,
  input  in_5,
  input  in_6,
  input  in_7,
  input  in_8,
  input  in_9,
  input  in_10,
  input  in_11,
  input  in_12,
  output out_13,
  output out_14,
  output out_15,
  output out_16,
  output out_17
);

  wire gfgg_2bit_decoder_1_out_3, gfgg_2bit_decoder_1_out_4, gfgg_2bit_decoder_1_out_5,
       gfgg_2bit_decoder_1_out_6, gfgg_8bit_ram_1_out_10, gfgg_8bit_ram_1_out_11, gfgg_8bit_ram_1_out_12,
       gfgg_8bit_ram_1_out_13, gfgg_8bit_ram_1_out_14, gfgg_8bit_ram_1_out_15, gfgg_8bit_ram_1_out_16,
       gfgg_8bit_ram_1_out_17;

  Gfgg_2Bit_Decoder gfgg_2bit_decoder_1 (
    .in_1(in_1), .in_2(in_2), .out_3(gfgg_2bit_decoder_1_out_3), .out_4(gfgg_2bit_decoder_1_out_4),
    .out_5(gfgg_2bit_decoder_1_out_5), .out_6(gfgg_2bit_decoder_1_out_6));
  Gfgg_8Bit_RAM gfgg_8bit_ram_1 (
    .in_1(in_3), .in_2(in_4), .in_3(in_5), .in_4(in_6), .in_5(in_7), .in_6(in_8), .in_7(in_9), .in_8(in_10),
    .in_9(in_11), .out_10(gfgg_8bit_ram_1_out_10), .out_11(gfgg_8bit_ram_1_out_11),
    .out_12(gfgg_8bit_ram_1_out_12), .out_13(gfgg_8bit_ram_1_out_13), .out_14(gfgg_8bit_ram_1_out_14),
    .out_15(gfgg_8bit_ram_1_out_15), .out_16(gfgg_8bit_ram_1_out_16), .out_17(gfgg_8bit_ram_1_out_17));
  Gfgg_4Bit_Adder gfgg_4bit_adder_1 (
    .in_1(gfgg_8bit_ram_1_out_10), .in_2(gfgg_8bit_ram_1_out_11), .in_3(gfgg_8bit_ram_1_out_12),
    .in_4(gfgg_8bit_ram_1_out_13), .in_5(gfgg_8bit_ram_1_out_14), .in_6(gfgg_8bit_ram_1_out_15),
    .in_7(gfgg_8bit_ram_1_out_16), .in_8(gfgg_8bit_ram_1_out_17), .in_9(in_12),
    .in_10(gfgg_2bit_decoder_1_out_3), .out_11(out_13), .out_12(out_14), .out_13(out_15), .out_14(out_16),
    .out_15(out_17));
  LED led_1 (.in(gfgg_2bit_decoder_1_out_3));
  LED led_2 (.in(gfgg_2bit_decoder_1_out_5));
  LED led_3 (.in(out_13));
  LED led_4 (.in(out_15));
  LED led_5 (.in(out_17));
  LED led_6 (.in(gfgg_2bit_decoder_1_out_4));
  LED led_7 (.in(gfgg_2bit_decoder_1_out_6));
  LED led_8 (.in(out_14));
  LED led_9 (.in(out_16));
endmodule

module Gfgg_PC_1_View (
  input  in_1,
  input  in_2,
  input  in_3,
  input  in_4,
  input  Confirm,
  input  in_6,
  input  in_7,
  input  in_8,
  input  in_9,
  input  Confirm_2,
  input  Subtract,
  output out_12,
  output out_13,
  output out_14,
  output out_15,
  output Carry,
  output Negative,
  output Zero
);

  Gfgg_PC_1 gfgg_pc_1_1 (
    .in_1(in_1), .in_2(in_2), .in_3(in_3), .in_4(in_4), .in_5(Confirm), .in_6(in_6), .in_7(in_7),
    .in_8(in_8), .in_9(in_9), .in_10(Confirm_2), .in_11(Subtract), .out_13(out_12), .out_14(out_13),
    .out_15(out_14), .out_16(out_15), .out_17(Carry), .out_18(Negative), .out_19(Zero));  // open: in_12

  // Notes on the sheet:
  //   Specs:
  //   1 Byte Ram
  //   4-Bit CPU
  //   -8
  //   4
  //   Number 1 (-8 - 7)
  //   Number 2 (-8 - 7)
  //   2
  //   1        1           0          1
  //   1
  //   -8 + 4 + 1 = -3
  //   Output (Binary)
endmodule

module Gfgg_PC_3_View (
  input  in_1,
  input  in_2,
  input  in_3,
  input  in_4,
  input  in_5,
  input  in_6,
  input  in_7,
  input  in_8,
  input  in_9,
  input  in_10,
  input  in_11,
  input  in_12,
  output out_13,
  output out_14,
  output out_15,
  output out_16,
  output out_17
);

  Gfgg_PC_3 gfgg_pc_3_1 (
    .in_1(in_1), .in_2(in_2), .in_3(in_3), .in_4(in_4), .in_5(in_5), .in_6(in_6), .in_7(in_7), .in_8(in_8),
    .in_9(in_9), .in_10(in_10), .in_11(in_11), .in_12(in_12), .out_13(out_13), .out_14(out_14),
    .out_15(out_15), .out_16(out_16), .out_17(out_17));

  // Notes on the sheet:
  //   8
  //   4
  //   2
  //   1            1            0           1
  //   1
  //   8x1 + 4x1 + 2x0 + 1x1 =  13
endmodule

module Gfgg_PC_1_Basic (
  input  in_1,
  input  in_2,
  input  in_3,
  input  in_4,
  input  in_5,
  input  in_6,
  input  in_7,
  input  in_8,
  input  in_9,
  output out_10,
  output out_11,
  output out_12,
  output out_13,
  output out_14
);

  Gfgg_4Bit_Adder_Old gfgg_4bit_adder_old_1 (
    .in_1(in_1), .in_2(in_2), .in_3(in_3), .in_4(in_4), .in_5(in_5), .in_6(in_6), .in_7(in_7), .in_8(in_8),
    .in_9(in_9), .out_10(out_10), .out_11(out_11), .out_12(out_12), .out_13(out_13), .out_14(out_14));

  // Notes on the sheet:
  //   Number 1 (0 - 15)
  //   Number 2 (0 - 15)
  //   8
  //   4
  //   2
  //   1        1           0          1
  //   1
  //   8 + 4 + 1 = 13
  //   Output (0 - 30)
endmodule

module Gfgg_4Bit_Adder_Old (
  input  in_1,
  input  in_2,
  input  in_3,
  input  in_4,
  input  in_5,
  input  in_6,
  input  in_7,
  input  in_8,
  input  in_9,
  output out_10,
  output out_11,
  output out_12,
  output out_13,
  output out_14
);

  wire gfgg_full_adder_1_out_5, gfgg_full_adder_2_out_5, gfgg_full_adder_3_out_5;

  Gfgg_Full_Adder gfgg_full_adder_1 (
    .in_1(in_4), .in_2(in_8), .in_3(in_9), .out_4(out_13), .out_5(gfgg_full_adder_1_out_5));
  Gfgg_Full_Adder gfgg_full_adder_2 (
    .in_1(in_3), .in_2(in_7), .in_3(gfgg_full_adder_1_out_5), .out_4(out_12), .out_5(gfgg_full_adder_2_out_5));
  Gfgg_Full_Adder gfgg_full_adder_3 (
    .in_1(in_2), .in_2(in_6), .in_3(gfgg_full_adder_2_out_5), .out_4(out_11), .out_5(gfgg_full_adder_3_out_5));
  Gfgg_Full_Adder gfgg_full_adder_4 (
    .in_1(in_1), .in_2(in_5), .in_3(gfgg_full_adder_3_out_5), .out_4(out_10), .out_5(out_14));
endmodule

module Gfgg_2Bit_RAM (
  input  in_1,
  input  in_2,
  input  in_3,
  output out_4,
  output out_5
);

  Gfgg_D_Latch gfgg_d_latch_1 (.in_1(in_1), .in_2(in_3), .out_3(out_4));
  Gfgg_D_Latch gfgg_d_latch_2 (.in_1(in_2), .in_2(in_3), .out_3(out_5));
endmodule

module Gfgg_8Bit_Register (
  input  Read_Enable,
  input  Write_Enable,
  input  in_3,
  input  in_4,
  input  in_5,
  input  in_6,
  input  in_7,
  input  in_8,
  input  in_9,
  input  in_10,
  output out_11,
  output out_12,
  output out_13,
  output out_14,
  output out_15,
  output out_16,
  output out_17,
  output out_18
);

  wire gfgg_d_latch_1_out_3, gfgg_d_latch_2_out_3, gfgg_d_latch_3_out_3, gfgg_d_latch_4_out_3,
       gfgg_d_latch_5_out_3, gfgg_d_latch_6_out_3, gfgg_d_latch_7_out_3, gfgg_d_latch_8_out_3;

  Gfgg_D_Latch gfgg_d_latch_1 (.in_1(in_3), .in_2(Write_Enable), .out_3(gfgg_d_latch_1_out_3));
  Gfgg_D_Latch gfgg_d_latch_2 (.in_1(in_4), .in_2(Write_Enable), .out_3(gfgg_d_latch_2_out_3));
  Gfgg_D_Latch gfgg_d_latch_3 (.in_1(in_5), .in_2(Write_Enable), .out_3(gfgg_d_latch_3_out_3));
  Gfgg_D_Latch gfgg_d_latch_4 (.in_1(in_6), .in_2(Write_Enable), .out_3(gfgg_d_latch_4_out_3));
  Gfgg_D_Latch gfgg_d_latch_5 (.in_1(in_7), .in_2(Write_Enable), .out_3(gfgg_d_latch_5_out_3));
  Gfgg_D_Latch gfgg_d_latch_6 (.in_1(in_8), .in_2(Write_Enable), .out_3(gfgg_d_latch_6_out_3));
  Gfgg_D_Latch gfgg_d_latch_7 (.in_1(in_9), .in_2(Write_Enable), .out_3(gfgg_d_latch_7_out_3));
  Gfgg_D_Latch gfgg_d_latch_8 (.in_1(in_10), .in_2(Write_Enable), .out_3(gfgg_d_latch_8_out_3));
  and and_1 (out_11, Read_Enable, gfgg_d_latch_1_out_3);
  and and_2 (out_12, Read_Enable, gfgg_d_latch_2_out_3);
  and and_3 (out_13, Read_Enable, gfgg_d_latch_3_out_3);
  and and_4 (out_14, Read_Enable, gfgg_d_latch_4_out_3);
  and and_5 (out_15, Read_Enable, gfgg_d_latch_5_out_3);
  and and_6 (out_16, Read_Enable, gfgg_d_latch_6_out_3);
  and and_7 (out_17, Read_Enable, gfgg_d_latch_7_out_3);
  and and_8 (out_18, Read_Enable, gfgg_d_latch_8_out_3);
endmodule

module Gfgg_8Bit_ALU (
  input  in_1,
  input  in_2,
  input  in_3,
  input  in_4,
  input  in_5,
  input  in_6,
  input  in_7,
  input  in_8,
  input  in_9,
  input  in_10,
  input  in_11,
  input  in_12,
  input  in_13,
  input  in_14,
  input  in_15,
  input  in_16,
  input  in_17,
  input  in_18,
  output out_19,
  output out_20,
  output out_21,
  output out_22,
  output out_23,
  output out_24,
  output out_25,
  output out_26,
  output Negative,
  output Carry,
  output Zero
);

  wire and_1_out, and_2_out, gfgg_8bit_adder_1_out_19, gfgg_8bit_adder_1_out_20, gfgg_8bit_adder_1_out_21,
       gfgg_8bit_adder_1_out_22, gfgg_8bit_adder_1_out_23, gfgg_8bit_adder_1_out_24,
       gfgg_8bit_adder_1_out_25, not_1_out, not_2_out, not_3_out, not_4_out, xor_1_out, xor_2_out, xor_3_out,
       xor_4_out, xor_5_out, xor_6_out, xor_7_out, xor_8_out;

  xor xor_1 (xor_1_out, in_10, in_18);
  xor xor_2 (xor_2_out, in_11, in_18);
  xor xor_3 (xor_3_out, in_12, in_18);
  xor xor_4 (xor_4_out, in_13, in_18);
  xor xor_5 (xor_5_out, in_14, in_18);
  xor xor_6 (xor_6_out, in_15, in_18);
  xor xor_7 (xor_7_out, in_16, in_18);
  xor xor_8 (xor_8_out, in_17, in_18);
  Gfgg_8Bit_Adder gfgg_8bit_adder_1 (
    .in_1(in_2), .in_2(in_3), .in_3(in_4), .in_4(in_5), .in_5(in_6), .in_6(in_7), .in_7(in_8), .in_8(in_9),
    .in_9(xor_1_out), .in_10(xor_2_out), .in_11(xor_3_out), .in_12(xor_4_out), .in_13(xor_5_out),
    .in_14(xor_6_out), .in_15(xor_7_out), .in_16(xor_8_out), .in_17(in_18), .out_18(Negative),
    .out_19(gfgg_8bit_adder_1_out_19), .out_20(gfgg_8bit_adder_1_out_20), .out_21(gfgg_8bit_adder_1_out_21),
    .out_22(gfgg_8bit_adder_1_out_22), .out_23(gfgg_8bit_adder_1_out_23), .out_24(gfgg_8bit_adder_1_out_24),
    .out_25(gfgg_8bit_adder_1_out_25), .out_26(Carry));
  not not_1 (not_1_out, gfgg_8bit_adder_1_out_25);
  not not_2 (not_2_out, gfgg_8bit_adder_1_out_24);
  not not_3 (not_3_out, gfgg_8bit_adder_1_out_23);
  not not_4 (not_4_out, gfgg_8bit_adder_1_out_22);
  and and_1 (and_1_out, not_1_out, not_2_out);
  and and_2 (and_2_out, not_3_out, not_4_out);
  and and_3 (Zero, and_1_out, and_2_out);
  and and_4 (out_19, in_1, Negative);
  and and_5 (out_20, in_1, gfgg_8bit_adder_1_out_19);
  and and_6 (out_21, gfgg_8bit_adder_1_out_20, in_1);
  and and_7 (out_22, gfgg_8bit_adder_1_out_21, in_1);
  and and_8 (out_23, gfgg_8bit_adder_1_out_22, in_1);
  and and_9 (out_24, gfgg_8bit_adder_1_out_23, in_1);
  and and_10 (out_25, gfgg_8bit_adder_1_out_24, in_1);
  and and_11 (out_26, gfgg_8bit_adder_1_out_25, in_1);
endmodule

module Gfgg_8Bit_RAM_V2 (
  input  in_1,
  input  in_2,
  input  in_3,
  input  in_4,
  input  in_5,
  input  in_6,
  input  in_7,
  input  in_8,
  input  in_9,
  output out_10,
  output out_11,
  output out_12,
  output out_13,
  output out_14,
  output out_15,
  output out_16,
  output out_17
);

  Gfgg_D_Latch gfgg_d_latch_1 (.in_1(in_1), .in_2(in_9), .out_3(out_10));
  Gfgg_D_Latch gfgg_d_latch_2 (.in_1(in_2), .in_2(in_9), .out_3(out_11));
  Gfgg_D_Latch gfgg_d_latch_3 (.in_1(in_3), .in_2(in_9), .out_3(out_12));
  Gfgg_D_Latch gfgg_d_latch_4 (.in_1(in_4), .in_2(in_9), .out_3(out_13));
  Gfgg_D_Latch gfgg_d_latch_5 (.in_1(in_5), .in_2(in_9), .out_3(out_14));
  Gfgg_D_Latch gfgg_d_latch_6 (.in_1(in_6), .in_2(in_9), .out_3(out_15));
  Gfgg_D_Latch gfgg_d_latch_7 (.in_1(in_7), .in_2(in_9), .out_3(out_16));
  Gfgg_D_Latch gfgg_d_latch_8 (.in_1(in_8), .in_2(in_9), .out_3(out_17));
endmodule

module Gfgg_4Byte_RAM (
  input  in_1,
  input  in_2,
  input  in_3,
  input  in_4,
  input  in_5,
  input  in_6,
  input  in_7,
  input  in_8,
  input  Write_Adress_4,
  input  Write_Adress_2,
  input  Write_Adress_1,
  input  Write_Enable,
  input  Read_Enable,
  input  Read_Adress_4,
  input  Read_Adress_2,
  input  Read_Adress_1,
  output out_17,
  output out_18,
  output out_19,
  output out_20,
  output out_21,
  output out_22,
  output out_23,
  output out_24,
  output out_25,
  output out_26,
  output out_27,
  output out_28,
  output out_29,
  output out_30,
  output out_31,
  output out_32,
  output out_33,
  output out_34,
  output out_35,
  output out_36,
  output out_37,
  output out_38,
  output out_39,
  output out_40,
  output out_41,
  output out_42,
  output out_43,
  output out_44,
  output out_45,
  output out_46,
  output out_47,
  output out_48
);

  wire and_1_out, and_2_out, and_3_out, and_4_out, and_5_out, and_6_out, and_7_out, and_8_out,
       gfgg_3bit_decoder_1_out_5, gfgg_3bit_decoder_1_out_6, gfgg_3bit_decoder_1_out_7,
       gfgg_3bit_decoder_1_out_8, gfgg_3bit_decoder_2_out_5, gfgg_3bit_decoder_2_out_6,
       gfgg_3bit_decoder_2_out_7, gfgg_3bit_decoder_2_out_8, gfgg_8bit_ram_1_out_10, gfgg_8bit_ram_1_out_11,
       gfgg_8bit_ram_1_out_12, gfgg_8bit_ram_1_out_13, gfgg_8bit_ram_1_out_14, gfgg_8bit_ram_1_out_15,
       gfgg_8bit_ram_1_out_16, gfgg_8bit_ram_1_out_17, gfgg_8bit_ram_2_out_10, gfgg_8bit_ram_2_out_11,
       gfgg_8bit_ram_2_out_12, gfgg_8bit_ram_2_out_13, gfgg_8bit_ram_2_out_14, gfgg_8bit_ram_2_out_15,
       gfgg_8bit_ram_2_out_16, gfgg_8bit_ram_2_out_17, gfgg_8bit_ram_3_out_10, gfgg_8bit_ram_3_out_11,
       gfgg_8bit_ram_3_out_12, gfgg_8bit_ram_3_out_13, gfgg_8bit_ram_3_out_14, gfgg_8bit_ram_3_out_15,
       gfgg_8bit_ram_3_out_16, gfgg_8bit_ram_3_out_17, gfgg_8bit_ram_4_out_10, gfgg_8bit_ram_4_out_11,
       gfgg_8bit_ram_4_out_12, gfgg_8bit_ram_4_out_13, gfgg_8bit_ram_4_out_14, gfgg_8bit_ram_4_out_15,
       gfgg_8bit_ram_4_out_16, gfgg_8bit_ram_4_out_17;

  Gfgg_3Bit_Decoder gfgg_3bit_decoder_1 (
    .in_1(Write_Adress_4), .in_2(Write_Adress_2), .in_3(Write_Adress_1), .out_5(gfgg_3bit_decoder_1_out_5),
    .out_6(gfgg_3bit_decoder_1_out_6), .out_7(gfgg_3bit_decoder_1_out_7), .out_8(gfgg_3bit_decoder_1_out_8));  // open: out_4, out_9, out_10, out_11
  Gfgg_3Bit_Decoder gfgg_3bit_decoder_2 (
    .in_1(Read_Adress_4), .in_2(Read_Adress_2), .in_3(Read_Adress_1), .out_5(gfgg_3bit_decoder_2_out_5),
    .out_6(gfgg_3bit_decoder_2_out_6), .out_7(gfgg_3bit_decoder_2_out_7), .out_8(gfgg_3bit_decoder_2_out_8));  // open: out_4, out_9, out_10, out_11
  and and_1 (and_1_out, gfgg_3bit_decoder_1_out_5, Write_Enable);
  and and_2 (and_2_out, gfgg_3bit_decoder_1_out_6, Write_Enable);
  and and_3 (and_3_out, gfgg_3bit_decoder_1_out_7, Write_Enable);
  and and_4 (and_4_out, gfgg_3bit_decoder_1_out_8, Write_Enable);
  and and_5 (and_5_out, gfgg_3bit_decoder_2_out_5, Read_Enable);
  and and_6 (and_6_out, gfgg_3bit_decoder_2_out_6, Read_Enable);
  and and_7 (and_7_out, gfgg_3bit_decoder_2_out_7, Read_Enable);
  and and_8 (and_8_out, gfgg_3bit_decoder_2_out_8, Read_Enable);
  Gfgg_8Bit_RAM gfgg_8bit_ram_1 (
    .in_1(in_1), .in_2(in_2), .in_3(in_3), .in_4(in_4), .in_5(in_5), .in_6(in_6), .in_7(in_7), .in_8(in_8),
    .in_9(and_1_out), .out_10(gfgg_8bit_ram_1_out_10), .out_11(gfgg_8bit_ram_1_out_11),
    .out_12(gfgg_8bit_ram_1_out_12), .out_13(gfgg_8bit_ram_1_out_13), .out_14(gfgg_8bit_ram_1_out_14),
    .out_15(gfgg_8bit_ram_1_out_15), .out_16(gfgg_8bit_ram_1_out_16), .out_17(gfgg_8bit_ram_1_out_17));
  Gfgg_8Bit_RAM gfgg_8bit_ram_2 (
    .in_1(in_1), .in_2(in_2), .in_3(in_3), .in_4(in_4), .in_5(in_5), .in_6(in_6), .in_7(in_7), .in_8(in_8),
    .in_9(and_2_out), .out_10(gfgg_8bit_ram_2_out_10), .out_11(gfgg_8bit_ram_2_out_11),
    .out_12(gfgg_8bit_ram_2_out_12), .out_13(gfgg_8bit_ram_2_out_13), .out_14(gfgg_8bit_ram_2_out_14),
    .out_15(gfgg_8bit_ram_2_out_15), .out_16(gfgg_8bit_ram_2_out_16), .out_17(gfgg_8bit_ram_2_out_17));
  Gfgg_8Bit_RAM gfgg_8bit_ram_3 (
    .in_1(in_1), .in_2(in_2), .in_3(in_3), .in_4(in_4), .in_5(in_5), .in_6(in_6), .in_7(in_7), .in_8(in_8),
    .in_9(and_3_out), .out_10(gfgg_8bit_ram_3_out_10), .out_11(gfgg_8bit_ram_3_out_11),
    .out_12(gfgg_8bit_ram_3_out_12), .out_13(gfgg_8bit_ram_3_out_13), .out_14(gfgg_8bit_ram_3_out_14),
    .out_15(gfgg_8bit_ram_3_out_15), .out_16(gfgg_8bit_ram_3_out_16), .out_17(gfgg_8bit_ram_3_out_17));
  Gfgg_8Bit_RAM gfgg_8bit_ram_4 (
    .in_1(in_1), .in_2(in_2), .in_3(in_3), .in_4(in_4), .in_5(in_5), .in_6(in_6), .in_7(in_7), .in_8(in_8),
    .in_9(and_4_out), .out_10(gfgg_8bit_ram_4_out_10), .out_11(gfgg_8bit_ram_4_out_11),
    .out_12(gfgg_8bit_ram_4_out_12), .out_13(gfgg_8bit_ram_4_out_13), .out_14(gfgg_8bit_ram_4_out_14),
    .out_15(gfgg_8bit_ram_4_out_15), .out_16(gfgg_8bit_ram_4_out_16), .out_17(gfgg_8bit_ram_4_out_17));
  and and_9 (out_17, gfgg_8bit_ram_1_out_10, and_5_out);
  and and_10 (out_18, gfgg_8bit_ram_1_out_11, and_5_out);
  and and_11 (out_19, gfgg_8bit_ram_1_out_12, and_5_out);
  and and_12 (out_20, gfgg_8bit_ram_1_out_13, and_5_out);
  and and_13 (out_21, gfgg_8bit_ram_1_out_14, and_5_out);
  and and_14 (out_22, gfgg_8bit_ram_1_out_15, and_5_out);
  and and_15 (out_23, gfgg_8bit_ram_1_out_16, and_5_out);
  and and_16 (out_24, gfgg_8bit_ram_1_out_17, and_5_out);
  and and_17 (out_25, gfgg_8bit_ram_2_out_10, and_6_out);
  and and_18 (out_26, gfgg_8bit_ram_2_out_11, and_6_out);
  and and_19 (out_27, gfgg_8bit_ram_2_out_12, and_6_out);
  and and_20 (out_28, gfgg_8bit_ram_2_out_13, and_6_out);
  and and_21 (out_29, gfgg_8bit_ram_2_out_14, and_6_out);
  and and_22 (out_30, gfgg_8bit_ram_2_out_15, and_6_out);
  and and_23 (out_31, gfgg_8bit_ram_2_out_16, and_6_out);
  and and_24 (out_32, gfgg_8bit_ram_2_out_17, and_6_out);
  and and_25 (out_33, gfgg_8bit_ram_3_out_10, and_7_out);
  and and_26 (out_34, gfgg_8bit_ram_3_out_11, and_7_out);
  and and_27 (out_35, gfgg_8bit_ram_3_out_12, and_7_out);
  and and_28 (out_36, gfgg_8bit_ram_3_out_13, and_7_out);
  and and_29 (out_37, gfgg_8bit_ram_3_out_14, and_7_out);
  and and_30 (out_38, gfgg_8bit_ram_3_out_15, and_7_out);
  and and_31 (out_39, gfgg_8bit_ram_3_out_16, and_7_out);
  and and_32 (out_40, gfgg_8bit_ram_3_out_17, and_7_out);
  and and_33 (out_41, gfgg_8bit_ram_4_out_10, and_8_out);
  and and_34 (out_42, gfgg_8bit_ram_4_out_11, and_8_out);
  and and_35 (out_43, gfgg_8bit_ram_4_out_12, and_8_out);
  and and_36 (out_44, gfgg_8bit_ram_4_out_13, and_8_out);
  and and_37 (out_45, gfgg_8bit_ram_4_out_14, and_8_out);
  and and_38 (out_46, gfgg_8bit_ram_4_out_15, and_8_out);
  and and_39 (out_47, gfgg_8bit_ram_4_out_16, and_8_out);
  and and_40 (out_48, gfgg_8bit_ram_4_out_17, and_8_out);
endmodule

module Gfgg_3Bit_Decoder (
  input  in_1,
  input  in_2,
  input  in_3,
  output out_4,
  output out_5,
  output out_6,
  output out_7,
  output out_8,
  output out_9,
  output out_10,
  output out_11
);

  wire not_1_out, not_2_out, not_3_out, not_4_out, not_5_out, not_6_out, not_7_out, not_8_out, not_9_out,
       not_10_out, not_11_out, not_12_out;

  not not_1 (not_1_out, in_1);
  not not_2 (not_2_out, in_2);
  not not_3 (not_3_out, in_3);
  not not_4 (not_4_out, in_1);
  not not_5 (not_5_out, in_2);
  not not_6 (not_6_out, in_1);
  not not_7 (not_7_out, in_3);
  not not_8 (not_8_out, in_1);
  not not_9 (not_9_out, in_2);
  not not_10 (not_10_out, in_3);
  not not_11 (not_11_out, in_2);
  not not_12 (not_12_out, in_3);
  Gfgg_3_AND gfgg_3_and_1 (.in_1(not_1_out), .in_2(not_2_out), .in_3(not_3_out), .out_4(out_4));
  Gfgg_3_AND gfgg_3_and_2 (.in_1(not_4_out), .in_2(not_5_out), .in_3(in_3), .out_4(out_5));
  Gfgg_3_AND gfgg_3_and_3 (.in_1(not_6_out), .in_2(in_2), .in_3(not_7_out), .out_4(out_6));
  Gfgg_3_AND gfgg_3_and_4 (.in_1(not_8_out), .in_2(in_2), .in_3(in_3), .out_4(out_7));
  Gfgg_3_AND gfgg_3_and_5 (.in_1(in_1), .in_2(not_9_out), .in_3(not_10_out), .out_4(out_8));
  Gfgg_3_AND gfgg_3_and_6 (.in_1(in_1), .in_2(not_11_out), .in_3(in_3), .out_4(out_9));
  Gfgg_3_AND gfgg_3_and_7 (.in_1(in_1), .in_2(in_2), .in_3(not_12_out), .out_4(out_10));
  Gfgg_3_AND gfgg_3_and_8 (.in_1(in_1), .in_2(in_2), .in_3(in_3), .out_4(out_11));
endmodule

module Gfgg_3_AND (
  input  in_1,
  input  in_2,
  input  in_3,
  output out_4
);

  wire and_1_out;

  and and_1 (and_1_out, in_1, in_2);
  and and_2 (out_4, and_1_out, in_3);
endmodule

module Gfgg_PC_4 (
  input  Enable_In,
  input  in_2,
  input  in_3,
  input  in_4,
  input  in_5,
  input  in_6,
  input  in_7,
  input  in_8,
  input  Enable_Reg0,
  input  in_10,
  input  Enable_Reg1,
  input  in_12,
  input  in_13,
  input  Enable_4,
  input  Enable_3,
  input  Enable_2,
  input  Enable_1,
  input  in_18,
  input  in_19,
  input  in_20,
  input  in_21,
  input  in_22,
  input  in_23,
  input  in_24,
  input  in_25,
  input  in_26,
  input  Enable_Reg2,
  input  in_28,
  input  in_29,
  input  in_30,
  output out_31,
  output out_32,
  output out_33,
  output out_34,
  output out_35,
  output out_36,
  output out_37,
  output out_38
);

  wire gfgg_4byte_ram_1_out_17, gfgg_4byte_ram_1_out_18, gfgg_4byte_ram_1_out_19, gfgg_4byte_ram_1_out_20,
       gfgg_4byte_ram_1_out_21, gfgg_4byte_ram_1_out_22, gfgg_4byte_ram_1_out_23, gfgg_4byte_ram_1_out_24,
       gfgg_4byte_ram_1_out_25, gfgg_4byte_ram_1_out_26, gfgg_4byte_ram_1_out_27, gfgg_4byte_ram_1_out_28,
       gfgg_4byte_ram_1_out_29, gfgg_4byte_ram_1_out_30, gfgg_4byte_ram_1_out_31, gfgg_4byte_ram_1_out_32,
       gfgg_4byte_ram_1_out_33, gfgg_4byte_ram_1_out_34, gfgg_4byte_ram_1_out_35, gfgg_4byte_ram_1_out_36,
       gfgg_4byte_ram_1_out_37, gfgg_4byte_ram_1_out_38, gfgg_4byte_ram_1_out_39, gfgg_4byte_ram_1_out_40,
       gfgg_4byte_ram_1_out_41, gfgg_4byte_ram_1_out_42, gfgg_4byte_ram_1_out_43, gfgg_4byte_ram_1_out_44,
       gfgg_4byte_ram_1_out_45, gfgg_4byte_ram_1_out_46, gfgg_4byte_ram_1_out_47, gfgg_4byte_ram_1_out_48,
       gfgg_8bit_alu_1_out_19, gfgg_8bit_alu_1_out_20, gfgg_8bit_alu_1_out_21, gfgg_8bit_alu_1_out_22,
       gfgg_8bit_alu_1_out_23, gfgg_8bit_alu_1_out_24, gfgg_8bit_alu_1_out_25, gfgg_8bit_alu_1_out_26,
       gfgg_8bit_con_buffer_6_out_10, gfgg_8bit_con_buffer_6_out_11, gfgg_8bit_con_buffer_6_out_12,
       gfgg_8bit_con_buffer_6_out_13, gfgg_8bit_con_buffer_6_out_15, gfgg_8bit_con_buffer_6_out_16,
       gfgg_8bit_con_buffer_6_out_17, gfgg_8bit_con_buffer_7_out_10, gfgg_8bit_con_buffer_7_out_11,
       gfgg_8bit_con_buffer_7_out_12, gfgg_8bit_con_buffer_7_out_13, gfgg_8bit_con_buffer_7_out_14,
       gfgg_8bit_con_buffer_7_out_15, gfgg_8bit_con_buffer_7_out_16, gfgg_8bit_con_buffer_7_out_17,
       gfgg_8bit_register_1_out_11, gfgg_8bit_register_1_out_12, gfgg_8bit_register_1_out_13,
       gfgg_8bit_register_1_out_14, gfgg_8bit_register_1_out_15, gfgg_8bit_register_1_out_16,
       gfgg_8bit_register_1_out_17, gfgg_8bit_register_1_out_18, gfgg_8bit_register_2_out_11,
       gfgg_8bit_register_2_out_12, gfgg_8bit_register_2_out_13, gfgg_8bit_register_2_out_14,
       gfgg_8bit_register_2_out_15, gfgg_8bit_register_2_out_16, gfgg_8bit_register_2_out_17,
       gfgg_8bit_register_2_out_18, gfgg_8bit_register_3_out_11, gfgg_8bit_register_3_out_12,
       gfgg_8bit_register_3_out_13, gfgg_8bit_register_3_out_14, gfgg_8bit_register_3_out_15,
       gfgg_8bit_register_3_out_16, gfgg_8bit_register_3_out_17, gfgg_8bit_register_3_out_18;

  Gfgg_4Byte_RAM gfgg_4byte_ram_1 (
    .in_1(out_31), .in_2(out_32), .in_3(out_33), .in_4(out_34), .in_5(out_35), .in_6(out_36), .in_7(out_37),
    .in_8(out_38), .Write_Adress_4(in_20), .Write_Adress_2(in_21), .Write_Adress_1(in_22),
    .Write_Enable(in_23), .Read_Enable(in_24), .Read_Adress_4(in_25), .Read_Adress_2(in_26),
    .Read_Adress_1(in_28), .out_17(gfgg_4byte_ram_1_out_17), .out_18(gfgg_4byte_ram_1_out_18),
    .out_19(gfgg_4byte_ram_1_out_19), .out_20(gfgg_4byte_ram_1_out_20), .out_21(gfgg_4byte_ram_1_out_21),
    .out_22(gfgg_4byte_ram_1_out_22), .out_23(gfgg_4byte_ram_1_out_23), .out_24(gfgg_4byte_ram_1_out_24),
    .out_25(gfgg_4byte_ram_1_out_25), .out_26(gfgg_4byte_ram_1_out_26), .out_27(gfgg_4byte_ram_1_out_27),
    .out_28(gfgg_4byte_ram_1_out_28), .out_29(gfgg_4byte_ram_1_out_29), .out_30(gfgg_4byte_ram_1_out_30),
    .out_31(gfgg_4byte_ram_1_out_31), .out_32(gfgg_4byte_ram_1_out_32), .out_33(gfgg_4byte_ram_1_out_33),
    .out_34(gfgg_4byte_ram_1_out_34), .out_35(gfgg_4byte_ram_1_out_35), .out_36(gfgg_4byte_ram_1_out_36),
    .out_37(gfgg_4byte_ram_1_out_37), .out_38(gfgg_4byte_ram_1_out_38), .out_39(gfgg_4byte_ram_1_out_39),
    .out_40(gfgg_4byte_ram_1_out_40), .out_41(gfgg_4byte_ram_1_out_41), .out_42(gfgg_4byte_ram_1_out_42),
    .out_43(gfgg_4byte_ram_1_out_43), .out_44(gfgg_4byte_ram_1_out_44), .out_45(gfgg_4byte_ram_1_out_45),
    .out_46(gfgg_4byte_ram_1_out_46), .out_47(gfgg_4byte_ram_1_out_47), .out_48(gfgg_4byte_ram_1_out_48));
  Gfgg_8Bit_Con_Buffer gfgg_8bit_con_buffer_1 (
    .Enable(Enable_1), .in_2(gfgg_4byte_ram_1_out_17), .in_3(gfgg_4byte_ram_1_out_18),
    .in_4(gfgg_4byte_ram_1_out_19), .in_5(gfgg_4byte_ram_1_out_20), .in_6(gfgg_4byte_ram_1_out_21),
    .in_7(gfgg_4byte_ram_1_out_22), .in_8(gfgg_4byte_ram_1_out_23), .in_9(gfgg_4byte_ram_1_out_24),
    .out_10(out_31), .out_11(out_32), .out_12(out_33), .out_13(out_34), .out_14(out_35), .out_15(out_36),
    .out_16(out_37), .out_17(out_38));
  Gfgg_8Bit_Con_Buffer gfgg_8bit_con_buffer_2 (
    .Enable(Enable_2), .in_2(gfgg_4byte_ram_1_out_25), .in_3(gfgg_4byte_ram_1_out_26),
    .in_4(gfgg_4byte_ram_1_out_27), .in_5(gfgg_4byte_ram_1_out_28), .in_6(gfgg_4byte_ram_1_out_29),
    .in_7(gfgg_4byte_ram_1_out_30), .in_8(gfgg_4byte_ram_1_out_31), .in_9(gfgg_4byte_ram_1_out_32),
    .out_10(out_31), .out_11(out_32), .out_12(out_33), .out_13(out_34), .out_14(out_35), .out_15(out_36),
    .out_16(out_37), .out_17(out_38));
  Gfgg_8Bit_Con_Buffer gfgg_8bit_con_buffer_3 (
    .Enable(Enable_3), .in_2(gfgg_4byte_ram_1_out_33), .in_3(gfgg_4byte_ram_1_out_34),
    .in_4(gfgg_4byte_ram_1_out_35), .in_5(gfgg_4byte_ram_1_out_36), .in_6(gfgg_4byte_ram_1_out_37),
    .in_7(gfgg_4byte_ram_1_out_38), .in_8(gfgg_4byte_ram_1_out_39), .in_9(gfgg_4byte_ram_1_out_40),
    .out_10(out_31), .out_11(out_32), .out_12(out_33), .out_13(out_34), .out_14(out_35), .out_15(out_36),
    .out_16(out_37), .out_17(out_38));
  Gfgg_8Bit_Con_Buffer gfgg_8bit_con_buffer_4 (
    .Enable(Enable_In), .in_2(in_2), .in_3(in_3), .in_4(in_4), .in_5(in_5), .in_6(in_6), .in_7(in_7),
    .in_8(in_8), .in_9(in_10), .out_10(out_31), .out_11(out_32), .out_12(out_33), .out_13(out_34),
    .out_14(out_35), .out_15(out_36), .out_16(out_37), .out_17(out_38));
  Gfgg_8Bit_Con_Buffer gfgg_8bit_con_buffer_5 (
    .Enable(Enable_4), .in_2(gfgg_4byte_ram_1_out_41), .in_3(gfgg_4byte_ram_1_out_42),
    .in_4(gfgg_4byte_ram_1_out_43), .in_5(gfgg_4byte_ram_1_out_44), .in_6(gfgg_4byte_ram_1_out_45),
    .in_7(gfgg_4byte_ram_1_out_46), .in_8(gfgg_4byte_ram_1_out_47), .in_9(gfgg_4byte_ram_1_out_48),
    .out_10(out_31), .out_11(out_32), .out_12(out_33), .out_13(out_34), .out_14(out_35), .out_15(out_36),
    .out_16(out_37), .out_17(out_38));
  Gfgg_8Bit_Con_Buffer gfgg_8bit_con_buffer_6 (
    .Enable(Enable_Reg0), .in_2(out_31), .in_3(out_32), .in_4(out_33), .in_5(out_34), .in_6(out_35),
    .in_7(out_36), .in_8(out_37), .in_9(out_38), .out_10(gfgg_8bit_con_buffer_6_out_10),
    .out_11(gfgg_8bit_con_buffer_6_out_11), .out_12(gfgg_8bit_con_buffer_6_out_12),
    .out_13(gfgg_8bit_con_buffer_6_out_13), .out_14(gfgg_8bit_con_buffer_6_out_10),
    .out_15(gfgg_8bit_con_buffer_6_out_15), .out_16(gfgg_8bit_con_buffer_6_out_16),
    .out_17(gfgg_8bit_con_buffer_6_out_17));
  Gfgg_8Bit_Con_Buffer gfgg_8bit_con_buffer_7 (
    .Enable(Enable_Reg1), .in_2(out_31), .in_3(out_32), .in_4(out_33), .in_5(out_34), .in_6(out_35),
    .in_7(out_36), .in_8(out_37), .in_9(out_38), .out_10(gfgg_8bit_con_buffer_7_out_10),
    .out_11(gfgg_8bit_con_buffer_7_out_11), .out_12(gfgg_8bit_con_buffer_7_out_12),
    .out_13(gfgg_8bit_con_buffer_7_out_13), .out_14(gfgg_8bit_con_buffer_7_out_14),
    .out_15(gfgg_8bit_con_buffer_7_out_15), .out_16(gfgg_8bit_con_buffer_7_out_16),
    .out_17(gfgg_8bit_con_buffer_7_out_17));
  Gfgg_8Bit_Register gfgg_8bit_register_1 (
    .Read_Enable(in_12), .Write_Enable(in_13), .in_3(gfgg_8bit_con_buffer_6_out_10),
    .in_4(gfgg_8bit_con_buffer_6_out_11), .in_5(gfgg_8bit_con_buffer_6_out_12),
    .in_6(gfgg_8bit_con_buffer_6_out_13), .in_7(gfgg_8bit_con_buffer_6_out_10),
    .in_8(gfgg_8bit_con_buffer_6_out_15), .in_9(gfgg_8bit_con_buffer_6_out_16),
    .in_10(gfgg_8bit_con_buffer_6_out_17), .out_11(gfgg_8bit_register_1_out_11),
    .out_12(gfgg_8bit_register_1_out_12), .out_13(gfgg_8bit_register_1_out_13),
    .out_14(gfgg_8bit_register_1_out_14), .out_15(gfgg_8bit_register_1_out_15),
    .out_16(gfgg_8bit_register_1_out_16), .out_17(gfgg_8bit_register_1_out_17),
    .out_18(gfgg_8bit_register_1_out_18));
  Gfgg_8Bit_Register gfgg_8bit_register_2 (
    .Read_Enable(in_18), .Write_Enable(in_19), .in_3(gfgg_8bit_con_buffer_7_out_10),
    .in_4(gfgg_8bit_con_buffer_7_out_11), .in_5(gfgg_8bit_con_buffer_7_out_12),
    .in_6(gfgg_8bit_con_buffer_7_out_13), .in_7(gfgg_8bit_con_buffer_7_out_14),
    .in_8(gfgg_8bit_con_buffer_7_out_15), .in_9(gfgg_8bit_con_buffer_7_out_16),
    .in_10(gfgg_8bit_con_buffer_7_out_17), .out_11(gfgg_8bit_register_2_out_11),
    .out_12(gfgg_8bit_register_2_out_12), .out_13(gfgg_8bit_register_2_out_13),
    .out_14(gfgg_8bit_register_2_out_14), .out_15(gfgg_8bit_register_2_out_15),
    .out_16(gfgg_8bit_register_2_out_16), .out_17(gfgg_8bit_register_2_out_17),
    .out_18(gfgg_8bit_register_2_out_18));
  Gfgg_8Bit_Register gfgg_8bit_register_3 (
    .Read_Enable(in_29), .Write_Enable(in_30), .in_3(gfgg_8bit_alu_1_out_19), .in_4(gfgg_8bit_alu_1_out_20),
    .in_5(gfgg_8bit_alu_1_out_21), .in_6(gfgg_8bit_alu_1_out_22), .in_7(gfgg_8bit_alu_1_out_23),
    .in_8(gfgg_8bit_alu_1_out_24), .in_9(gfgg_8bit_alu_1_out_25), .in_10(gfgg_8bit_alu_1_out_26),
    .out_11(gfgg_8bit_register_3_out_11), .out_12(gfgg_8bit_register_3_out_12),
    .out_13(gfgg_8bit_register_3_out_13), .out_14(gfgg_8bit_register_3_out_14),
    .out_15(gfgg_8bit_register_3_out_15), .out_16(gfgg_8bit_register_3_out_16),
    .out_17(gfgg_8bit_register_3_out_17), .out_18(gfgg_8bit_register_3_out_18));
  Gfgg_8Bit_ALU gfgg_8bit_alu_1 (
    .in_1(gfgg_8bit_register_1_out_11), .in_2(gfgg_8bit_register_1_out_12),
    .in_3(gfgg_8bit_register_1_out_13), .in_4(gfgg_8bit_register_1_out_14),
    .in_5(gfgg_8bit_register_1_out_15), .in_6(gfgg_8bit_register_1_out_16),
    .in_7(gfgg_8bit_register_1_out_17), .in_8(gfgg_8bit_register_1_out_18),
    .in_9(gfgg_8bit_register_2_out_11), .in_10(gfgg_8bit_register_2_out_12),
    .in_11(gfgg_8bit_register_2_out_13), .in_12(gfgg_8bit_register_2_out_14),
    .in_13(gfgg_8bit_register_2_out_15), .in_14(gfgg_8bit_register_2_out_16),
    .in_15(gfgg_8bit_register_2_out_17), .in_16(gfgg_8bit_register_2_out_18),
    .out_19(gfgg_8bit_alu_1_out_19), .out_20(gfgg_8bit_alu_1_out_20), .out_21(gfgg_8bit_alu_1_out_21),
    .out_22(gfgg_8bit_alu_1_out_22), .out_23(gfgg_8bit_alu_1_out_23), .out_24(gfgg_8bit_alu_1_out_24),
    .out_25(gfgg_8bit_alu_1_out_25), .out_26(gfgg_8bit_alu_1_out_26));  // open: in_17, in_18, Negative, Carry, Zero
  Gfgg_8Bit_Con_Buffer gfgg_8bit_con_buffer_8 (
    .Enable(Enable_Reg2), .in_2(gfgg_8bit_register_3_out_11), .in_3(gfgg_8bit_register_3_out_12),
    .in_4(gfgg_8bit_register_3_out_13), .in_5(gfgg_8bit_register_3_out_14),
    .in_6(gfgg_8bit_register_3_out_15), .in_7(gfgg_8bit_register_3_out_16),
    .in_8(gfgg_8bit_register_3_out_17), .in_9(gfgg_8bit_register_3_out_18), .out_10(out_31), .out_11(out_32),
    .out_12(out_33), .out_13(out_34), .out_14(out_35), .out_15(out_36), .out_16(out_37), .out_17(out_38));
endmodule

module Gfgg_Enable_And (
  input  in_1,
  input  in_2,
  input  in_3,
  input  in_4,
  input  in_5,
  input  in_6,
  input  in_7,
  input  in_8,
  input  Enable,
  output out_10,
  output out_11,
  output out_12,
  output out_13,
  output out_14,
  output out_15,
  output out_16,
  output out_17
);

  and and_1 (out_10, Enable, in_1);
  and and_2 (out_11, Enable, in_2);
  and and_3 (out_12, Enable, in_3);
  and and_4 (out_13, Enable, in_4);
  and and_5 (out_14, Enable, in_5);
  and and_6 (out_15, Enable, in_6);
  and and_7 (out_16, Enable, in_7);
  and and_8 (out_17, Enable, in_8);
endmodule

module Gfgg_8_Bit_Tri_Buffer (
  input  Disabled,
  input  Enable,
  input  in_3,
  input  in_4,
  input  in_5,
  input  in_6,
  input  in_7,
  input  in_8,
  input  in_9,
  input  in_10,
  output out_11,
  output out_12,
  output out_13,
  output out_14,
  output out_15,
  output out_16,
  output out_17,
  output out_18
);

  Gfgg_2_1_MUX gfgg_2_1_mux_1 (.in_1(Disabled), .in_2(in_3), .in_3(Enable), .out_4(out_11));
  Gfgg_2_1_MUX gfgg_2_1_mux_2 (.in_1(Disabled), .in_2(in_4), .in_3(Enable), .out_4(out_12));
  Gfgg_2_1_MUX gfgg_2_1_mux_3 (.in_1(Disabled), .in_2(in_5), .in_3(Enable), .out_4(out_13));
  Gfgg_2_1_MUX gfgg_2_1_mux_4 (.in_1(Disabled), .in_2(in_6), .in_3(Enable), .out_4(out_14));
  Gfgg_2_1_MUX gfgg_2_1_mux_5 (.in_1(Disabled), .in_2(in_7), .in_3(Enable), .out_4(out_15));
  Gfgg_2_1_MUX gfgg_2_1_mux_6 (.in_1(Disabled), .in_2(in_8), .in_3(Enable), .out_4(out_16));
  Gfgg_2_1_MUX gfgg_2_1_mux_7 (.in_1(Disabled), .in_2(in_9), .in_3(Enable), .out_4(out_17));
  Gfgg_2_1_MUX gfgg_2_1_mux_8 (.in_1(Disabled), .in_2(in_10), .in_3(Enable), .out_4(out_18));
endmodule

module Gfgg_2_1_MUX (
  input  in_1,
  input  in_2,
  input  in_3,
  output out_4
);

  wire and_1_out, and_2_out, not_1_out;

  not not_1 (not_1_out, in_3);
  and and_1 (and_1_out, in_1, not_1_out);
  and and_2 (and_2_out, in_2, in_3);
  or or_1 (out_4, and_1_out, and_2_out);
endmodule

module Gfgg_8Bit_Con_Buffer (
  input  Enable,
  input  in_2,
  input  in_3,
  input  in_4,
  input  in_5,
  input  in_6,
  input  in_7,
  input  in_8,
  input  in_9,
  output out_10,
  output out_11,
  output out_12,
  output out_13,
  output out_14,
  output out_15,
  output out_16,
  output out_17
);

  assign out_10 = Enable ? in_2 : 1'bz;  // Controlled_Buffer controlled_buffer_1
  assign out_11 = Enable ? in_3 : 1'bz;  // Controlled_Buffer controlled_buffer_2
  assign out_12 = Enable ? in_4 : 1'bz;  // Controlled_Buffer controlled_buffer_3
  assign out_13 = Enable ? in_5 : 1'bz;  // Controlled_Buffer controlled_buffer_4
  assign out_14 = Enable ? in_6 : 1'bz;  // Controlled_Buffer controlled_buffer_5
  assign out_15 = Enable ? in_7 : 1'bz;  // Controlled_Buffer controlled_buffer_6
  assign out_16 = Enable ? in_8 : 1'bz;  // Controlled_Buffer controlled_buffer_7
  assign out_17 = Enable ? in_9 : 1'bz;  // Controlled_Buffer controlled_buffer_8
endmodule

module Gfgg_PC_6 (
  input  Enable_Reg1,
  input  Enable_Reg0,
  input  Enable_In,
  input  in_4,
  input  in_5,
  input  in_6,
  input  in_7,
  input  in_8,
  input  in_9,
  input  in_10,
  input  in_11,
  input  in_12,
  input  in_13,
  input  in_14,
  input  in_15,
  input  in_16,
  input  in_17,
  input  Enable_Reg2,
  input  in_19,
  input  in_20,
  input  in_21,
  input  in_22,
  input  in_23,
  input  in_24,
  input  in_25,
  input  in_26,
  input  in_27,
  input  in_28,
  output out_29,
  output out_30,
  output out_31,
  output out_32,
  output out_33,
  output out_34,
  output out_35,
  output out_36,
  output out_37,
  output out_38,
  output out_39
);

  wire gfgg_6byte_ram_1_out_17, gfgg_6byte_ram_1_out_18, gfgg_6byte_ram_1_out_19, gfgg_6byte_ram_1_out_20,
       gfgg_6byte_ram_1_out_21, gfgg_6byte_ram_1_out_22, gfgg_6byte_ram_1_out_23, gfgg_6byte_ram_1_out_24,
       gfgg_8bit_alu_1_out_19, gfgg_8bit_alu_1_out_20, gfgg_8bit_alu_1_out_21, gfgg_8bit_alu_1_out_22,
       gfgg_8bit_alu_1_out_23, gfgg_8bit_alu_1_out_24, gfgg_8bit_alu_1_out_25, gfgg_8bit_alu_1_out_26,
       gfgg_8bit_con_buffer_3_out_10, gfgg_8bit_con_buffer_3_out_11, gfgg_8bit_con_buffer_3_out_12,
       gfgg_8bit_con_buffer_3_out_13, gfgg_8bit_con_buffer_3_out_14, gfgg_8bit_con_buffer_3_out_15,
       gfgg_8bit_con_buffer_3_out_16, gfgg_8bit_con_buffer_3_out_17, gfgg_8bit_con_buffer_4_out_10,
       gfgg_8bit_con_buffer_4_out_11, gfgg_8bit_con_buffer_4_out_12, gfgg_8bit_con_buffer_4_out_13,
       gfgg_8bit_con_buffer_4_out_14, gfgg_8bit_con_buffer_4_out_15, gfgg_8bit_con_buffer_4_out_16,
       gfgg_8bit_con_buffer_4_out_17, gfgg_8bit_register_1_out_11, gfgg_8bit_register_1_out_12,
       gfgg_8bit_register_1_out_13, gfgg_8bit_register_1_out_14, gfgg_8bit_register_1_out_15,
       gfgg_8bit_register_1_out_16, gfgg_8bit_register_1_out_17, gfgg_8bit_register_1_out_18,
       gfgg_8bit_register_2_out_11, gfgg_8bit_register_2_out_12, gfgg_8bit_register_2_out_13,
       gfgg_8bit_register_2_out_14, gfgg_8bit_register_2_out_15, gfgg_8bit_register_2_out_16,
       gfgg_8bit_register_2_out_17, gfgg_8bit_register_2_out_18, gfgg_8bit_register_3_out_11,
       gfgg_8bit_register_3_out_12, gfgg_8bit_register_3_out_13, gfgg_8bit_register_3_out_14,
       gfgg_8bit_register_3_out_15, gfgg_8bit_register_3_out_16, gfgg_8bit_register_3_out_17,
       gfgg_8bit_register_3_out_18;

  Gfgg_6Byte_RAM gfgg_6byte_ram_1 (
    .in_1(out_32), .in_2(out_33), .in_3(out_34), .in_4(out_35), .in_5(out_36), .in_6(out_37), .in_7(out_38),
    .in_8(out_39), .Write_Adress_4(in_21), .Write_Adress_2(in_22), .Write_Adress_1(in_23),
    .Write_Enable(in_24), .Read_Enable(in_25), .Read_Adress_4(in_26), .Read_Adress_2(in_27),
    .Read_Adress_1(in_28), .out_17(gfgg_6byte_ram_1_out_17), .out_18(gfgg_6byte_ram_1_out_18),
    .out_19(gfgg_6byte_ram_1_out_19), .out_20(gfgg_6byte_ram_1_out_20), .out_21(gfgg_6byte_ram_1_out_21),
    .out_22(gfgg_6byte_ram_1_out_22), .out_23(gfgg_6byte_ram_1_out_23), .out_24(gfgg_6byte_ram_1_out_24));
  Gfgg_8Bit_Con_Buffer gfgg_8bit_con_buffer_1 (
    .Enable(in_17), .in_2(gfgg_6byte_ram_1_out_17), .in_3(gfgg_6byte_ram_1_out_18),
    .in_4(gfgg_6byte_ram_1_out_19), .in_5(gfgg_6byte_ram_1_out_20), .in_6(gfgg_6byte_ram_1_out_21),
    .in_7(gfgg_6byte_ram_1_out_22), .in_8(gfgg_6byte_ram_1_out_23), .in_9(gfgg_6byte_ram_1_out_24),
    .out_10(out_32), .out_11(out_33), .out_12(out_34), .out_13(out_35), .out_14(out_36), .out_15(out_37),
    .out_16(out_38), .out_17(out_39));
  Gfgg_8Bit_Con_Buffer gfgg_8bit_con_buffer_2 (
    .Enable(Enable_In), .in_2(in_4), .in_3(in_5), .in_4(in_6), .in_5(in_7), .in_6(in_8), .in_7(in_9),
    .in_8(in_10), .in_9(in_11), .out_10(out_32), .out_11(out_33), .out_12(out_34), .out_13(out_35),
    .out_14(out_36), .out_15(out_37), .out_16(out_38), .out_17(out_39));
  Gfgg_8Bit_Con_Buffer gfgg_8bit_con_buffer_3 (
    .Enable(Enable_Reg0), .in_2(out_32), .in_3(out_33), .in_4(out_34), .in_5(out_35), .in_6(out_36),
    .in_7(out_37), .in_8(out_38), .in_9(out_39), .out_10(gfgg_8bit_con_buffer_3_out_10),
    .out_11(gfgg_8bit_con_buffer_3_out_11), .out_12(gfgg_8bit_con_buffer_3_out_12),
    .out_13(gfgg_8bit_con_buffer_3_out_13), .out_14(gfgg_8bit_con_buffer_3_out_14),
    .out_15(gfgg_8bit_con_buffer_3_out_15), .out_16(gfgg_8bit_con_buffer_3_out_16),
    .out_17(gfgg_8bit_con_buffer_3_out_17));
  Gfgg_8Bit_Con_Buffer gfgg_8bit_con_buffer_4 (
    .Enable(Enable_Reg1), .in_2(out_32), .in_3(out_33), .in_4(out_34), .in_5(out_35), .in_6(out_36),
    .in_7(out_37), .in_8(out_38), .in_9(out_39), .out_10(gfgg_8bit_con_buffer_4_out_10),
    .out_11(gfgg_8bit_con_buffer_4_out_11), .out_12(gfgg_8bit_con_buffer_4_out_12),
    .out_13(gfgg_8bit_con_buffer_4_out_13), .out_14(gfgg_8bit_con_buffer_4_out_14),
    .out_15(gfgg_8bit_con_buffer_4_out_15), .out_16(gfgg_8bit_con_buffer_4_out_16),
    .out_17(gfgg_8bit_con_buffer_4_out_17));
  Gfgg_8Bit_Register gfgg_8bit_register_1 (
    .Read_Enable(in_12), .Write_Enable(in_13), .in_3(gfgg_8bit_con_buffer_3_out_10),
    .in_4(gfgg_8bit_con_buffer_3_out_11), .in_5(gfgg_8bit_con_buffer_3_out_12),
    .in_6(gfgg_8bit_con_buffer_3_out_13), .in_7(gfgg_8bit_con_buffer_3_out_14),
    .in_8(gfgg_8bit_con_buffer_3_out_15), .in_9(gfgg_8bit_con_buffer_3_out_16),
    .in_10(gfgg_8bit_con_buffer_3_out_17), .out_11(gfgg_8bit_register_1_out_11),
    .out_12(gfgg_8bit_register_1_out_12), .out_13(gfgg_8bit_register_1_out_13),
    .out_14(gfgg_8bit_register_1_out_14), .out_15(gfgg_8bit_register_1_out_15),
    .out_16(gfgg_8bit_register_1_out_16), .out_17(gfgg_8bit_register_1_out_17),
    .out_18(gfgg_8bit_register_1_out_18));
  Gfgg_8Bit_Register gfgg_8bit_register_2 (
    .Read_Enable(in_15), .Write_Enable(in_16), .in_3(gfgg_8bit_con_buffer_4_out_10),
    .in_4(gfgg_8bit_con_buffer_4_out_11), .in_5(gfgg_8bit_con_buffer_4_out_12),
    .in_6(gfgg_8bit_con_buffer_4_out_13), .in_7(gfgg_8bit_con_buffer_4_out_14),
    .in_8(gfgg_8bit_con_buffer_4_out_15), .in_9(gfgg_8bit_con_buffer_4_out_16),
    .in_10(gfgg_8bit_con_buffer_4_out_17), .out_11(gfgg_8bit_register_2_out_11),
    .out_12(gfgg_8bit_register_2_out_12), .out_13(gfgg_8bit_register_2_out_13),
    .out_14(gfgg_8bit_register_2_out_14), .out_15(gfgg_8bit_register_2_out_15),
    .out_16(gfgg_8bit_register_2_out_16), .out_17(gfgg_8bit_register_2_out_17),
    .out_18(gfgg_8bit_register_2_out_18));
  Gfgg_8Bit_Register gfgg_8bit_register_3 (
    .Read_Enable(in_19), .Write_Enable(in_20), .in_3(gfgg_8bit_alu_1_out_19), .in_4(gfgg_8bit_alu_1_out_20),
    .in_5(gfgg_8bit_alu_1_out_21), .in_6(gfgg_8bit_alu_1_out_22), .in_7(gfgg_8bit_alu_1_out_23),
    .in_8(gfgg_8bit_alu_1_out_24), .in_9(gfgg_8bit_alu_1_out_25), .in_10(gfgg_8bit_alu_1_out_26),
    .out_11(gfgg_8bit_register_3_out_11), .out_12(gfgg_8bit_register_3_out_12),
    .out_13(gfgg_8bit_register_3_out_13), .out_14(gfgg_8bit_register_3_out_14),
    .out_15(gfgg_8bit_register_3_out_15), .out_16(gfgg_8bit_register_3_out_16),
    .out_17(gfgg_8bit_register_3_out_17), .out_18(gfgg_8bit_register_3_out_18));
  Gfgg_8Bit_ALU gfgg_8bit_alu_1 (
    .in_1(gfgg_8bit_register_1_out_11), .in_2(gfgg_8bit_register_1_out_12),
    .in_3(gfgg_8bit_register_1_out_13), .in_4(gfgg_8bit_register_1_out_14),
    .in_5(gfgg_8bit_register_1_out_15), .in_6(gfgg_8bit_register_1_out_16),
    .in_7(gfgg_8bit_register_1_out_17), .in_8(gfgg_8bit_register_1_out_18),
    .in_9(gfgg_8bit_register_2_out_11), .in_10(gfgg_8bit_register_2_out_12),
    .in_11(gfgg_8bit_register_2_out_13), .in_12(gfgg_8bit_register_2_out_14),
    .in_13(gfgg_8bit_register_2_out_15), .in_14(gfgg_8bit_register_2_out_16),
    .in_15(gfgg_8bit_register_2_out_17), .in_16(gfgg_8bit_register_2_out_18), .in_17(in_14),
    .out_19(gfgg_8bit_alu_1_out_19), .out_20(gfgg_8bit_alu_1_out_20), .out_21(gfgg_8bit_alu_1_out_21),
    .out_22(gfgg_8bit_alu_1_out_22), .out_23(gfgg_8bit_alu_1_out_23), .out_24(gfgg_8bit_alu_1_out_24),
    .out_25(gfgg_8bit_alu_1_out_25), .out_26(gfgg_8bit_alu_1_out_26), .Negative(out_29), .Carry(out_30),
    .Zero(out_31));  // open: in_18
  Gfgg_8Bit_Con_Buffer gfgg_8bit_con_buffer_5 (
    .Enable(Enable_Reg2), .in_2(gfgg_8bit_register_3_out_11), .in_3(gfgg_8bit_register_3_out_12),
    .in_4(gfgg_8bit_register_3_out_13), .in_5(gfgg_8bit_register_3_out_14),
    .in_6(gfgg_8bit_register_3_out_15), .in_7(gfgg_8bit_register_3_out_16),
    .in_8(gfgg_8bit_register_3_out_17), .in_9(gfgg_8bit_register_3_out_18), .out_10(out_32), .out_11(out_33),
    .out_12(out_34), .out_13(out_35), .out_14(out_36), .out_15(out_37), .out_16(out_38), .out_17(out_39));
endmodule

module Gfgg_Bitwise_And (
  input  in_1,
  input  in_2,
  input  in_3,
  input  in_4,
  input  in_5,
  input  in_6,
  input  in_7,
  input  in_8,
  input  in_9,
  input  in_10,
  input  in_11,
  input  in_12,
  input  in_13,
  input  in_14,
  input  in_15,
  input  in_16,
  output out_17,
  output out_18,
  output out_19,
  output out_20,
  output out_21,
  output out_22,
  output out_23,
  output out_24
);

  and and_1 (out_17, in_1, in_9);
  and and_2 (out_18, in_2, in_10);
  and and_3 (out_19, in_3, in_11);
  and and_4 (out_20, in_4, in_12);
  and and_5 (out_21, in_5, in_13);
  and and_6 (out_22, in_6, in_14);
  and and_7 (out_23, in_7, in_15);
  and and_8 (out_24, in_8, in_16);
endmodule

module Gfgg_4_OR (
  input  in_1,
  input  in_2,
  input  in_3,
  input  in_4,
  output out_5
);

  wire or_1_out, or_2_out;

  or or_1 (or_1_out, in_1, in_2);
  or or_2 (or_2_out, in_3, in_4);
  or or_3 (out_5, or_1_out, or_2_out);
endmodule

module Gfgg_6Byte_RAM (
  input  in_1,
  input  in_2,
  input  in_3,
  input  in_4,
  input  in_5,
  input  in_6,
  input  in_7,
  input  in_8,
  input  Write_Adress_4,
  input  Write_Adress_2,
  input  Write_Adress_1,
  input  Write_Enable,
  input  Read_Enable,
  input  Read_Adress_4,
  input  Read_Adress_2,
  input  Read_Adress_1,
  output out_17,
  output out_18,
  output out_19,
  output out_20,
  output out_21,
  output out_22,
  output out_23,
  output out_24
);

  wire and_1_out, and_2_out, and_3_out, and_4_out, and_5_out, and_6_out, and_7_out, and_8_out, and_9_out,
       and_10_out, and_11_out, and_12_out, gfgg_3bit_decoder_1_out_5, gfgg_3bit_decoder_1_out_6,
       gfgg_3bit_decoder_1_out_7, gfgg_3bit_decoder_1_out_8, gfgg_3bit_decoder_1_out_9,
       gfgg_3bit_decoder_1_out_10, gfgg_3bit_decoder_2_out_5, gfgg_3bit_decoder_2_out_6,
       gfgg_3bit_decoder_2_out_7, gfgg_3bit_decoder_2_out_8, gfgg_3bit_decoder_2_out_9,
       gfgg_3bit_decoder_2_out_10, gfgg_8bit_ram_1_out_10, gfgg_8bit_ram_1_out_11, gfgg_8bit_ram_1_out_12,
       gfgg_8bit_ram_1_out_13, gfgg_8bit_ram_1_out_14, gfgg_8bit_ram_1_out_15, gfgg_8bit_ram_1_out_16,
       gfgg_8bit_ram_1_out_17, gfgg_8bit_ram_2_out_10, gfgg_8bit_ram_2_out_11, gfgg_8bit_ram_2_out_12,
       gfgg_8bit_ram_2_out_13, gfgg_8bit_ram_2_out_14, gfgg_8bit_ram_2_out_15, gfgg_8bit_ram_2_out_16,
       gfgg_8bit_ram_2_out_17, gfgg_8bit_ram_3_out_10, gfgg_8bit_ram_3_out_11, gfgg_8bit_ram_3_out_12,
       gfgg_8bit_ram_3_out_13, gfgg_8bit_ram_3_out_14, gfgg_8bit_ram_3_out_15, gfgg_8bit_ram_3_out_16,
       gfgg_8bit_ram_3_out_17, gfgg_8bit_ram_4_out_10, gfgg_8bit_ram_4_out_11, gfgg_8bit_ram_4_out_12,
       gfgg_8bit_ram_4_out_13, gfgg_8bit_ram_4_out_14, gfgg_8bit_ram_4_out_15, gfgg_8bit_ram_4_out_16,
       gfgg_8bit_ram_4_out_17, gfgg_8bit_ram_5_out_10, gfgg_8bit_ram_5_out_11, gfgg_8bit_ram_5_out_12,
       gfgg_8bit_ram_5_out_13, gfgg_8bit_ram_5_out_14, gfgg_8bit_ram_5_out_15, gfgg_8bit_ram_5_out_16,
       gfgg_8bit_ram_5_out_17, gfgg_8bit_ram_6_out_10, gfgg_8bit_ram_6_out_11, gfgg_8bit_ram_6_out_12,
       gfgg_8bit_ram_6_out_13, gfgg_8bit_ram_6_out_14, gfgg_8bit_ram_6_out_15, gfgg_8bit_ram_6_out_16,
       gfgg_8bit_ram_6_out_17, gfgg_enable_and_1_out_10, gfgg_enable_and_1_out_11, gfgg_enable_and_1_out_12,
       gfgg_enable_and_1_out_13, gfgg_enable_and_1_out_14, gfgg_enable_and_1_out_15,
       gfgg_enable_and_1_out_16, gfgg_enable_and_1_out_17, gfgg_enable_and_2_out_10,
       gfgg_enable_and_2_out_11, gfgg_enable_and_2_out_12, gfgg_enable_and_2_out_13,
       gfgg_enable_and_2_out_14, gfgg_enable_and_2_out_15, gfgg_enable_and_2_out_16,
       gfgg_enable_and_2_out_17, gfgg_enable_and_3_out_10, gfgg_enable_and_3_out_11,
       gfgg_enable_and_3_out_12, gfgg_enable_and_3_out_13, gfgg_enable_and_3_out_14,
       gfgg_enable_and_3_out_15, gfgg_enable_and_3_out_16, gfgg_enable_and_3_out_17,
       gfgg_enable_and_4_out_10, gfgg_enable_and_4_out_11, gfgg_enable_and_4_out_12,
       gfgg_enable_and_4_out_13, gfgg_enable_and_4_out_14, gfgg_enable_and_4_out_15,
       gfgg_enable_and_4_out_16, gfgg_enable_and_4_out_17, gfgg_enable_and_5_out_10,
       gfgg_enable_and_5_out_11, gfgg_enable_and_5_out_12, gfgg_enable_and_5_out_13,
       gfgg_enable_and_5_out_14, gfgg_enable_and_5_out_15, gfgg_enable_and_5_out_16,
       gfgg_enable_and_5_out_17, gfgg_enable_and_6_out_10, gfgg_enable_and_6_out_11,
       gfgg_enable_and_6_out_12, gfgg_enable_and_6_out_13, gfgg_enable_and_6_out_14,
       gfgg_enable_and_6_out_15, gfgg_enable_and_6_out_16, gfgg_enable_and_6_out_17;

  Gfgg_3Bit_Decoder gfgg_3bit_decoder_1 (
    .in_1(Write_Adress_4), .in_2(Write_Adress_2), .in_3(Write_Adress_1), .out_5(gfgg_3bit_decoder_1_out_5),
    .out_6(gfgg_3bit_decoder_1_out_6), .out_7(gfgg_3bit_decoder_1_out_7), .out_8(gfgg_3bit_decoder_1_out_8),
    .out_9(gfgg_3bit_decoder_1_out_9), .out_10(gfgg_3bit_decoder_1_out_10));  // open: out_4, out_11
  Gfgg_3Bit_Decoder gfgg_3bit_decoder_2 (
    .in_1(Read_Adress_4), .in_2(Read_Adress_2), .in_3(Read_Adress_1), .out_5(gfgg_3bit_decoder_2_out_5),
    .out_6(gfgg_3bit_decoder_2_out_6), .out_7(gfgg_3bit_decoder_2_out_7), .out_8(gfgg_3bit_decoder_2_out_8),
    .out_9(gfgg_3bit_decoder_2_out_9), .out_10(gfgg_3bit_decoder_2_out_10));  // open: out_4, out_11
  and and_1 (and_1_out, gfgg_3bit_decoder_1_out_5, Write_Enable);
  and and_2 (and_2_out, gfgg_3bit_decoder_1_out_6, Write_Enable);
  and and_3 (and_3_out, gfgg_3bit_decoder_1_out_7, Write_Enable);
  and and_4 (and_4_out, gfgg_3bit_decoder_1_out_8, Write_Enable);
  and and_5 (and_5_out, gfgg_3bit_decoder_1_out_9, Write_Enable);
  and and_6 (and_6_out, gfgg_3bit_decoder_1_out_10, Write_Enable);
  and and_7 (and_7_out, gfgg_3bit_decoder_2_out_5, Read_Enable);
  and and_8 (and_8_out, gfgg_3bit_decoder_2_out_6, Read_Enable);
  and and_9 (and_9_out, gfgg_3bit_decoder_2_out_7, Read_Enable);
  and and_10 (and_10_out, gfgg_3bit_decoder_2_out_8, Read_Enable);
  and and_11 (and_11_out, gfgg_3bit_decoder_2_out_9, Read_Enable);
  and and_12 (and_12_out, gfgg_3bit_decoder_2_out_10, Read_Enable);
  Gfgg_8Bit_RAM gfgg_8bit_ram_1 (
    .in_1(in_1), .in_2(in_2), .in_3(in_3), .in_4(in_4), .in_5(in_5), .in_6(in_6), .in_7(in_7), .in_8(in_8),
    .in_9(and_1_out), .out_10(gfgg_8bit_ram_1_out_10), .out_11(gfgg_8bit_ram_1_out_11),
    .out_12(gfgg_8bit_ram_1_out_12), .out_13(gfgg_8bit_ram_1_out_13), .out_14(gfgg_8bit_ram_1_out_14),
    .out_15(gfgg_8bit_ram_1_out_15), .out_16(gfgg_8bit_ram_1_out_16), .out_17(gfgg_8bit_ram_1_out_17));
  Gfgg_8Bit_RAM gfgg_8bit_ram_2 (
    .in_1(in_1), .in_2(in_2), .in_3(in_3), .in_4(in_4), .in_5(in_5), .in_6(in_6), .in_7(in_7), .in_8(in_8),
    .in_9(and_2_out), .out_10(gfgg_8bit_ram_2_out_10), .out_11(gfgg_8bit_ram_2_out_11),
    .out_12(gfgg_8bit_ram_2_out_12), .out_13(gfgg_8bit_ram_2_out_13), .out_14(gfgg_8bit_ram_2_out_14),
    .out_15(gfgg_8bit_ram_2_out_15), .out_16(gfgg_8bit_ram_2_out_16), .out_17(gfgg_8bit_ram_2_out_17));
  Gfgg_8Bit_RAM gfgg_8bit_ram_3 (
    .in_1(in_1), .in_2(in_2), .in_3(in_3), .in_4(in_4), .in_5(in_5), .in_6(in_6), .in_7(in_7), .in_8(in_8),
    .in_9(and_3_out), .out_10(gfgg_8bit_ram_3_out_10), .out_11(gfgg_8bit_ram_3_out_11),
    .out_12(gfgg_8bit_ram_3_out_12), .out_13(gfgg_8bit_ram_3_out_13), .out_14(gfgg_8bit_ram_3_out_14),
    .out_15(gfgg_8bit_ram_3_out_15), .out_16(gfgg_8bit_ram_3_out_16), .out_17(gfgg_8bit_ram_3_out_17));
  Gfgg_8Bit_RAM gfgg_8bit_ram_4 (
    .in_1(in_1), .in_2(in_2), .in_3(in_3), .in_4(in_4), .in_5(in_5), .in_6(in_6), .in_7(in_7), .in_8(in_8),
    .in_9(and_4_out), .out_10(gfgg_8bit_ram_4_out_10), .out_11(gfgg_8bit_ram_4_out_11),
    .out_12(gfgg_8bit_ram_4_out_12), .out_13(gfgg_8bit_ram_4_out_13), .out_14(gfgg_8bit_ram_4_out_14),
    .out_15(gfgg_8bit_ram_4_out_15), .out_16(gfgg_8bit_ram_4_out_16), .out_17(gfgg_8bit_ram_4_out_17));
  Gfgg_8Bit_RAM gfgg_8bit_ram_5 (
    .in_1(in_1), .in_2(in_2), .in_3(in_3), .in_4(in_4), .in_5(in_5), .in_6(in_6), .in_7(in_7), .in_8(in_8),
    .in_9(and_5_out), .out_10(gfgg_8bit_ram_5_out_10), .out_11(gfgg_8bit_ram_5_out_11),
    .out_12(gfgg_8bit_ram_5_out_12), .out_13(gfgg_8bit_ram_5_out_13), .out_14(gfgg_8bit_ram_5_out_14),
    .out_15(gfgg_8bit_ram_5_out_15), .out_16(gfgg_8bit_ram_5_out_16), .out_17(gfgg_8bit_ram_5_out_17));
  Gfgg_8Bit_RAM gfgg_8bit_ram_6 (
    .in_1(in_1), .in_2(in_2), .in_3(in_3), .in_4(in_4), .in_5(in_5), .in_6(in_6), .in_7(in_7), .in_8(in_8),
    .in_9(and_6_out), .out_10(gfgg_8bit_ram_6_out_10), .out_11(gfgg_8bit_ram_6_out_11),
    .out_12(gfgg_8bit_ram_6_out_12), .out_13(gfgg_8bit_ram_6_out_13), .out_14(gfgg_8bit_ram_6_out_14),
    .out_15(gfgg_8bit_ram_6_out_15), .out_16(gfgg_8bit_ram_6_out_16), .out_17(gfgg_8bit_ram_6_out_17));
  Gfgg_Enable_And gfgg_enable_and_1 (
    .in_1(gfgg_8bit_ram_1_out_10), .in_2(gfgg_8bit_ram_1_out_11), .in_3(gfgg_8bit_ram_1_out_12),
    .in_4(gfgg_8bit_ram_1_out_13), .in_5(gfgg_8bit_ram_1_out_14), .in_6(gfgg_8bit_ram_1_out_15),
    .in_7(gfgg_8bit_ram_1_out_16), .in_8(gfgg_8bit_ram_1_out_17), .Enable(and_7_out),
    .out_10(gfgg_enable_and_1_out_10), .out_11(gfgg_enable_and_1_out_11), .out_12(gfgg_enable_and_1_out_12),
    .out_13(gfgg_enable_and_1_out_13), .out_14(gfgg_enable_and_1_out_14), .out_15(gfgg_enable_and_1_out_15),
    .out_16(gfgg_enable_and_1_out_16), .out_17(gfgg_enable_and_1_out_17));
  Gfgg_Enable_And gfgg_enable_and_2 (
    .in_1(gfgg_8bit_ram_2_out_10), .in_2(gfgg_8bit_ram_2_out_11), .in_3(gfgg_8bit_ram_2_out_12),
    .in_4(gfgg_8bit_ram_2_out_13), .in_5(gfgg_8bit_ram_2_out_14), .in_6(gfgg_8bit_ram_2_out_15),
    .in_7(gfgg_8bit_ram_2_out_16), .in_8(gfgg_8bit_ram_2_out_17), .Enable(and_8_out),
    .out_10(gfgg_enable_and_2_out_10), .out_11(gfgg_enable_and_2_out_11), .out_12(gfgg_enable_and_2_out_12),
    .out_13(gfgg_enable_and_2_out_13), .out_14(gfgg_enable_and_2_out_14), .out_15(gfgg_enable_and_2_out_15),
    .out_16(gfgg_enable_and_2_out_16), .out_17(gfgg_enable_and_2_out_17));
  Gfgg_Enable_And gfgg_enable_and_3 (
    .in_1(gfgg_8bit_ram_3_out_10), .in_2(gfgg_8bit_ram_3_out_11), .in_3(gfgg_8bit_ram_3_out_12),
    .in_4(gfgg_8bit_ram_3_out_13), .in_5(gfgg_8bit_ram_3_out_14), .in_6(gfgg_8bit_ram_3_out_15),
    .in_7(gfgg_8bit_ram_3_out_16), .in_8(gfgg_8bit_ram_3_out_17), .Enable(and_9_out),
    .out_10(gfgg_enable_and_3_out_10), .out_11(gfgg_enable_and_3_out_11), .out_12(gfgg_enable_and_3_out_12),
    .out_13(gfgg_enable_and_3_out_13), .out_14(gfgg_enable_and_3_out_14), .out_15(gfgg_enable_and_3_out_15),
    .out_16(gfgg_enable_and_3_out_16), .out_17(gfgg_enable_and_3_out_17));
  Gfgg_Enable_And gfgg_enable_and_4 (
    .in_1(gfgg_8bit_ram_4_out_10), .in_2(gfgg_8bit_ram_4_out_11), .in_3(gfgg_8bit_ram_4_out_12),
    .in_4(gfgg_8bit_ram_4_out_13), .in_5(gfgg_8bit_ram_4_out_14), .in_6(gfgg_8bit_ram_4_out_15),
    .in_7(gfgg_8bit_ram_4_out_16), .in_8(gfgg_8bit_ram_4_out_17), .Enable(and_10_out),
    .out_10(gfgg_enable_and_4_out_10), .out_11(gfgg_enable_and_4_out_11), .out_12(gfgg_enable_and_4_out_12),
    .out_13(gfgg_enable_and_4_out_13), .out_14(gfgg_enable_and_4_out_14), .out_15(gfgg_enable_and_4_out_15),
    .out_16(gfgg_enable_and_4_out_16), .out_17(gfgg_enable_and_4_out_17));
  Gfgg_Enable_And gfgg_enable_and_5 (
    .in_1(gfgg_8bit_ram_5_out_10), .in_2(gfgg_8bit_ram_5_out_11), .in_3(gfgg_8bit_ram_5_out_12),
    .in_4(gfgg_8bit_ram_5_out_13), .in_5(gfgg_8bit_ram_5_out_14), .in_6(gfgg_8bit_ram_5_out_15),
    .in_7(gfgg_8bit_ram_5_out_16), .in_8(gfgg_8bit_ram_5_out_17), .Enable(and_11_out),
    .out_10(gfgg_enable_and_5_out_10), .out_11(gfgg_enable_and_5_out_11), .out_12(gfgg_enable_and_5_out_12),
    .out_13(gfgg_enable_and_5_out_13), .out_14(gfgg_enable_and_5_out_14), .out_15(gfgg_enable_and_5_out_15),
    .out_16(gfgg_enable_and_5_out_16), .out_17(gfgg_enable_and_5_out_17));
  Gfgg_Enable_And gfgg_enable_and_6 (
    .in_1(gfgg_8bit_ram_6_out_10), .in_2(gfgg_8bit_ram_6_out_11), .in_3(gfgg_8bit_ram_6_out_12),
    .in_4(gfgg_8bit_ram_6_out_13), .in_5(gfgg_8bit_ram_6_out_14), .in_6(gfgg_8bit_ram_6_out_15),
    .in_7(gfgg_8bit_ram_6_out_16), .in_8(gfgg_8bit_ram_6_out_17), .Enable(and_12_out),
    .out_10(gfgg_enable_and_6_out_10), .out_11(gfgg_enable_and_6_out_11), .out_12(gfgg_enable_and_6_out_12),
    .out_13(gfgg_enable_and_6_out_13), .out_14(gfgg_enable_and_6_out_14), .out_15(gfgg_enable_and_6_out_15),
    .out_16(gfgg_enable_and_6_out_16), .out_17(gfgg_enable_and_6_out_17));
  Gfgg_6_OR gfgg_6_or_1 (
    .in_1(gfgg_enable_and_1_out_10), .in_2(gfgg_enable_and_2_out_10), .in_3(gfgg_enable_and_3_out_10),
    .in_4(gfgg_enable_and_4_out_10), .in_5(gfgg_enable_and_5_out_10), .in_6(gfgg_enable_and_6_out_10),
    .out_7(out_17));
  Gfgg_6_OR gfgg_6_or_2 (
    .in_1(gfgg_enable_and_1_out_11), .in_2(gfgg_enable_and_2_out_11), .in_3(gfgg_enable_and_3_out_11),
    .in_4(gfgg_enable_and_4_out_11), .in_5(gfgg_enable_and_5_out_11), .in_6(gfgg_enable_and_6_out_11),
    .out_7(out_18));
  Gfgg_6_OR gfgg_6_or_3 (
    .in_1(gfgg_enable_and_1_out_12), .in_2(gfgg_enable_and_2_out_12), .in_3(gfgg_enable_and_3_out_12),
    .in_4(gfgg_enable_and_4_out_12), .in_5(gfgg_enable_and_5_out_12), .in_6(gfgg_enable_and_6_out_12),
    .out_7(out_19));
  Gfgg_6_OR gfgg_6_or_4 (
    .in_1(gfgg_enable_and_1_out_13), .in_2(gfgg_enable_and_2_out_13), .in_3(gfgg_enable_and_3_out_13),
    .in_4(gfgg_enable_and_4_out_13), .in_5(gfgg_enable_and_5_out_13), .in_6(gfgg_enable_and_6_out_13),
    .out_7(out_20));
  Gfgg_6_OR gfgg_6_or_5 (
    .in_1(gfgg_enable_and_1_out_14), .in_2(gfgg_enable_and_2_out_14), .in_3(gfgg_enable_and_3_out_14),
    .in_4(gfgg_enable_and_4_out_14), .in_5(gfgg_enable_and_5_out_14), .in_6(gfgg_enable_and_6_out_14),
    .out_7(out_21));
  Gfgg_6_OR gfgg_6_or_6 (
    .in_1(gfgg_enable_and_1_out_15), .in_2(gfgg_enable_and_2_out_15), .in_3(gfgg_enable_and_3_out_15),
    .in_4(gfgg_enable_and_4_out_15), .in_5(gfgg_enable_and_5_out_15), .in_6(gfgg_enable_and_6_out_15),
    .out_7(out_22));
  Gfgg_6_OR gfgg_6_or_7 (
    .in_1(gfgg_enable_and_1_out_16), .in_2(gfgg_enable_and_2_out_16), .in_3(gfgg_enable_and_3_out_16),
    .in_4(gfgg_enable_and_4_out_16), .in_5(gfgg_enable_and_5_out_16), .in_6(gfgg_enable_and_6_out_16),
    .out_7(out_23));
  Gfgg_6_OR gfgg_6_or_8 (
    .in_1(gfgg_enable_and_1_out_17), .in_2(gfgg_enable_and_2_out_17), .in_3(gfgg_enable_and_3_out_17),
    .in_4(gfgg_enable_and_4_out_17), .in_5(gfgg_enable_and_5_out_17), .in_6(gfgg_enable_and_6_out_17),
    .out_7(out_24));
endmodule

module Gfgg_6_OR (
  input  in_1,
  input  in_2,
  input  in_3,
  input  in_4,
  input  in_5,
  input  in_6,
  output out_7
);

  wire gfgg_4_or_1_out_5, or_1_out;

  or or_1 (or_1_out, in_1, in_2);
  Gfgg_4_OR gfgg_4_or_1 (.in_1(in_3), .in_2(in_4), .in_3(in_5), .in_4(in_6), .out_5(gfgg_4_or_1_out_5));
  or or_2 (out_7, or_1_out, gfgg_4_or_1_out_5);
endmodule

module Gfgg_8Byte_RAM (
  input  in_1,
  input  in_2,
  input  in_3,
  input  in_4,
  input  in_5,
  input  in_6,
  input  in_7,
  input  in_8,
  input  Write_Adress_4,
  input  Write_Adress_2,
  input  Write_Adress_1,
  input  Write_Enable,
  input  Read_Enable,
  input  Read_Adress_4,
  input  Read_Adress_2,
  input  Read_Adress_1,
  output out_17,
  output out_18,
  output out_19,
  output out_20,
  output out_21,
  output out_22,
  output out_23,
  output out_24
);

  wire and_1_out, and_2_out, and_3_out, and_4_out, and_5_out, and_6_out, and_7_out, and_8_out, and_9_out,
       and_10_out, and_11_out, and_12_out, and_13_out, and_14_out, and_15_out, and_16_out,
       gfgg_3bit_decoder_1_out_4, gfgg_3bit_decoder_1_out_5, gfgg_3bit_decoder_1_out_6,
       gfgg_3bit_decoder_1_out_7, gfgg_3bit_decoder_1_out_8, gfgg_3bit_decoder_1_out_9,
       gfgg_3bit_decoder_1_out_10, gfgg_3bit_decoder_1_out_11, gfgg_3bit_decoder_2_out_4,
       gfgg_3bit_decoder_2_out_5, gfgg_3bit_decoder_2_out_6, gfgg_3bit_decoder_2_out_7,
       gfgg_3bit_decoder_2_out_8, gfgg_3bit_decoder_2_out_9, gfgg_3bit_decoder_2_out_10,
       gfgg_3bit_decoder_2_out_11, gfgg_8bit_ram_1_out_10, gfgg_8bit_ram_1_out_11, gfgg_8bit_ram_1_out_12,
       gfgg_8bit_ram_1_out_13, gfgg_8bit_ram_1_out_14, gfgg_8bit_ram_1_out_15, gfgg_8bit_ram_1_out_16,
       gfgg_8bit_ram_1_out_17, gfgg_8bit_ram_2_out_10, gfgg_8bit_ram_2_out_11, gfgg_8bit_ram_2_out_12,
       gfgg_8bit_ram_2_out_13, gfgg_8bit_ram_2_out_14, gfgg_8bit_ram_2_out_15, gfgg_8bit_ram_2_out_16,
       gfgg_8bit_ram_2_out_17, gfgg_8bit_ram_3_out_10, gfgg_8bit_ram_3_out_11, gfgg_8bit_ram_3_out_12,
       gfgg_8bit_ram_3_out_13, gfgg_8bit_ram_3_out_14, gfgg_8bit_ram_3_out_15, gfgg_8bit_ram_3_out_16,
       gfgg_8bit_ram_3_out_17, gfgg_8bit_ram_4_out_10, gfgg_8bit_ram_4_out_11, gfgg_8bit_ram_4_out_12,
       gfgg_8bit_ram_4_out_13, gfgg_8bit_ram_4_out_14, gfgg_8bit_ram_4_out_15, gfgg_8bit_ram_4_out_16,
       gfgg_8bit_ram_4_out_17, gfgg_8bit_ram_5_out_10, gfgg_8bit_ram_5_out_11, gfgg_8bit_ram_5_out_12,
       gfgg_8bit_ram_5_out_13, gfgg_8bit_ram_5_out_14, gfgg_8bit_ram_5_out_15, gfgg_8bit_ram_5_out_16,
       gfgg_8bit_ram_5_out_17, gfgg_8bit_ram_6_out_10, gfgg_8bit_ram_6_out_11, gfgg_8bit_ram_6_out_12,
       gfgg_8bit_ram_6_out_13, gfgg_8bit_ram_6_out_14, gfgg_8bit_ram_6_out_15, gfgg_8bit_ram_6_out_16,
       gfgg_8bit_ram_6_out_17, gfgg_8bit_ram_7_out_10, gfgg_8bit_ram_7_out_11, gfgg_8bit_ram_7_out_12,
       gfgg_8bit_ram_7_out_13, gfgg_8bit_ram_7_out_14, gfgg_8bit_ram_7_out_15, gfgg_8bit_ram_7_out_16,
       gfgg_8bit_ram_7_out_17, gfgg_8bit_ram_8_out_10, gfgg_8bit_ram_8_out_11, gfgg_8bit_ram_8_out_12,
       gfgg_8bit_ram_8_out_13, gfgg_8bit_ram_8_out_14, gfgg_8bit_ram_8_out_15, gfgg_8bit_ram_8_out_16,
       gfgg_8bit_ram_8_out_17, gfgg_enable_and_1_out_10, gfgg_enable_and_1_out_11, gfgg_enable_and_1_out_12,
       gfgg_enable_and_1_out_13, gfgg_enable_and_1_out_14, gfgg_enable_and_1_out_15,
       gfgg_enable_and_1_out_16, gfgg_enable_and_1_out_17, gfgg_enable_and_2_out_10,
       gfgg_enable_and_2_out_11, gfgg_enable_and_2_out_12, gfgg_enable_and_2_out_13,
       gfgg_enable_and_2_out_14, gfgg_enable_and_2_out_15, gfgg_enable_and_2_out_16,
       gfgg_enable_and_2_out_17, gfgg_enable_and_3_out_10, gfgg_enable_and_3_out_11,
       gfgg_enable_and_3_out_12, gfgg_enable_and_3_out_13, gfgg_enable_and_3_out_14,
       gfgg_enable_and_3_out_15, gfgg_enable_and_3_out_16, gfgg_enable_and_3_out_17,
       gfgg_enable_and_4_out_10, gfgg_enable_and_4_out_11, gfgg_enable_and_4_out_12,
       gfgg_enable_and_4_out_13, gfgg_enable_and_4_out_14, gfgg_enable_and_4_out_15,
       gfgg_enable_and_4_out_16, gfgg_enable_and_4_out_17, gfgg_enable_and_5_out_10,
       gfgg_enable_and_5_out_11, gfgg_enable_and_5_out_12, gfgg_enable_and_5_out_13,
       gfgg_enable_and_5_out_14, gfgg_enable_and_5_out_15, gfgg_enable_and_5_out_16,
       gfgg_enable_and_5_out_17, gfgg_enable_and_6_out_10, gfgg_enable_and_6_out_11,
       gfgg_enable_and_6_out_12, gfgg_enable_and_6_out_13, gfgg_enable_and_6_out_14,
       gfgg_enable_and_6_out_15, gfgg_enable_and_6_out_16, gfgg_enable_and_6_out_17,
       gfgg_enable_and_7_out_10, gfgg_enable_and_7_out_11, gfgg_enable_and_7_out_12,
       gfgg_enable_and_7_out_13, gfgg_enable_and_7_out_14, gfgg_enable_and_7_out_15,
       gfgg_enable_and_7_out_16, gfgg_enable_and_7_out_17, gfgg_enable_and_8_out_10,
       gfgg_enable_and_8_out_11, gfgg_enable_and_8_out_12, gfgg_enable_and_8_out_13,
       gfgg_enable_and_8_out_14, gfgg_enable_and_8_out_15, gfgg_enable_and_8_out_16, gfgg_enable_and_8_out_17;

  Gfgg_3Bit_Decoder gfgg_3bit_decoder_1 (
    .in_1(Write_Adress_4), .in_2(Write_Adress_2), .in_3(Write_Adress_1), .out_4(gfgg_3bit_decoder_1_out_4),
    .out_5(gfgg_3bit_decoder_1_out_5), .out_6(gfgg_3bit_decoder_1_out_6), .out_7(gfgg_3bit_decoder_1_out_7),
    .out_8(gfgg_3bit_decoder_1_out_8), .out_9(gfgg_3bit_decoder_1_out_9),
    .out_10(gfgg_3bit_decoder_1_out_10), .out_11(gfgg_3bit_decoder_1_out_11));
  Gfgg_3Bit_Decoder gfgg_3bit_decoder_2 (
    .in_1(Read_Adress_4), .in_2(Read_Adress_2), .in_3(Read_Adress_1), .out_4(gfgg_3bit_decoder_2_out_4),
    .out_5(gfgg_3bit_decoder_2_out_5), .out_6(gfgg_3bit_decoder_2_out_6), .out_7(gfgg_3bit_decoder_2_out_7),
    .out_8(gfgg_3bit_decoder_2_out_8), .out_9(gfgg_3bit_decoder_2_out_9),
    .out_10(gfgg_3bit_decoder_2_out_10), .out_11(gfgg_3bit_decoder_2_out_11));
  and and_1 (and_1_out, Write_Enable, gfgg_3bit_decoder_1_out_11);
  and and_2 (and_2_out, gfgg_3bit_decoder_1_out_4, Write_Enable);
  and and_3 (and_3_out, gfgg_3bit_decoder_1_out_5, Write_Enable);
  and and_4 (and_4_out, gfgg_3bit_decoder_1_out_6, Write_Enable);
  and and_5 (and_5_out, gfgg_3bit_decoder_1_out_7, Write_Enable);
  and and_6 (and_6_out, gfgg_3bit_decoder_1_out_8, Write_Enable);
  and and_7 (and_7_out, gfgg_3bit_decoder_1_out_9, Write_Enable);
  and and_8 (and_8_out, Write_Enable, gfgg_3bit_decoder_1_out_10);
  and and_9 (and_9_out, gfgg_3bit_decoder_2_out_4, Read_Enable);
  and and_10 (and_10_out, gfgg_3bit_decoder_2_out_5, Read_Enable);
  and and_11 (and_11_out, gfgg_3bit_decoder_2_out_6, Read_Enable);
  and and_12 (and_12_out, gfgg_3bit_decoder_2_out_7, Read_Enable);
  and and_13 (and_13_out, gfgg_3bit_decoder_2_out_8, Read_Enable);
  and and_14 (and_14_out, gfgg_3bit_decoder_2_out_9, Read_Enable);
  and and_15 (and_15_out, Read_Enable, gfgg_3bit_decoder_2_out_10);
  and and_16 (and_16_out, Read_Enable, gfgg_3bit_decoder_2_out_11);
  Gfgg_8Bit_RAM gfgg_8bit_ram_1 (
    .in_1(in_1), .in_2(in_2), .in_3(in_3), .in_4(in_4), .in_5(in_5), .in_6(in_6), .in_7(in_7), .in_8(in_8),
    .in_9(and_2_out), .out_10(gfgg_8bit_ram_1_out_10), .out_11(gfgg_8bit_ram_1_out_11),
    .out_12(gfgg_8bit_ram_1_out_12), .out_13(gfgg_8bit_ram_1_out_13), .out_14(gfgg_8bit_ram_1_out_14),
    .out_15(gfgg_8bit_ram_1_out_15), .out_16(gfgg_8bit_ram_1_out_16), .out_17(gfgg_8bit_ram_1_out_17));
  Gfgg_8Bit_RAM gfgg_8bit_ram_2 (
    .in_1(in_1), .in_2(in_2), .in_3(in_3), .in_4(in_4), .in_5(in_5), .in_6(in_6), .in_7(in_7), .in_8(in_8),
    .in_9(and_3_out), .out_10(gfgg_8bit_ram_2_out_10), .out_11(gfgg_8bit_ram_2_out_11),
    .out_12(gfgg_8bit_ram_2_out_12), .out_13(gfgg_8bit_ram_2_out_13), .out_14(gfgg_8bit_ram_2_out_14),
    .out_15(gfgg_8bit_ram_2_out_15), .out_16(gfgg_8bit_ram_2_out_16), .out_17(gfgg_8bit_ram_2_out_17));
  Gfgg_8Bit_RAM gfgg_8bit_ram_3 (
    .in_1(in_1), .in_2(in_2), .in_3(in_3), .in_4(in_4), .in_5(in_5), .in_6(in_6), .in_7(in_7), .in_8(in_8),
    .in_9(and_4_out), .out_10(gfgg_8bit_ram_3_out_10), .out_11(gfgg_8bit_ram_3_out_11),
    .out_12(gfgg_8bit_ram_3_out_12), .out_13(gfgg_8bit_ram_3_out_13), .out_14(gfgg_8bit_ram_3_out_14),
    .out_15(gfgg_8bit_ram_3_out_15), .out_16(gfgg_8bit_ram_3_out_16), .out_17(gfgg_8bit_ram_3_out_17));
  Gfgg_8Bit_RAM gfgg_8bit_ram_4 (
    .in_1(in_1), .in_2(in_2), .in_3(in_3), .in_4(in_4), .in_5(in_5), .in_6(in_6), .in_7(in_7), .in_8(in_8),
    .in_9(and_5_out), .out_10(gfgg_8bit_ram_4_out_10), .out_11(gfgg_8bit_ram_4_out_11),
    .out_12(gfgg_8bit_ram_4_out_12), .out_13(gfgg_8bit_ram_4_out_13), .out_14(gfgg_8bit_ram_4_out_14),
    .out_15(gfgg_8bit_ram_4_out_15), .out_16(gfgg_8bit_ram_4_out_16), .out_17(gfgg_8bit_ram_4_out_17));
  Gfgg_8Bit_RAM gfgg_8bit_ram_5 (
    .in_1(in_1), .in_2(in_2), .in_3(in_3), .in_4(in_4), .in_5(in_5), .in_6(in_6), .in_7(in_7), .in_8(in_8),
    .in_9(and_6_out), .out_10(gfgg_8bit_ram_5_out_10), .out_11(gfgg_8bit_ram_5_out_11),
    .out_12(gfgg_8bit_ram_5_out_12), .out_13(gfgg_8bit_ram_5_out_13), .out_14(gfgg_8bit_ram_5_out_14),
    .out_15(gfgg_8bit_ram_5_out_15), .out_16(gfgg_8bit_ram_5_out_16), .out_17(gfgg_8bit_ram_5_out_17));
  Gfgg_8Bit_RAM gfgg_8bit_ram_6 (
    .in_1(in_1), .in_2(in_2), .in_3(in_3), .in_4(in_4), .in_5(in_5), .in_6(in_6), .in_7(in_7), .in_8(in_8),
    .in_9(and_7_out), .out_10(gfgg_8bit_ram_6_out_10), .out_11(gfgg_8bit_ram_6_out_11),
    .out_12(gfgg_8bit_ram_6_out_12), .out_13(gfgg_8bit_ram_6_out_13), .out_14(gfgg_8bit_ram_6_out_14),
    .out_15(gfgg_8bit_ram_6_out_15), .out_16(gfgg_8bit_ram_6_out_16), .out_17(gfgg_8bit_ram_6_out_17));
  Gfgg_8Bit_RAM gfgg_8bit_ram_7 (
    .in_1(in_1), .in_2(in_2), .in_3(in_3), .in_4(in_4), .in_5(in_5), .in_6(in_6), .in_7(in_7), .in_8(in_8),
    .in_9(and_8_out), .out_10(gfgg_8bit_ram_7_out_10), .out_11(gfgg_8bit_ram_7_out_11),
    .out_12(gfgg_8bit_ram_7_out_12), .out_13(gfgg_8bit_ram_7_out_13), .out_14(gfgg_8bit_ram_7_out_14),
    .out_15(gfgg_8bit_ram_7_out_15), .out_16(gfgg_8bit_ram_7_out_16), .out_17(gfgg_8bit_ram_7_out_17));
  Gfgg_8Bit_RAM gfgg_8bit_ram_8 (
    .in_1(in_1), .in_2(in_2), .in_3(in_3), .in_4(in_4), .in_5(in_5), .in_6(in_6), .in_7(in_7), .in_8(in_8),
    .in_9(and_1_out), .out_10(gfgg_8bit_ram_8_out_10), .out_11(gfgg_8bit_ram_8_out_11),
    .out_12(gfgg_8bit_ram_8_out_12), .out_13(gfgg_8bit_ram_8_out_13), .out_14(gfgg_8bit_ram_8_out_14),
    .out_15(gfgg_8bit_ram_8_out_15), .out_16(gfgg_8bit_ram_8_out_16), .out_17(gfgg_8bit_ram_8_out_17));
  Gfgg_Enable_And gfgg_enable_and_1 (
    .in_1(gfgg_8bit_ram_1_out_10), .in_2(gfgg_8bit_ram_1_out_11), .in_3(gfgg_8bit_ram_1_out_12),
    .in_4(gfgg_8bit_ram_1_out_13), .in_5(gfgg_8bit_ram_1_out_14), .in_6(gfgg_8bit_ram_1_out_15),
    .in_7(gfgg_8bit_ram_1_out_16), .in_8(gfgg_8bit_ram_1_out_17), .Enable(and_9_out),
    .out_10(gfgg_enable_and_1_out_10), .out_11(gfgg_enable_and_1_out_11), .out_12(gfgg_enable_and_1_out_12),
    .out_13(gfgg_enable_and_1_out_13), .out_14(gfgg_enable_and_1_out_14), .out_15(gfgg_enable_and_1_out_15),
    .out_16(gfgg_enable_and_1_out_16), .out_17(gfgg_enable_and_1_out_17));
  Gfgg_Enable_And gfgg_enable_and_2 (
    .in_1(gfgg_8bit_ram_2_out_10), .in_2(gfgg_8bit_ram_2_out_11), .in_3(gfgg_8bit_ram_2_out_12),
    .in_4(gfgg_8bit_ram_2_out_13), .in_5(gfgg_8bit_ram_2_out_14), .in_6(gfgg_8bit_ram_2_out_15),
    .in_7(gfgg_8bit_ram_2_out_16), .in_8(gfgg_8bit_ram_2_out_17), .Enable(and_10_out),
    .out_10(gfgg_enable_and_2_out_10), .out_11(gfgg_enable_and_2_out_11), .out_12(gfgg_enable_and_2_out_12),
    .out_13(gfgg_enable_and_2_out_13), .out_14(gfgg_enable_and_2_out_14), .out_15(gfgg_enable_and_2_out_15),
    .out_16(gfgg_enable_and_2_out_16), .out_17(gfgg_enable_and_2_out_17));
  Gfgg_Enable_And gfgg_enable_and_3 (
    .in_1(gfgg_8bit_ram_3_out_10), .in_2(gfgg_8bit_ram_3_out_11), .in_3(gfgg_8bit_ram_3_out_12),
    .in_4(gfgg_8bit_ram_3_out_13), .in_5(gfgg_8bit_ram_3_out_14), .in_6(gfgg_8bit_ram_3_out_15),
    .in_7(gfgg_8bit_ram_3_out_16), .in_8(gfgg_8bit_ram_3_out_17), .Enable(and_11_out),
    .out_10(gfgg_enable_and_3_out_10), .out_11(gfgg_enable_and_3_out_11), .out_12(gfgg_enable_and_3_out_12),
    .out_13(gfgg_enable_and_3_out_13), .out_14(gfgg_enable_and_3_out_14), .out_15(gfgg_enable_and_3_out_15),
    .out_16(gfgg_enable_and_3_out_16), .out_17(gfgg_enable_and_3_out_17));
  Gfgg_Enable_And gfgg_enable_and_4 (
    .in_1(gfgg_8bit_ram_4_out_10), .in_2(gfgg_8bit_ram_4_out_11), .in_3(gfgg_8bit_ram_4_out_12),
    .in_4(gfgg_8bit_ram_4_out_13), .in_5(gfgg_8bit_ram_4_out_14), .in_6(gfgg_8bit_ram_4_out_15),
    .in_7(gfgg_8bit_ram_4_out_16), .in_8(gfgg_8bit_ram_4_out_17), .Enable(and_12_out),
    .out_10(gfgg_enable_and_4_out_10), .out_11(gfgg_enable_and_4_out_11), .out_12(gfgg_enable_and_4_out_12),
    .out_13(gfgg_enable_and_4_out_13), .out_14(gfgg_enable_and_4_out_14), .out_15(gfgg_enable_and_4_out_15),
    .out_16(gfgg_enable_and_4_out_16), .out_17(gfgg_enable_and_4_out_17));
  Gfgg_Enable_And gfgg_enable_and_5 (
    .in_1(gfgg_8bit_ram_5_out_10), .in_2(gfgg_8bit_ram_5_out_11), .in_3(gfgg_8bit_ram_5_out_12),
    .in_4(gfgg_8bit_ram_5_out_13), .in_5(gfgg_8bit_ram_5_out_14), .in_6(gfgg_8bit_ram_5_out_15),
    .in_7(gfgg_8bit_ram_5_out_16), .in_8(gfgg_8bit_ram_5_out_17), .Enable(and_13_out),
    .out_10(gfgg_enable_and_5_out_10), .out_11(gfgg_enable_and_5_out_11), .out_12(gfgg_enable_and_5_out_12),
    .out_13(gfgg_enable_and_5_out_13), .out_14(gfgg_enable_and_5_out_14), .out_15(gfgg_enable_and_5_out_15),
    .out_16(gfgg_enable_and_5_out_16), .out_17(gfgg_enable_and_5_out_17));
  Gfgg_Enable_And gfgg_enable_and_6 (
    .in_1(gfgg_8bit_ram_6_out_10), .in_2(gfgg_8bit_ram_6_out_11), .in_3(gfgg_8bit_ram_6_out_12),
    .in_4(gfgg_8bit_ram_6_out_13), .in_5(gfgg_8bit_ram_6_out_14), .in_6(gfgg_8bit_ram_6_out_15),
    .in_7(gfgg_8bit_ram_6_out_16), .in_8(gfgg_8bit_ram_6_out_17), .Enable(and_14_out),
    .out_10(gfgg_enable_and_6_out_10), .out_11(gfgg_enable_and_6_out_11), .out_12(gfgg_enable_and_6_out_12),
    .out_13(gfgg_enable_and_6_out_13), .out_14(gfgg_enable_and_6_out_14), .out_15(gfgg_enable_and_6_out_15),
    .out_16(gfgg_enable_and_6_out_16), .out_17(gfgg_enable_and_6_out_17));
  Gfgg_Enable_And gfgg_enable_and_7 (
    .in_1(gfgg_8bit_ram_7_out_10), .in_2(gfgg_8bit_ram_7_out_11), .in_3(gfgg_8bit_ram_7_out_12),
    .in_4(gfgg_8bit_ram_7_out_13), .in_5(gfgg_8bit_ram_7_out_14), .in_6(gfgg_8bit_ram_7_out_15),
    .in_7(gfgg_8bit_ram_7_out_16), .in_8(gfgg_8bit_ram_7_out_17), .Enable(and_15_out),
    .out_10(gfgg_enable_and_7_out_10), .out_11(gfgg_enable_and_7_out_11), .out_12(gfgg_enable_and_7_out_12),
    .out_13(gfgg_enable_and_7_out_13), .out_14(gfgg_enable_and_7_out_14), .out_15(gfgg_enable_and_7_out_15),
    .out_16(gfgg_enable_and_7_out_16), .out_17(gfgg_enable_and_7_out_17));
  Gfgg_Enable_And gfgg_enable_and_8 (
    .in_1(gfgg_8bit_ram_8_out_10), .in_2(gfgg_8bit_ram_8_out_11), .in_3(gfgg_8bit_ram_8_out_12),
    .in_4(gfgg_8bit_ram_8_out_13), .in_5(gfgg_8bit_ram_8_out_14), .in_6(gfgg_8bit_ram_8_out_15),
    .in_7(gfgg_8bit_ram_8_out_16), .in_8(gfgg_8bit_ram_8_out_17), .Enable(and_16_out),
    .out_10(gfgg_enable_and_8_out_10), .out_11(gfgg_enable_and_8_out_11), .out_12(gfgg_enable_and_8_out_12),
    .out_13(gfgg_enable_and_8_out_13), .out_14(gfgg_enable_and_8_out_14), .out_15(gfgg_enable_and_8_out_15),
    .out_16(gfgg_enable_and_8_out_16), .out_17(gfgg_enable_and_8_out_17));
  Gfgg_8_OR gfgg_8_or_1 (
    .in_1(gfgg_enable_and_1_out_10), .in_2(gfgg_enable_and_2_out_10), .in_3(gfgg_enable_and_3_out_10),
    .in_4(gfgg_enable_and_4_out_10), .in_5(gfgg_enable_and_5_out_10), .in_6(gfgg_enable_and_6_out_10),
    .in_7(gfgg_enable_and_7_out_10), .in_8(gfgg_enable_and_8_out_10), .out_9(out_17));
  Gfgg_8_OR gfgg_8_or_2 (
    .in_1(gfgg_enable_and_1_out_11), .in_2(gfgg_enable_and_2_out_11), .in_3(gfgg_enable_and_3_out_11),
    .in_4(gfgg_enable_and_4_out_11), .in_5(gfgg_enable_and_5_out_11), .in_6(gfgg_enable_and_6_out_11),
    .in_7(gfgg_enable_and_7_out_11), .in_8(gfgg_enable_and_8_out_11), .out_9(out_18));
  Gfgg_8_OR gfgg_8_or_3 (
    .in_1(gfgg_enable_and_1_out_12), .in_2(gfgg_enable_and_2_out_12), .in_3(gfgg_enable_and_3_out_12),
    .in_4(gfgg_enable_and_4_out_12), .in_5(gfgg_enable_and_5_out_12), .in_6(gfgg_enable_and_6_out_12),
    .in_7(gfgg_enable_and_7_out_12), .in_8(gfgg_enable_and_8_out_12), .out_9(out_19));
  Gfgg_8_OR gfgg_8_or_4 (
    .in_1(gfgg_enable_and_1_out_13), .in_2(gfgg_enable_and_2_out_13), .in_3(gfgg_enable_and_3_out_13),
    .in_4(gfgg_enable_and_4_out_13), .in_5(gfgg_enable_and_5_out_13), .in_6(gfgg_enable_and_6_out_13),
    .in_7(gfgg_enable_and_7_out_13), .in_8(gfgg_enable_and_8_out_13), .out_9(out_20));
  Gfgg_8_OR gfgg_8_or_5 (
    .in_1(gfgg_enable_and_1_out_14), .in_2(gfgg_enable_and_2_out_14), .in_3(gfgg_enable_and_3_out_14),
    .in_4(gfgg_enable_and_4_out_14), .in_5(gfgg_enable_and_5_out_14), .in_6(gfgg_enable_and_6_out_14),
    .in_7(gfgg_enable_and_7_out_14), .in_8(gfgg_enable_and_8_out_14), .out_9(out_21));
  Gfgg_8_OR gfgg_8_or_6 (
    .in_1(gfgg_enable_and_1_out_15), .in_2(gfgg_enable_and_2_out_15), .in_3(gfgg_enable_and_3_out_15),
    .in_4(gfgg_enable_and_4_out_15), .in_5(gfgg_enable_and_5_out_15), .in_6(gfgg_enable_and_6_out_15),
    .in_7(gfgg_enable_and_7_out_15), .in_8(gfgg_enable_and_8_out_15), .out_9(out_22));
  Gfgg_8_OR gfgg_8_or_7 (
    .in_1(gfgg_enable_and_1_out_16), .in_2(gfgg_enable_and_2_out_16), .in_3(gfgg_enable_and_3_out_16),
    .in_4(gfgg_enable_and_4_out_16), .in_5(gfgg_enable_and_5_out_16), .in_6(gfgg_enable_and_6_out_16),
    .in_7(gfgg_enable_and_7_out_16), .in_8(gfgg_enable_and_8_out_16), .out_9(out_23));
  Gfgg_8_OR gfgg_8_or_8 (
    .in_1(gfgg_enable_and_1_out_17), .in_2(gfgg_enable_and_2_out_17), .in_3(gfgg_enable_and_3_out_17),
    .in_4(gfgg_enable_and_4_out_17), .in_5(gfgg_enable_and_5_out_17), .in_6(gfgg_enable_and_6_out_17),
    .in_7(gfgg_enable_and_7_out_17), .in_8(gfgg_enable_and_8_out_17), .out_9(out_24));
endmodule

module Gfgg_8_OR (
  input  in_1,
  input  in_2,
  input  in_3,
  input  in_4,
  input  in_5,
  input  in_6,
  input  in_7,
  input  in_8,
  output out_9
);

  wire gfgg_4_or_1_out_5, gfgg_4_or_2_out_5;

  Gfgg_4_OR gfgg_4_or_1 (.in_1(in_1), .in_2(in_2), .in_3(in_3), .in_4(in_4), .out_5(gfgg_4_or_1_out_5));
  Gfgg_4_OR gfgg_4_or_2 (.in_1(in_5), .in_2(in_6), .in_3(in_7), .in_4(in_8), .out_5(gfgg_4_or_2_out_5));
  or or_1 (out_9, gfgg_4_or_1_out_5, gfgg_4_or_2_out_5);
endmodule

module Gfgg_PC_7 (
  input  in_1,
  input  in_2,
  input  in_3,
  input  in_4,
  input  in_5,
  input  in_6,
  input  in_7,
  input  in_8,
  input  in_9,
  input  in_10,
  input  in_11,
  input  in_12,
  input  in_13,
  input  in_14,
  input  in_15,
  input  in_16,
  input  in_17,
  input  in_18,
  input  in_19,
  input  in_20,
  input  in_21,
  input  in_22,
  input  in_23,
  input  in_24,
  output out_25,
  output out_26,
  output out_27,
  output out_28
);

  wire and_5_out, gfgg_3_1_mux_1_out_6, gfgg_3_1_mux_1_out_7, gfgg_3_1_mux_1_out_8, gfgg_3_1_mux_2_out_6,
       gfgg_3_1_mux_2_out_7, gfgg_3_1_mux_2_out_8, gfgg_4_1_mux_1_out_7, gfgg_4_1_mux_1_out_8,
       gfgg_4_1_mux_1_out_9, gfgg_4_1_mux_1_out_10, gfgg_8byte_rom_1_out_17, gfgg_8byte_rom_1_out_18,
       gfgg_8byte_rom_1_out_19, gfgg_8byte_rom_1_out_20, gfgg_8byte_rom_1_out_21, gfgg_8byte_rom_1_out_22;

  Gfgg_8Byte_RAM gfgg_8byte_ram_1 (
    .Write_Adress_4(in_17), .Write_Adress_2(in_18), .Write_Adress_1(in_19), .Write_Enable(in_20),
    .Read_Enable(in_21), .Read_Adress_4(in_22), .Read_Adress_2(in_23), .Read_Adress_1(in_24));  // open: in_1, in_2, in_3, in_4, in_5, in_6, in_7, in_8, out_17, out_18, out_19, out_20, out_21, out_22, out_23, out_24
  Gfgg_Video_1 gfgg_video_1_1 ();  // open: in_1, in_2, in_3, in_4, in_5, in_6, in_7, in_8, in_9, in_10, in_11, in_12, in_13
  Gfgg_8Byte_ROM gfgg_8byte_rom_1 (
    .in_1(in_1), .in_2(in_2), .in_3(in_3), .in_4(in_4), .in_5(in_5), .in_6(in_6), .in_7(in_7), .in_8(in_8),
    .Write_Adress_4(in_9), .Write_Adress_2(in_10), .Write_Adress_1(in_11), .Write_Enable(in_12),
    .Read_Enable(in_13), .Read_Adress_4(in_14), .Read_Adress_2(in_15), .Read_Adress_1(in_16),
    .out_17(gfgg_8byte_rom_1_out_17), .out_18(gfgg_8byte_rom_1_out_18), .out_19(gfgg_8byte_rom_1_out_19),
    .out_20(gfgg_8byte_rom_1_out_20), .out_21(gfgg_8byte_rom_1_out_21), .out_22(gfgg_8byte_rom_1_out_22));  // open: out_23, out_24
  Gfgg_4_1_MUX gfgg_4_1_mux_1 (
    .Select_A(gfgg_8byte_rom_1_out_21), .Select_B(gfgg_8byte_rom_1_out_22), .out_7(gfgg_4_1_mux_1_out_7),
    .out_8(gfgg_4_1_mux_1_out_8), .out_9(gfgg_4_1_mux_1_out_9), .out_10(gfgg_4_1_mux_1_out_10));  // open: in_1, in_2, in_3, in_4
  Gfgg_3_1_MUX gfgg_3_1_mux_1 (
    .in_1(1'b1), .in_2(1'b1), .in_3(1'b1), .Select_A(gfgg_8byte_rom_1_out_17),
    .Select_B(gfgg_8byte_rom_1_out_18), .out_6(gfgg_3_1_mux_1_out_6), .out_7(gfgg_3_1_mux_1_out_7),
    .out_8(gfgg_3_1_mux_1_out_8));
  Gfgg_3_1_MUX gfgg_3_1_mux_2 (
    .in_1(1'b1), .in_2(1'b1), .in_3(1'b1), .Select_A(gfgg_8byte_rom_1_out_19),
    .Select_B(gfgg_8byte_rom_1_out_20), .out_6(gfgg_3_1_mux_2_out_6), .out_7(gfgg_3_1_mux_2_out_7),
    .out_8(gfgg_3_1_mux_2_out_8));
  Gfgg_8Bit_Register_2 gfgg_8bit_register_2_1 (.Load(gfgg_4_1_mux_1_out_7));  // open: in_1, in_2, in_3, in_4, in_5, in_6, in_7, in_8, out_10, out_11, out_12, out_13, out_14, out_15, out_16, out_17
  Gfgg_8Bit_Register_2 gfgg_8bit_register_2_2 (.Load(gfgg_4_1_mux_1_out_8));  // open: in_1, in_2, in_3, in_4, in_5, in_6, in_7, in_8, out_10, out_11, out_12, out_13, out_14, out_15, out_16, out_17
  Gfgg_8Bit_Register_2 gfgg_8bit_register_2_3 (.Load(gfgg_4_1_mux_1_out_9));  // open: in_1, in_2, in_3, in_4, in_5, in_6, in_7, in_8, out_10, out_11, out_12, out_13, out_14, out_15, out_16, out_17
  Gfgg_8Bit_Register_2 gfgg_8bit_register_2_4 (.Load(gfgg_4_1_mux_1_out_10));  // open: in_1, in_2, in_3, in_4, in_5, in_6, in_7, in_8, out_10, out_11, out_12, out_13, out_14, out_15, out_16, out_17
  and and_1 (out_25, gfgg_3_1_mux_1_out_8, gfgg_3_1_mux_2_out_6);
  and and_2 (out_26, gfgg_3_1_mux_1_out_8, gfgg_3_1_mux_2_out_8);
  and and_3 (out_27, gfgg_3_1_mux_2_out_8, gfgg_3_1_mux_1_out_7);
  and and_4 (out_28, gfgg_3_1_mux_2_out_7, gfgg_3_1_mux_1_out_7);
  and and_5 (and_5_out, gfgg_3_1_mux_1_out_6, gfgg_3_1_mux_2_out_8);
  Gfgg_8Bit_ALU gfgg_8bit_alu_1 (.in_1(and_5_out));  // open: in_2, in_3, in_4, in_5, in_6, in_7, in_8, in_9, in_10, in_11, in_12, in_13, in_14, in_15, in_16, in_17, in_18, out_19, out_20, out_21, out_22, out_23, out_24, out_25, out_26, Negative, Carry, Zero

  // Notes on the sheet:
  //   HALT
  //   NOP
  //   LOAD
  //   STORE
  //   ADD
endmodule
module Gfgg_8Byte_ROM (
  input  in_1,
  input  in_2,
  input  in_3,
  input  in_4,
  input  in_5,
  input  in_6,
  input  in_7,
  input  in_8,
  input  Write_Adress_4,
  input  Write_Adress_2,
  input  Write_Adress_1,
  input  Write_Enable,
  input  Read_Enable,
  input  Read_Adress_4,
  input  Read_Adress_2,
  input  Read_Adress_1,
  output out_17,
  output out_18,
  output out_19,
  output out_20,
  output out_21,
  output out_22,
  output out_23,
  output out_24
);

  wire and_1_out, and_2_out, and_3_out, and_4_out, and_5_out, and_6_out, and_7_out, and_8_out, and_9_out,
       and_10_out, and_11_out, and_12_out, and_13_out, and_14_out, and_15_out, and_16_out,
       gfgg_3bit_decoder_1_out_4, gfgg_3bit_decoder_1_out_5, gfgg_3bit_decoder_1_out_6,
       gfgg_3bit_decoder_1_out_7, gfgg_3bit_decoder_1_out_8, gfgg_3bit_decoder_1_out_9,
       gfgg_3bit_decoder_1_out_10, gfgg_3bit_decoder_1_out_11, gfgg_3bit_decoder_2_out_4,
       gfgg_3bit_decoder_2_out_5, gfgg_3bit_decoder_2_out_6, gfgg_3bit_decoder_2_out_7,
       gfgg_3bit_decoder_2_out_8, gfgg_3bit_decoder_2_out_9, gfgg_3bit_decoder_2_out_10,
       gfgg_3bit_decoder_2_out_11, gfgg_8bit_ram_1_out_10, gfgg_8bit_ram_1_out_11, gfgg_8bit_ram_1_out_12,
       gfgg_8bit_ram_1_out_13, gfgg_8bit_ram_1_out_14, gfgg_8bit_ram_1_out_15, gfgg_8bit_ram_1_out_16,
       gfgg_8bit_ram_1_out_17, gfgg_8bit_ram_2_out_10, gfgg_8bit_ram_2_out_11, gfgg_8bit_ram_2_out_12,
       gfgg_8bit_ram_2_out_13, gfgg_8bit_ram_2_out_14, gfgg_8bit_ram_2_out_15, gfgg_8bit_ram_2_out_16,
       gfgg_8bit_ram_2_out_17, gfgg_8bit_ram_3_out_10, gfgg_8bit_ram_3_out_11, gfgg_8bit_ram_3_out_12,
       gfgg_8bit_ram_3_out_13, gfgg_8bit_ram_3_out_14, gfgg_8bit_ram_3_out_15, gfgg_8bit_ram_3_out_16,
       gfgg_8bit_ram_3_out_17, gfgg_8bit_ram_4_out_10, gfgg_8bit_ram_4_out_11, gfgg_8bit_ram_4_out_12,
       gfgg_8bit_ram_4_out_13, gfgg_8bit_ram_4_out_14, gfgg_8bit_ram_4_out_15, gfgg_8bit_ram_4_out_16,
       gfgg_8bit_ram_4_out_17, gfgg_8bit_ram_5_out_10, gfgg_8bit_ram_5_out_11, gfgg_8bit_ram_5_out_12,
       gfgg_8bit_ram_5_out_13, gfgg_8bit_ram_5_out_14, gfgg_8bit_ram_5_out_15, gfgg_8bit_ram_5_out_16,
       gfgg_8bit_ram_5_out_17, gfgg_8bit_ram_6_out_10, gfgg_8bit_ram_6_out_11, gfgg_8bit_ram_6_out_12,
       gfgg_8bit_ram_6_out_13, gfgg_8bit_ram_6_out_14, gfgg_8bit_ram_6_out_15, gfgg_8bit_ram_6_out_16,
       gfgg_8bit_ram_6_out_17, gfgg_8bit_ram_7_out_10, gfgg_8bit_ram_7_out_11, gfgg_8bit_ram_7_out_12,
       gfgg_8bit_ram_7_out_13, gfgg_8bit_ram_7_out_14, gfgg_8bit_ram_7_out_15, gfgg_8bit_ram_7_out_16,
       gfgg_8bit_ram_7_out_17, gfgg_8bit_ram_8_out_10, gfgg_8bit_ram_8_out_11, gfgg_8bit_ram_8_out_12,
       gfgg_8bit_ram_8_out_13, gfgg_8bit_ram_8_out_14, gfgg_8bit_ram_8_out_15, gfgg_8bit_ram_8_out_16,
       gfgg_8bit_ram_8_out_17, gfgg_enable_and_1_out_10, gfgg_enable_and_1_out_11, gfgg_enable_and_1_out_12,
       gfgg_enable_and_1_out_13, gfgg_enable_and_1_out_14, gfgg_enable_and_1_out_15,
       gfgg_enable_and_1_out_16, gfgg_enable_and_1_out_17, gfgg_enable_and_2_out_10,
       gfgg_enable_and_2_out_11, gfgg_enable_and_2_out_12, gfgg_enable_and_2_out_13,
       gfgg_enable_and_2_out_14, gfgg_enable_and_2_out_15, gfgg_enable_and_2_out_16,
       gfgg_enable_and_2_out_17, gfgg_enable_and_3_out_10, gfgg_enable_and_3_out_11,
       gfgg_enable_and_3_out_12, gfgg_enable_and_3_out_13, gfgg_enable_and_3_out_14,
       gfgg_enable_and_3_out_15, gfgg_enable_and_3_out_16, gfgg_enable_and_3_out_17,
       gfgg_enable_and_4_out_10, gfgg_enable_and_4_out_11, gfgg_enable_and_4_out_12,
       gfgg_enable_and_4_out_13, gfgg_enable_and_4_out_14, gfgg_enable_and_4_out_15,
       gfgg_enable_and_4_out_16, gfgg_enable_and_4_out_17, gfgg_enable_and_5_out_10,
       gfgg_enable_and_5_out_11, gfgg_enable_and_5_out_12, gfgg_enable_and_5_out_13,
       gfgg_enable_and_5_out_14, gfgg_enable_and_5_out_15, gfgg_enable_and_5_out_16,
       gfgg_enable_and_5_out_17, gfgg_enable_and_6_out_10, gfgg_enable_and_6_out_11,
       gfgg_enable_and_6_out_12, gfgg_enable_and_6_out_13, gfgg_enable_and_6_out_14,
       gfgg_enable_and_6_out_15, gfgg_enable_and_6_out_16, gfgg_enable_and_6_out_17,
       gfgg_enable_and_7_out_10, gfgg_enable_and_7_out_11, gfgg_enable_and_7_out_12,
       gfgg_enable_and_7_out_13, gfgg_enable_and_7_out_14, gfgg_enable_and_7_out_15,
       gfgg_enable_and_7_out_16, gfgg_enable_and_7_out_17, gfgg_enable_and_8_out_10,
       gfgg_enable_and_8_out_11, gfgg_enable_and_8_out_12, gfgg_enable_and_8_out_13,
       gfgg_enable_and_8_out_14, gfgg_enable_and_8_out_15, gfgg_enable_and_8_out_16, gfgg_enable_and_8_out_17;

  Gfgg_3Bit_Decoder gfgg_3bit_decoder_1 (
    .in_1(Write_Adress_4), .in_2(Write_Adress_2), .in_3(Write_Adress_1), .out_4(gfgg_3bit_decoder_1_out_4),
    .out_5(gfgg_3bit_decoder_1_out_5), .out_6(gfgg_3bit_decoder_1_out_6), .out_7(gfgg_3bit_decoder_1_out_7),
    .out_8(gfgg_3bit_decoder_1_out_8), .out_9(gfgg_3bit_decoder_1_out_9),
    .out_10(gfgg_3bit_decoder_1_out_10), .out_11(gfgg_3bit_decoder_1_out_11));
  Gfgg_3Bit_Decoder gfgg_3bit_decoder_2 (
    .in_1(Read_Adress_4), .in_2(Read_Adress_2), .in_3(Read_Adress_1), .out_4(gfgg_3bit_decoder_2_out_4),
    .out_5(gfgg_3bit_decoder_2_out_5), .out_6(gfgg_3bit_decoder_2_out_6), .out_7(gfgg_3bit_decoder_2_out_7),
    .out_8(gfgg_3bit_decoder_2_out_8), .out_9(gfgg_3bit_decoder_2_out_9),
    .out_10(gfgg_3bit_decoder_2_out_10), .out_11(gfgg_3bit_decoder_2_out_11));
  and and_1 (and_1_out, Write_Enable, gfgg_3bit_decoder_1_out_11);
  and and_2 (and_2_out, gfgg_3bit_decoder_1_out_4, Write_Enable);
  and and_3 (and_3_out, gfgg_3bit_decoder_1_out_5, Write_Enable);
  and and_4 (and_4_out, gfgg_3bit_decoder_1_out_6, Write_Enable);
  and and_5 (and_5_out, gfgg_3bit_decoder_1_out_7, Write_Enable);
  and and_6 (and_6_out, gfgg_3bit_decoder_1_out_8, Write_Enable);
  and and_7 (and_7_out, gfgg_3bit_decoder_1_out_9, Write_Enable);
  and and_8 (and_8_out, Write_Enable, gfgg_3bit_decoder_1_out_10);
  and and_9 (and_9_out, gfgg_3bit_decoder_2_out_4, Read_Enable);
  and and_10 (and_10_out, gfgg_3bit_decoder_2_out_5, Read_Enable);
  and and_11 (and_11_out, gfgg_3bit_decoder_2_out_6, Read_Enable);
  and and_12 (and_12_out, gfgg_3bit_decoder_2_out_7, Read_Enable);
  and and_13 (and_13_out, gfgg_3bit_decoder_2_out_8, Read_Enable);
  and and_14 (and_14_out, gfgg_3bit_decoder_2_out_9, Read_Enable);
  and and_15 (and_15_out, Read_Enable, gfgg_3bit_decoder_2_out_10);
  and and_16 (and_16_out, Read_Enable, gfgg_3bit_decoder_2_out_11);
  Gfgg_8Bit_RAM gfgg_8bit_ram_1 (
    .in_1(in_1), .in_2(in_2), .in_3(in_3), .in_4(in_4), .in_5(in_5), .in_6(in_6), .in_7(in_7), .in_8(in_8),
    .in_9(and_2_out), .out_10(gfgg_8bit_ram_1_out_10), .out_11(gfgg_8bit_ram_1_out_11),
    .out_12(gfgg_8bit_ram_1_out_12), .out_13(gfgg_8bit_ram_1_out_13), .out_14(gfgg_8bit_ram_1_out_14),
    .out_15(gfgg_8bit_ram_1_out_15), .out_16(gfgg_8bit_ram_1_out_16), .out_17(gfgg_8bit_ram_1_out_17));
  Gfgg_8Bit_RAM gfgg_8bit_ram_2 (
    .in_1(in_1), .in_2(in_2), .in_3(in_3), .in_4(in_4), .in_5(in_5), .in_6(in_6), .in_7(in_7), .in_8(in_8),
    .in_9(and_3_out), .out_10(gfgg_8bit_ram_2_out_10), .out_11(gfgg_8bit_ram_2_out_11),
    .out_12(gfgg_8bit_ram_2_out_12), .out_13(gfgg_8bit_ram_2_out_13), .out_14(gfgg_8bit_ram_2_out_14),
    .out_15(gfgg_8bit_ram_2_out_15), .out_16(gfgg_8bit_ram_2_out_16), .out_17(gfgg_8bit_ram_2_out_17));
  Gfgg_8Bit_RAM gfgg_8bit_ram_3 (
    .in_1(in_1), .in_2(in_2), .in_3(in_3), .in_4(in_4), .in_5(in_5), .in_6(in_6), .in_7(in_7), .in_8(in_8),
    .in_9(and_4_out), .out_10(gfgg_8bit_ram_3_out_10), .out_11(gfgg_8bit_ram_3_out_11),
    .out_12(gfgg_8bit_ram_3_out_12), .out_13(gfgg_8bit_ram_3_out_13), .out_14(gfgg_8bit_ram_3_out_14),
    .out_15(gfgg_8bit_ram_3_out_15), .out_16(gfgg_8bit_ram_3_out_16), .out_17(gfgg_8bit_ram_3_out_17));
  Gfgg_8Bit_RAM gfgg_8bit_ram_4 (
    .in_1(in_1), .in_2(in_2), .in_3(in_3), .in_4(in_4), .in_5(in_5), .in_6(in_6), .in_7(in_7), .in_8(in_8),
    .in_9(and_5_out), .out_10(gfgg_8bit_ram_4_out_10), .out_11(gfgg_8bit_ram_4_out_11),
    .out_12(gfgg_8bit_ram_4_out_12), .out_13(gfgg_8bit_ram_4_out_13), .out_14(gfgg_8bit_ram_4_out_14),
    .out_15(gfgg_8bit_ram_4_out_15), .out_16(gfgg_8bit_ram_4_out_16), .out_17(gfgg_8bit_ram_4_out_17));
  Gfgg_8Bit_RAM gfgg_8bit_ram_5 (
    .in_1(in_1), .in_2(in_2), .in_3(in_3), .in_4(in_4), .in_5(in_5), .in_6(in_6), .in_7(in_7), .in_8(in_8),
    .in_9(and_6_out), .out_10(gfgg_8bit_ram_5_out_10), .out_11(gfgg_8bit_ram_5_out_11),
    .out_12(gfgg_8bit_ram_5_out_12), .out_13(gfgg_8bit_ram_5_out_13), .out_14(gfgg_8bit_ram_5_out_14),
    .out_15(gfgg_8bit_ram_5_out_15), .out_16(gfgg_8bit_ram_5_out_16), .out_17(gfgg_8bit_ram_5_out_17));
  Gfgg_8Bit_RAM gfgg_8bit_ram_6 (
    .in_1(in_1), .in_2(in_2), .in_3(in_3), .in_4(in_4), .in_5(in_5), .in_6(in_6), .in_7(in_7), .in_8(in_8),
    .in_9(and_7_out), .out_10(gfgg_8bit_ram_6_out_10), .out_11(gfgg_8bit_ram_6_out_11),
    .out_12(gfgg_8bit_ram_6_out_12), .out_13(gfgg_8bit_ram_6_out_13), .out_14(gfgg_8bit_ram_6_out_14),
    .out_15(gfgg_8bit_ram_6_out_15), .out_16(gfgg_8bit_ram_6_out_16), .out_17(gfgg_8bit_ram_6_out_17));
  Gfgg_8Bit_RAM gfgg_8bit_ram_7 (
    .in_1(in_1), .in_2(in_2), .in_3(in_3), .in_4(in_4), .in_5(in_5), .in_6(in_6), .in_7(in_7), .in_8(in_8),
    .in_9(and_8_out), .out_10(gfgg_8bit_ram_7_out_10), .out_11(gfgg_8bit_ram_7_out_11),
    .out_12(gfgg_8bit_ram_7_out_12), .out_13(gfgg_8bit_ram_7_out_13), .out_14(gfgg_8bit_ram_7_out_14),
    .out_15(gfgg_8bit_ram_7_out_15), .out_16(gfgg_8bit_ram_7_out_16), .out_17(gfgg_8bit_ram_7_out_17));
  Gfgg_8Bit_RAM gfgg_8bit_ram_8 (
    .in_1(in_1), .in_2(in_2), .in_3(in_3), .in_4(in_4), .in_5(in_5), .in_6(in_6), .in_7(in_7), .in_8(in_8),
    .in_9(and_1_out), .out_10(gfgg_8bit_ram_8_out_10), .out_11(gfgg_8bit_ram_8_out_11),
    .out_12(gfgg_8bit_ram_8_out_12), .out_13(gfgg_8bit_ram_8_out_13), .out_14(gfgg_8bit_ram_8_out_14),
    .out_15(gfgg_8bit_ram_8_out_15), .out_16(gfgg_8bit_ram_8_out_16), .out_17(gfgg_8bit_ram_8_out_17));
  Gfgg_Enable_And gfgg_enable_and_1 (
    .in_1(gfgg_8bit_ram_1_out_10), .in_2(gfgg_8bit_ram_1_out_11), .in_3(gfgg_8bit_ram_1_out_12),
    .in_4(gfgg_8bit_ram_1_out_13), .in_5(gfgg_8bit_ram_1_out_14), .in_6(gfgg_8bit_ram_1_out_15),
    .in_7(gfgg_8bit_ram_1_out_16), .in_8(gfgg_8bit_ram_1_out_17), .Enable(and_9_out),
    .out_10(gfgg_enable_and_1_out_10), .out_11(gfgg_enable_and_1_out_11), .out_12(gfgg_enable_and_1_out_12),
    .out_13(gfgg_enable_and_1_out_13), .out_14(gfgg_enable_and_1_out_14), .out_15(gfgg_enable_and_1_out_15),
    .out_16(gfgg_enable_and_1_out_16), .out_17(gfgg_enable_and_1_out_17));
  Gfgg_Enable_And gfgg_enable_and_2 (
    .in_1(gfgg_8bit_ram_2_out_10), .in_2(gfgg_8bit_ram_2_out_11), .in_3(gfgg_8bit_ram_2_out_12),
    .in_4(gfgg_8bit_ram_2_out_13), .in_5(gfgg_8bit_ram_2_out_14), .in_6(gfgg_8bit_ram_2_out_15),
    .in_7(gfgg_8bit_ram_2_out_16), .in_8(gfgg_8bit_ram_2_out_17), .Enable(and_10_out),
    .out_10(gfgg_enable_and_2_out_10), .out_11(gfgg_enable_and_2_out_11), .out_12(gfgg_enable_and_2_out_12),
    .out_13(gfgg_enable_and_2_out_13), .out_14(gfgg_enable_and_2_out_14), .out_15(gfgg_enable_and_2_out_15),
    .out_16(gfgg_enable_and_2_out_16), .out_17(gfgg_enable_and_2_out_17));
  Gfgg_Enable_And gfgg_enable_and_3 (
    .in_1(gfgg_8bit_ram_3_out_10), .in_2(gfgg_8bit_ram_3_out_11), .in_3(gfgg_8bit_ram_3_out_12),
    .in_4(gfgg_8bit_ram_3_out_13), .in_5(gfgg_8bit_ram_3_out_14), .in_6(gfgg_8bit_ram_3_out_15),
    .in_7(gfgg_8bit_ram_3_out_16), .in_8(gfgg_8bit_ram_3_out_17), .Enable(and_11_out),
    .out_10(gfgg_enable_and_3_out_10), .out_11(gfgg_enable_and_3_out_11), .out_12(gfgg_enable_and_3_out_12),
    .out_13(gfgg_enable_and_3_out_13), .out_14(gfgg_enable_and_3_out_14), .out_15(gfgg_enable_and_3_out_15),
    .out_16(gfgg_enable_and_3_out_16), .out_17(gfgg_enable_and_3_out_17));
  Gfgg_Enable_And gfgg_enable_and_4 (
    .in_1(gfgg_8bit_ram_4_out_10), .in_2(gfgg_8bit_ram_4_out_11), .in_3(gfgg_8bit_ram_4_out_12),
    .in_4(gfgg_8bit_ram_4_out_13), .in_5(gfgg_8bit_ram_4_out_14), .in_6(gfgg_8bit_ram_4_out_15),
    .in_7(gfgg_8bit_ram_4_out_16), .in_8(gfgg_8bit_ram_4_out_17), .Enable(and_12_out),
    .out_10(gfgg_enable_and_4_out_10), .out_11(gfgg_enable_and_4_out_11), .out_12(gfgg_enable_and_4_out_12),
    .out_13(gfgg_enable_and_4_out_13), .out_14(gfgg_enable_and_4_out_14), .out_15(gfgg_enable_and_4_out_15),
    .out_16(gfgg_enable_and_4_out_16), .out_17(gfgg_enable_and_4_out_17));
  Gfgg_Enable_And gfgg_enable_and_5 (
    .in_1(gfgg_8bit_ram_5_out_10), .in_2(gfgg_8bit_ram_5_out_11), .in_3(gfgg_8bit_ram_5_out_12),
    .in_4(gfgg_8bit_ram_5_out_13), .in_5(gfgg_8bit_ram_5_out_14), .in_6(gfgg_8bit_ram_5_out_15),
    .in_7(gfgg_8bit_ram_5_out_16), .in_8(gfgg_8bit_ram_5_out_17), .Enable(and_13_out),
    .out_10(gfgg_enable_and_5_out_10), .out_11(gfgg_enable_and_5_out_11), .out_12(gfgg_enable_and_5_out_12),
    .out_13(gfgg_enable_and_5_out_13), .out_14(gfgg_enable_and_5_out_14), .out_15(gfgg_enable_and_5_out_15),
    .out_16(gfgg_enable_and_5_out_16), .out_17(gfgg_enable_and_5_out_17));
  Gfgg_Enable_And gfgg_enable_and_6 (
    .in_1(gfgg_8bit_ram_6_out_10), .in_2(gfgg_8bit_ram_6_out_11), .in_3(gfgg_8bit_ram_6_out_12),
    .in_4(gfgg_8bit_ram_6_out_13), .in_5(gfgg_8bit_ram_6_out_14), .in_6(gfgg_8bit_ram_6_out_15),
    .in_7(gfgg_8bit_ram_6_out_16), .in_8(gfgg_8bit_ram_6_out_17), .Enable(and_14_out),
    .out_10(gfgg_enable_and_6_out_10), .out_11(gfgg_enable_and_6_out_11), .out_12(gfgg_enable_and_6_out_12),
    .out_13(gfgg_enable_and_6_out_13), .out_14(gfgg_enable_and_6_out_14), .out_15(gfgg_enable_and_6_out_15),
    .out_16(gfgg_enable_and_6_out_16), .out_17(gfgg_enable_and_6_out_17));
  Gfgg_Enable_And gfgg_enable_and_7 (
    .in_1(gfgg_8bit_ram_7_out_10), .in_2(gfgg_8bit_ram_7_out_11), .in_3(gfgg_8bit_ram_7_out_12),
    .in_4(gfgg_8bit_ram_7_out_13), .in_5(gfgg_8bit_ram_7_out_14), .in_6(gfgg_8bit_ram_7_out_15),
    .in_7(gfgg_8bit_ram_7_out_16), .in_8(gfgg_8bit_ram_7_out_17), .Enable(and_15_out),
    .out_10(gfgg_enable_and_7_out_10), .out_11(gfgg_enable_and_7_out_11), .out_12(gfgg_enable_and_7_out_12),
    .out_13(gfgg_enable_and_7_out_13), .out_14(gfgg_enable_and_7_out_14), .out_15(gfgg_enable_and_7_out_15),
    .out_16(gfgg_enable_and_7_out_16), .out_17(gfgg_enable_and_7_out_17));
  Gfgg_Enable_And gfgg_enable_and_8 (
    .in_1(gfgg_8bit_ram_8_out_10), .in_2(gfgg_8bit_ram_8_out_11), .in_3(gfgg_8bit_ram_8_out_12),
    .in_4(gfgg_8bit_ram_8_out_13), .in_5(gfgg_8bit_ram_8_out_14), .in_6(gfgg_8bit_ram_8_out_15),
    .in_7(gfgg_8bit_ram_8_out_16), .in_8(gfgg_8bit_ram_8_out_17), .Enable(and_16_out),
    .out_10(gfgg_enable_and_8_out_10), .out_11(gfgg_enable_and_8_out_11), .out_12(gfgg_enable_and_8_out_12),
    .out_13(gfgg_enable_and_8_out_13), .out_14(gfgg_enable_and_8_out_14), .out_15(gfgg_enable_and_8_out_15),
    .out_16(gfgg_enable_and_8_out_16), .out_17(gfgg_enable_and_8_out_17));
  Gfgg_8_OR gfgg_8_or_1 (
    .in_1(gfgg_enable_and_1_out_10), .in_2(gfgg_enable_and_2_out_10), .in_3(gfgg_enable_and_3_out_10),
    .in_4(gfgg_enable_and_4_out_10), .in_5(gfgg_enable_and_5_out_10), .in_6(gfgg_enable_and_6_out_10),
    .in_7(gfgg_enable_and_7_out_10), .in_8(gfgg_enable_and_8_out_10), .out_9(out_17));
  Gfgg_8_OR gfgg_8_or_2 (
    .in_1(gfgg_enable_and_1_out_11), .in_2(gfgg_enable_and_2_out_11), .in_3(gfgg_enable_and_3_out_11),
    .in_4(gfgg_enable_and_4_out_11), .in_5(gfgg_enable_and_5_out_11), .in_6(gfgg_enable_and_6_out_11),
    .in_7(gfgg_enable_and_7_out_11), .in_8(gfgg_enable_and_8_out_11), .out_9(out_18));
  Gfgg_8_OR gfgg_8_or_3 (
    .in_1(gfgg_enable_and_1_out_12), .in_2(gfgg_enable_and_2_out_12), .in_3(gfgg_enable_and_3_out_12),
    .in_4(gfgg_enable_and_4_out_12), .in_5(gfgg_enable_and_5_out_12), .in_6(gfgg_enable_and_6_out_12),
    .in_7(gfgg_enable_and_7_out_12), .in_8(gfgg_enable_and_8_out_12), .out_9(out_19));
  Gfgg_8_OR gfgg_8_or_4 (
    .in_1(gfgg_enable_and_1_out_13), .in_2(gfgg_enable_and_2_out_13), .in_3(gfgg_enable_and_3_out_13),
    .in_4(gfgg_enable_and_4_out_13), .in_5(gfgg_enable_and_5_out_13), .in_6(gfgg_enable_and_6_out_13),
    .in_7(gfgg_enable_and_7_out_13), .in_8(gfgg_enable_and_8_out_13), .out_9(out_20));
  Gfgg_8_OR gfgg_8_or_5 (
    .in_1(gfgg_enable_and_1_out_14), .in_2(gfgg_enable_and_2_out_14), .in_3(gfgg_enable_and_3_out_14),
    .in_4(gfgg_enable_and_4_out_14), .in_5(gfgg_enable_and_5_out_14), .in_6(gfgg_enable_and_6_out_14),
    .in_7(gfgg_enable_and_7_out_14), .in_8(gfgg_enable_and_8_out_14), .out_9(out_21));
  Gfgg_8_OR gfgg_8_or_6 (
    .in_1(gfgg_enable_and_1_out_15), .in_2(gfgg_enable_and_2_out_15), .in_3(gfgg_enable_and_3_out_15),
    .in_4(gfgg_enable_and_4_out_15), .in_5(gfgg_enable_and_5_out_15), .in_6(gfgg_enable_and_6_out_15),
    .in_7(gfgg_enable_and_7_out_15), .in_8(gfgg_enable_and_8_out_15), .out_9(out_22));
  Gfgg_8_OR gfgg_8_or_7 (
    .in_1(gfgg_enable_and_1_out_16), .in_2(gfgg_enable_and_2_out_16), .in_3(gfgg_enable_and_3_out_16),
    .in_4(gfgg_enable_and_4_out_16), .in_5(gfgg_enable_and_5_out_16), .in_6(gfgg_enable_and_6_out_16),
    .in_7(gfgg_enable_and_7_out_16), .in_8(gfgg_enable_and_8_out_16), .out_9(out_23));
  Gfgg_8_OR gfgg_8_or_8 (
    .in_1(gfgg_enable_and_1_out_17), .in_2(gfgg_enable_and_2_out_17), .in_3(gfgg_enable_and_3_out_17),
    .in_4(gfgg_enable_and_4_out_17), .in_5(gfgg_enable_and_5_out_17), .in_6(gfgg_enable_and_6_out_17),
    .in_7(gfgg_enable_and_7_out_17), .in_8(gfgg_enable_and_8_out_17), .out_9(out_24));
endmodule

module Gfgg_D_Flip_Flop (
  input  in_1,
  output out_2,
  output out_3
);

  wire clock_1_out, nand_1_out, nand_2_out, not_1_out;

  not not_1 (not_1_out, in_1);
  Clock clock_1 (.out(clock_1_out));
  nand nand_1 (nand_1_out, in_1, clock_1_out);
  nand nand_2 (nand_2_out, not_1_out, clock_1_out);
  nand nand_3 (out_2, nand_1_out, out_3);
  nand nand_4 (out_3, out_2, nand_2_out);
endmodule

module Gfgg_3Bit_PC (
  output out_1,
  output out_2,
  output out_3,
  output out_4,
  output out_5,
  output out_6
);

  wire gfgg_full_adder_1_out_4, gfgg_full_adder_2_out_4, gfgg_full_adder_2_out_5, gfgg_full_adder_3_out_4,
       gfgg_full_adder_3_out_5;

  Gfgg_Full_Adder gfgg_full_adder_1 (
    .in_1(out_1), .in_2(1'b1), .in_3(gfgg_full_adder_2_out_5), .out_4(gfgg_full_adder_1_out_4));  // open: out_5
  Gfgg_D_Flip_Flop gfgg_d_flip_flop_1 (.in_1(gfgg_full_adder_1_out_4), .out_2(out_1), .out_3(out_4));
  Gfgg_Full_Adder gfgg_full_adder_2 (
    .in_1(out_2), .in_2(1'b1), .in_3(gfgg_full_adder_3_out_5), .out_4(gfgg_full_adder_2_out_4),
    .out_5(gfgg_full_adder_2_out_5));
  Gfgg_D_Flip_Flop gfgg_d_flip_flop_2 (.in_1(gfgg_full_adder_2_out_4), .out_2(out_2), .out_3(out_5));
  Gfgg_Full_Adder gfgg_full_adder_3 (
    .in_1(out_3), .in_2(1'b1), .in_3(1'b0), .out_4(gfgg_full_adder_3_out_4), .out_5(gfgg_full_adder_3_out_5));
  Gfgg_D_Flip_Flop gfgg_d_flip_flop_3 (.in_1(gfgg_full_adder_3_out_4), .out_2(out_3), .out_3(out_6));
endmodule

module Gfgg_8Bit_Register_2 (
  input  in_1,
  input  in_2,
  input  in_3,
  input  in_4,
  input  in_5,
  input  in_6,
  input  in_7,
  input  in_8,
  input  Load,
  output out_10,
  output out_11,
  output out_12,
  output out_13,
  output out_14,
  output out_15,
  output out_16,
  output out_17
);

  wire and_1_out, and_2_out, and_3_out, and_4_out, and_5_out, and_6_out, and_7_out, and_8_out;

  and and_1 (and_1_out, in_6, Load);
  and and_2 (and_2_out, in_7, Load);
  and and_3 (and_3_out, in_8, Load);
  and and_4 (and_4_out, in_1, Load);
  and and_5 (and_5_out, Load, in_2);
  and and_6 (and_6_out, Load, in_3);
  and and_7 (and_7_out, in_4, Load);
  and and_8 (and_8_out, in_5, Load);
  Gfgg_D_Flip_Flop gfgg_d_flip_flop_1 (.in_1(and_1_out), .out_2(out_15));  // open: out_3
  Gfgg_D_Flip_Flop gfgg_d_flip_flop_2 (.in_1(and_2_out), .out_2(out_16));  // open: out_3
  Gfgg_D_Flip_Flop gfgg_d_flip_flop_3 (.in_1(and_3_out), .out_2(out_17));  // open: out_3
  Gfgg_D_Flip_Flop gfgg_d_flip_flop_4 (.in_1(and_4_out), .out_2(out_10));  // open: out_3
  Gfgg_D_Flip_Flop gfgg_d_flip_flop_5 (.in_1(and_5_out), .out_2(out_11));  // open: out_3
  Gfgg_D_Flip_Flop gfgg_d_flip_flop_6 (.in_1(and_6_out), .out_2(out_12));  // open: out_3
  Gfgg_D_Flip_Flop gfgg_d_flip_flop_7 (.in_1(and_7_out), .out_2(out_13));  // open: out_3
  Gfgg_D_Flip_Flop gfgg_d_flip_flop_8 (.in_1(and_8_out), .out_2(out_14));  // open: out_3
endmodule

module Gfgg_4_1_MUX (
  input  in_1,
  input  in_2,
  input  in_3,
  input  in_4,
  input  Select_A,
  input  Select_B,
  output out_7,
  output out_8,
  output out_9,
  output out_10
);

  wire not_1_out, not_2_out;

  not not_1 (not_1_out, Select_A);
  not not_2 (not_2_out, Select_B);
  Gfgg_3_AND gfgg_3_and_1 (.in_1(in_1), .in_2(Select_A), .in_3(Select_B), .out_4(out_7));
  Gfgg_3_AND gfgg_3_and_2 (.in_1(in_2), .in_2(Select_A), .in_3(not_2_out), .out_4(out_8));
  Gfgg_3_AND gfgg_3_and_3 (.in_1(in_3), .in_2(Select_B), .in_3(not_1_out), .out_4(out_9));
  Gfgg_3_AND gfgg_3_and_4 (.in_1(in_4), .in_2(not_1_out), .in_3(not_2_out), .out_4(out_10));
endmodule

module Gfgg_4_1_8_MUX (
  input  in_1,
  input  in_2,
  input  in_3,
  input  in_4,
  input  in_5,
  input  in_6,
  input  in_7,
  input  in_8,
  input  in_9,
  input  in_10,
  input  in_11,
  input  in_12,
  input  in_13,
  input  in_14,
  input  in_15,
  input  in_16,
  input  in_17,
  input  in_18,
  input  in_19,
  input  in_20,
  input  in_21,
  input  in_22,
  input  in_23,
  input  in_24,
  input  in_25,
  input  in_26,
  input  in_27,
  input  in_28,
  input  in_29,
  input  in_30,
  input  in_31,
  input  in_32,
  input  Select_A,
  input  Select_B,
  output out_35,
  output out_36,
  output out_37,
  output out_38,
  output out_39,
  output out_40,
  output out_41,
  output out_42,
  output out_43,
  output out_44,
  output out_45,
  output out_46,
  output out_47,
  output out_48,
  output out_49,
  output out_50,
  output out_51,
  output out_52,
  output out_53,
  output out_54,
  output out_55,
  output out_56,
  output out_57,
  output out_58,
  output out_59,
  output out_60,
  output out_61,
  output out_62,
  output out_63,
  output out_64,
  output out_65,
  output out_66
);

  Gfgg_4_1_MUX gfgg_4_1_mux_1 (
    .in_1(in_1), .in_2(in_9), .in_3(in_17), .in_4(in_25), .Select_A(Select_A), .Select_B(Select_B),
    .out_7(out_35), .out_8(out_36), .out_9(out_37), .out_10(out_38));
  Gfgg_4_1_MUX gfgg_4_1_mux_2 (
    .in_1(in_2), .in_2(in_10), .in_3(in_18), .in_4(in_26), .Select_A(Select_A), .Select_B(Select_B),
    .out_7(out_39), .out_8(out_40), .out_9(out_41), .out_10(out_42));
  Gfgg_4_1_MUX gfgg_4_1_mux_3 (
    .in_1(in_3), .in_2(in_11), .in_3(in_19), .in_4(in_27), .Select_A(Select_A), .Select_B(Select_B),
    .out_7(out_43), .out_8(out_44), .out_9(out_45), .out_10(out_46));
  Gfgg_4_1_MUX gfgg_4_1_mux_4 (
    .in_1(in_4), .in_2(in_12), .in_3(in_20), .in_4(in_28), .Select_A(Select_A), .Select_B(Select_B),
    .out_7(out_47), .out_8(out_48), .out_9(out_49), .out_10(out_50));
  Gfgg_4_1_MUX gfgg_4_1_mux_5 (
    .in_1(in_5), .in_2(in_13), .in_3(in_21), .in_4(in_29), .Select_A(Select_A), .Select_B(Select_B),
    .out_7(out_51), .out_8(out_52), .out_9(out_53), .out_10(out_54));
  Gfgg_4_1_MUX gfgg_4_1_mux_6 (
    .in_1(in_6), .in_2(in_14), .in_3(in_22), .in_4(in_30), .Select_A(Select_A), .Select_B(Select_B),
    .out_7(out_55), .out_8(out_56), .out_9(out_57), .out_10(out_58));
  Gfgg_4_1_MUX gfgg_4_1_mux_7 (
    .in_1(in_7), .in_2(in_15), .in_3(in_23), .in_4(in_31), .Select_A(Select_A), .Select_B(Select_B),
    .out_7(out_59), .out_8(out_60), .out_9(out_61), .out_10(out_62));
  Gfgg_4_1_MUX gfgg_4_1_mux_8 (
    .in_1(in_8), .in_2(in_16), .in_3(in_24), .in_4(in_32), .Select_A(Select_A), .Select_B(Select_B),
    .out_7(out_63), .out_8(out_64), .out_9(out_65), .out_10(out_66));
endmodule

module Gfgg_3_1_MUX (
  input  in_1,
  input  in_2,
  input  in_3,
  input  Select_A,
  input  Select_B,
  output out_6,
  output out_7,
  output out_8
);

  wire not_1_out, not_2_out, not_3_out;

  not not_1 (not_1_out, Select_A);
  not not_2 (not_2_out, Select_B);
  not not_3 (not_3_out, not_2_out);
  Gfgg_3_AND gfgg_3_and_1 (.in_1(in_1), .in_2(Select_A), .in_3(not_3_out), .out_4(out_6));
  Gfgg_3_AND gfgg_3_and_2 (.in_1(in_2), .in_2(Select_B), .in_3(not_1_out), .out_4(out_7));
  Gfgg_3_AND gfgg_3_and_3 (.in_1(in_3), .in_2(not_1_out), .in_3(not_2_out), .out_4(out_8));
endmodule

module Gfgg_3_1_MUX_2 (
  input  in_1,
  input  in_2,
  input  in_3,
  input  Select_A,
  input  Select_B,
  output out_6,
  output out_7,
  output out_8
);

  wire not_1_out, not_2_out;

  not not_1 (not_1_out, Select_A);
  not not_2 (not_2_out, Select_B);
  Gfgg_3_AND gfgg_3_and_1 (.in_1(in_1), .in_2(Select_A), .in_3(not_2_out), .out_4(out_6));
  Gfgg_3_AND gfgg_3_and_2 (.in_1(in_2), .in_2(Select_B), .in_3(not_1_out), .out_4(out_7));
  Gfgg_3_AND gfgg_3_and_3 (.in_1(in_3), .in_2(not_1_out), .in_3(not_2_out), .out_4(out_8));
endmodule

module Gfgg_Video_1 (
  input  in_1,
  input  in_2,
  input  in_3,
  input  in_4,
  input  in_5,
  input  in_6,
  input  in_7,
  input  in_8,
  input  in_9,
  input  in_10,
  input  in_11,
  input  in_12,
  input  in_13
);

  wire clock_1_out, gfgg_8byte_ram_1_out_17, gfgg_8byte_ram_1_out_18, gfgg_8byte_ram_1_out_19,
       gfgg_8byte_ram_1_out_20, gfgg_8byte_ram_1_out_21, gfgg_8byte_ram_1_out_22, gfgg_8byte_ram_1_out_23,
       gfgg_8byte_ram_1_out_24, gfgg_8byte_ram_2_out_17, gfgg_8byte_ram_2_out_18, gfgg_8byte_ram_2_out_19,
       gfgg_8byte_ram_2_out_20, gfgg_8byte_ram_2_out_21, gfgg_8byte_ram_2_out_22, gfgg_8byte_ram_2_out_23,
       gfgg_8byte_ram_2_out_24;

  Clock clock_1 (.out(clock_1_out));
  Gfgg_8Byte_RAM gfgg_8byte_ram_1 (
    .in_1(in_1), .in_2(in_2), .in_3(in_3), .in_4(in_4), .in_5(in_5), .in_6(in_6), .in_7(in_7), .in_8(in_8),
    .Write_Adress_1(in_9), .Write_Enable(in_10), .Read_Enable(in_11), .Read_Adress_1(clock_1_out),
    .out_17(gfgg_8byte_ram_1_out_17), .out_18(gfgg_8byte_ram_1_out_18), .out_19(gfgg_8byte_ram_1_out_19),
    .out_20(gfgg_8byte_ram_1_out_20), .out_21(gfgg_8byte_ram_1_out_21), .out_22(gfgg_8byte_ram_1_out_22),
    .out_23(gfgg_8byte_ram_1_out_23), .out_24(gfgg_8byte_ram_1_out_24));  // open: Write_Adress_4, Write_Adress_2, Read_Adress_4, Read_Adress_2
  Gfgg_8Byte_RAM gfgg_8byte_ram_2 (
    .in_1(in_1), .in_2(in_2), .in_3(in_3), .in_4(in_4), .in_5(in_5), .in_6(in_6), .in_7(in_7), .in_8(in_8),
    .Write_Adress_1(in_12), .Write_Enable(in_13), .Read_Enable(in_11), .Read_Adress_1(clock_1_out),
    .out_17(gfgg_8byte_ram_2_out_17), .out_18(gfgg_8byte_ram_2_out_18), .out_19(gfgg_8byte_ram_2_out_19),
    .out_20(gfgg_8byte_ram_2_out_20), .out_21(gfgg_8byte_ram_2_out_21), .out_22(gfgg_8byte_ram_2_out_22),
    .out_23(gfgg_8byte_ram_2_out_23), .out_24(gfgg_8byte_ram_2_out_24));  // open: Write_Adress_4, Write_Adress_2, Read_Adress_4, Read_Adress_2
  LED led_1 (.in(gfgg_8byte_ram_1_out_17));
  LED led_2 (.in(gfgg_8byte_ram_1_out_21));
  LED led_3 (.in(gfgg_8byte_ram_2_out_17));
  LED led_4 (.in(gfgg_8byte_ram_2_out_21));
  LED led_5 (.in(gfgg_8byte_ram_1_out_19));
  LED led_6 (.in(gfgg_8byte_ram_1_out_18));
  LED led_7 (.in(gfgg_8byte_ram_1_out_23));
  LED led_8 (.in(gfgg_8byte_ram_1_out_22));
  LED led_9 (.in(gfgg_8byte_ram_2_out_19));
  LED led_10 (.in(gfgg_8byte_ram_2_out_18));
  LED led_11 (.in(gfgg_8byte_ram_2_out_23));
  LED led_12 (.in(gfgg_8byte_ram_2_out_22));
  LED led_13 (.in(gfgg_8byte_ram_1_out_20));
  LED led_14 (.in(gfgg_8byte_ram_1_out_24));
  LED led_15 (.in(gfgg_8byte_ram_2_out_20));
  LED led_16 (.in(gfgg_8byte_ram_2_out_24));
endmodule

module Gfgg_PC_8 (
  output out_1,
  output out_2,
  output out_3,
  output out_4,
  output out_5,
  output out_6,
  output out_7,
  output out_8,
  output out_9,
  output out_10,
  output out_11,
  output out_12,
  output [2:0] out_13
);

  wire ADD_out_5, and_1_out, clock_1_out, HLT_out_5, not_1_out, not_2_out, not_3_out, not_4_out, not_5_out,
       not_6_out, not_7_out, not_8_out, not_9_out, not_10_out, not_11_out, not_12_out, not_13_out,
       not_14_out, not_15_out, not_16_out, not_17_out, not_18_out;
  wire [3:0] adder_1_out, and_2_out, and_3_out, RegA_q, RegB_q;
  wire [3:3] LDA_out_5, LDB_out_5;
  wire [7:0] rom_1_data;

  Clock clock_1 (.out(clock_1_out));
  not not_1 (not_1_out, HLT_out_5);
  and and_1 (and_1_out, clock_1_out, not_1_out);
  Gfgg_3Bit_PC_2 gfgg_3bit_pc_2_1 (.CLK(and_1_out), .out_2(out_13));
  ROM #(.addrWidth(3)) rom_1 (.addr(out_13), .data(rom_1_data));
  assign and_2_out = rom_1_data[7:4] & {4{LDA_out_5[3]}};  // AND_Gate and_2, 4 bits wide
  assign and_3_out = rom_1_data[7:4] & {4{LDB_out_5[3]}};  // AND_Gate and_3, 4 bits wide
  not not_2 (not_2_out, rom_1_data[3]);
  not not_3 (not_3_out, rom_1_data[2]);
  not not_4 (not_4_out, rom_1_data[1]);
  not not_5 (not_5_out, rom_1_data[0]);
  not not_6 (not_6_out, rom_1_data[2]);
  not not_7 (not_7_out, rom_1_data[3]);
  not not_8 (not_8_out, rom_1_data[1]);
  not not_9 (not_9_out, rom_1_data[3]);
  not not_10 (not_10_out, rom_1_data[2]);
  not not_11 (not_11_out, rom_1_data[3]);
  not not_12 (not_12_out, rom_1_data[1]);
  not not_13 (not_13_out, rom_1_data[0]);
  not not_14 (not_14_out, rom_1_data[3]);
  not not_15 (not_15_out, rom_1_data[1]);
  not not_16 (not_16_out, rom_1_data[3]);
  not not_17 (not_17_out, rom_1_data[0]);
  not not_18 (not_18_out, rom_1_data[3]);
  Register #(.width(4)) RegA (.D(and_2_out), .en(LDA_out_5[3]), .clk(and_1_out), .Q(RegA_q));  // open: clr
  Register #(.width(4)) RegB (.D(and_3_out), .en(LDB_out_5[3]), .clk(and_1_out), .Q(RegB_q));  // open: clr
  Gfgg_4_AND NOP (.in_1(not_2_out), .in_2(not_3_out), .in_3(not_4_out), .in_4(not_5_out), .out_5(out_9));
  Gfgg_4_AND LDA (
    .in_1(rom_1_data[3]), .in_2(not_6_out), .in_3(rom_1_data[1]), .in_4(rom_1_data[0]), .out_5(LDA_out_5[3]));
  Gfgg_4_AND LDB (.in_1(not_7_out), .in_2(rom_1_data[2]), .in_3(not_8_out), .in_4(rom_1_data[0]), .out_5(LDB_out_5[3]));
  Gfgg_4_AND STA (.in_1(not_9_out), .in_2(not_10_out), .in_3(rom_1_data[1]), .in_4(rom_1_data[0]), .out_5(out_10));
  Gfgg_4_AND STB (.in_1(not_11_out), .in_2(rom_1_data[2]), .in_3(not_12_out), .in_4(not_13_out), .out_5(out_11));
  Gfgg_4_AND ADD (.in_1(not_14_out), .in_2(rom_1_data[2]), .in_3(not_15_out), .in_4(rom_1_data[0]), .out_5(ADD_out_5));
  Gfgg_4_AND HLT (.in_1(not_16_out), .in_2(rom_1_data[2]), .in_3(rom_1_data[1]), .in_4(not_17_out), .out_5(HLT_out_5));
  Gfgg_4_AND GTO (.in_1(not_18_out), .in_2(rom_1_data[2]), .in_3(rom_1_data[1]), .in_4(rom_1_data[0]), .out_5(out_12));
  Adder #(.width(4)) adder_1 (.a(RegA_q), .b(RegB_q), .out(adder_1_out));  // open: cin, cout
  Register #(.width(4)) RegC (
    .D(adder_1_out), .en(ADD_out_5), .clk(and_1_out), .Q({out_5, out_6, out_7, out_8}));  // open: clr

  // Notes on the sheet:
  //   contents of rom_1 (hex, n*v repeats v):
  //   b 5 5 6
endmodule

module Gfgg_4_AND (
  input  in_1,
  input  in_2,
  input  in_3,
  input  in_4,
  output out_5
);

  wire and_1_out, and_2_out;

  and and_1 (and_1_out, in_1, in_2);
  and and_2 (and_2_out, in_3, in_4);
  and and_3 (out_5, and_1_out, and_2_out);
endmodule

module Gfgg_3Bit_PC_2 (
  input  CLK,
  output [2:0] out_2
);

  wire [2:0] adder_1_out;

  Adder #(.width(3)) adder_1 (.a(3'b001), .b(out_2), .out(adder_1_out));  // open: cin, cout
  Register #(.width(3)) register_1 (.D(adder_1_out), .en(1'b1), .clk(CLK), .Q(out_2));  // open: clr
endmodule
